// Logisim project CLA_ADDER.circ as structural Verilog: 4 circuits, main circuit main
module main (
  input  in_1,
  input  [7:0] in_2,
  input  [7:0] in_3,
  output [7:0] out_4,
  output out_5
);

  CLA_ADDER_8 cla_adder_8_1 (.Ci(in_1), .A(in_2), .B(in_3), .S(out_4), .Co(out_5));
endmodule

// ADD
module CLA_ADDER (
  input  Ci,
  input  [3:0] A,
  input  [3:0] B,
  output [3:0] S,
  output Co
);

  wire and_1_out, and_2_out, and_3_out, and_4_out, and_5_out, and_6_out, and_7_out, and_8_out, and_9_out,
       and_10_out, and_11_out, and_12_out, and_13_out, and_14_out, or_1_out, or_2_out, or_3_out, xor_1_out,
       xor_2_out, xor_3_out, xor_4_out;

  xor xor_1 (xor_1_out, A[0], B[0]);
  and and_1 (and_1_out, B[0], A[0]);
  xor xor_2 (xor_2_out, A[1], B[1]);
  and and_2 (and_2_out, B[1], A[1]);
  xor xor_3 (xor_3_out, A[2], B[2]);
  and and_3 (and_3_out, B[2], A[2]);
  xor xor_4 (xor_4_out, A[3], B[3]);
  and and_4 (and_4_out, B[3], A[3]);
  and and_5 (and_5_out, xor_1_out, Ci);
  and and_6 (and_6_out, xor_1_out, Ci, xor_2_out);
  and and_7 (and_7_out, xor_2_out, and_1_out);
  and and_8 (and_8_out, Ci, xor_1_out, xor_2_out, xor_3_out);
  and and_9 (and_9_out, and_1_out, xor_2_out, xor_3_out);
  and and_10 (and_10_out, and_2_out, xor_3_out);
  and and_11 (and_11_out, Ci, xor_1_out, xor_2_out, xor_3_out, xor_4_out);
  and and_12 (and_12_out, and_1_out, xor_2_out, xor_3_out, xor_4_out);
  and and_13 (and_13_out, and_2_out, xor_3_out, xor_4_out);
  and and_14 (and_14_out, and_3_out, xor_4_out);
  or or_1 (or_1_out, and_5_out, and_1_out);
  or or_2 (or_2_out, and_6_out, and_7_out, and_2_out);
  or or_3 (or_3_out, and_8_out, and_9_out, and_10_out, and_3_out);
  or or_4 (Co, and_11_out, and_12_out, and_13_out, and_14_out, and_4_out);
  xor xor_5 (S[0], Ci, xor_1_out);
  xor xor_6 (S[1], or_1_out, xor_2_out);
  xor xor_7 (S[2], or_2_out, xor_3_out);
  xor xor_8 (S[3], or_3_out, xor_4_out);

  // Notes on the sheet:
  //   4-Bit CLA Adder
endmodule

// ADD
module CLA_ADDER_8 (
  input  Ci,
  input  [7:0] A,
  input  [7:0] B,
  output [7:0] S,
  output Co
);

  wire cla_adder_1_co;

  CLA_ADDER cla_adder_1 (.Ci(Ci), .A(A[3:0]), .B(B[3:0]), .S(S[3:0]), .Co(cla_adder_1_co));
  CLA_ADDER cla_adder_2 (.Ci(cla_adder_1_co), .A(A[7:4]), .B(B[7:4]), .S(S[7:4]), .Co(Co));

  // Notes on the sheet:
  //   8-Bit CLA Adder
endmodule

module CLA_ADDER_16 (
  input  Ci,
  input  [15:0] A,
  input  [15:0] B,
  output [15:0] S,
  output Co
);

  wire cla_adder_8_1_co;

  CLA_ADDER_8 cla_adder_8_1 (.Ci(Ci), .A(A[7:0]), .B(B[7:0]), .S(S[7:0]), .Co(cla_adder_8_1_co));
  CLA_ADDER_8 cla_adder_8_2 (.Ci(cla_adder_8_1_co), .A(A[15:8]), .B(B[15:8]), .S(S[15:8]), .Co(Co));

  // Notes on the sheet:
  //   16-Bit CLA Adder
endmodule
