// Logisim project DIVISOR.circ as structural Verilog: 4 circuits, main circuit main
module main (
  input  [7:0] in_1,
  input  [7:0] in_2,
  input  [7:0] in_3,
  input  [7:0] in_4,
  input  [7:0] in_5,
  input  [7:0] in_6,
  input  [7:0] in_7,
  input  [7:0] in_8,
  input  [7:0] in_9,
  input  [7:0] in_10,
  input  [7:0] in_11,
  input  [7:0] in_12,
  output [7:0] out_13,
  output [7:0] out_14,
  output [7:0] out_15,
  output [7:0] out_16,
  output out_17,
  output out_18,
  output [7:0] out_19,
  output [7:0] out_20,
  output [7:0] out_21,
  output [7:0] out_22,
  output out_23,
  output out_24,
  output [7:0] out_25,
  output [7:0] out_26,
  output [7:0] out_27,
  output [7:0] out_28,
  output out_29,
  output out_30
);

  // Probe on in_1
  // Probe on in_3
  // Probe on in_5
  // Probe on in_7
  // Probe on in_9
  // Probe on in_11
  DIVISOR_8 divisor_8_1 (.A(in_1), .B(in_3), .R(out_15), .Q(out_13), .Z(out_17));
  DIVISOR_8 divisor_8_2 (.A(in_5), .B(in_7), .R(out_21), .Q(out_19), .Z(out_23));
  DIVISOR_8 divisor_8_3 (.A(in_9), .B(in_11), .R(out_27), .Q(out_25), .Z(out_29));
  // Probe on out_13
  // Probe on out_15
  // Probe on out_19
  // Probe on out_21
  // Probe on out_25
  // Probe on out_27
  // Probe on in_2
  // Probe on in_4
  // Probe on in_6
  // Probe on in_8
  // Probe on in_10
  // Probe on in_12
  // Probe on out_14
  DIVISOR_8 divisor_8_4 (.A(in_2), .B(in_4), .R(out_16), .Q(out_14), .Z(out_18));
  // Probe on out_16
  // Probe on out_20
  DIVISOR_8 divisor_8_5 (.A(in_6), .B(in_8), .R(out_22), .Q(out_20), .Z(out_24));
  // Probe on out_22
  // Probe on out_26
  DIVISOR_8 divisor_8_6 (.A(in_10), .B(in_12), .R(out_28), .Q(out_26), .Z(out_30));
  // Probe on out_28

  // Notes on the sheet:
  //   Division Chip Tests
endmodule

// SUB
module SUBTRACTOR_8 (
  input  Bi,
  input  [7:0] A,
  input  [7:0] B,
  output [7:0] S,
  output Bo
);

  wire and_1_out, and_2_out, and_3_out, and_4_out, and_5_out, and_6_out, and_7_out, and_8_out, and_9_out,
       and_10_out, and_11_out, and_12_out, and_13_out, and_14_out, and_15_out, and_16_out, not_1_out,
       not_2_out, not_3_out, not_4_out, not_5_out, not_6_out, not_7_out, not_8_out, not_9_out, not_10_out,
       not_11_out, not_12_out, not_13_out, not_14_out, not_15_out, not_16_out, or_1_out, or_2_out, or_3_out,
       or_4_out, or_5_out, or_6_out, or_7_out, xor_1_out, xor_2_out, xor_3_out, xor_4_out, xor_9_out,
       xor_10_out, xor_11_out, xor_12_out;

  xor xor_1 (xor_1_out, A[0], B[0]);
  not not_1 (not_1_out, xor_1_out);
  not not_2 (not_2_out, A[0]);
  xor xor_2 (xor_2_out, A[1], B[1]);
  not not_3 (not_3_out, xor_2_out);
  not not_4 (not_4_out, A[1]);
  xor xor_3 (xor_3_out, A[2], B[2]);
  not not_5 (not_5_out, xor_3_out);
  not not_6 (not_6_out, A[2]);
  xor xor_4 (xor_4_out, A[3], B[3]);
  not not_7 (not_7_out, xor_4_out);
  not not_8 (not_8_out, A[3]);
  xor xor_5 (S[0], Bi, xor_1_out);
  and and_1 (and_1_out, not_1_out, Bi);
  and and_2 (and_2_out, not_2_out, B[0]);
  xor xor_6 (S[1], or_1_out, xor_2_out);
  and and_3 (and_3_out, not_3_out, or_1_out);
  and and_4 (and_4_out, not_4_out, B[1]);
  xor xor_7 (S[2], or_2_out, xor_3_out);
  and and_5 (and_5_out, not_5_out, or_2_out);
  and and_6 (and_6_out, not_6_out, B[2]);
  xor xor_8 (S[3], or_3_out, xor_4_out);
  and and_7 (and_7_out, not_7_out, or_3_out);
  and and_8 (and_8_out, not_8_out, B[3]);
  or or_1 (or_1_out, and_1_out, and_2_out);
  or or_2 (or_2_out, and_3_out, and_4_out);
  or or_3 (or_3_out, and_5_out, and_6_out);
  or or_4 (or_4_out, and_7_out, and_8_out);
  xor xor_9 (xor_9_out, A[4], B[4]);
  xor xor_10 (xor_10_out, A[5], B[5]);
  xor xor_11 (xor_11_out, A[6], B[6]);
  xor xor_12 (xor_12_out, A[7], B[7]);
  not not_9 (not_9_out, xor_9_out);
  and and_9 (and_9_out, not_9_out, or_4_out);
  not not_10 (not_10_out, A[4]);
  and and_10 (and_10_out, not_10_out, B[4]);
  not not_11 (not_11_out, xor_10_out);
  and and_11 (and_11_out, not_11_out, or_5_out);
  not not_12 (not_12_out, A[5]);
  and and_12 (and_12_out, not_12_out, B[5]);
  not not_13 (not_13_out, xor_11_out);
  and and_13 (and_13_out, not_13_out, or_6_out);
  not not_14 (not_14_out, A[6]);
  and and_14 (and_14_out, not_14_out, B[6]);
  not not_15 (not_15_out, xor_12_out);
  and and_15 (and_15_out, not_15_out, or_7_out);
  not not_16 (not_16_out, A[7]);
  and and_16 (and_16_out, not_16_out, B[7]);
  xor xor_13 (S[4], or_4_out, xor_9_out);
  or or_5 (or_5_out, and_9_out, and_10_out);
  xor xor_14 (S[5], or_5_out, xor_10_out);
  or or_6 (or_6_out, and_11_out, and_12_out);
  xor xor_15 (S[6], or_6_out, xor_11_out);
  or or_7 (or_7_out, and_13_out, and_14_out);
  xor xor_16 (S[7], or_7_out, xor_12_out);
  or or_8 (Bo, and_15_out, and_16_out);

  // Notes on the sheet:
  //   A
  //   B
  //   Bi
  //   8-Bit Full-Subtractor
  //   S
  //   Bo
endmodule

// REM
module REMAINDER_MAKER (
  input  LSB,
  input  [7:0] A,
  input  [7:0] B,
  output [7:0] R,
  output Q
);

  wire subtractor_8_1_bo;
  wire [7:0] subtractor_8_1_s;

  SUBTRACTOR_8 subtractor_8_1 (.Bi(1'b0), .A({A[6:0], LSB}), .B(B), .S(subtractor_8_1_s), .Bo(subtractor_8_1_bo));
  not not_1 (Q, subtractor_8_1_bo);
  Multiplexer #(.width(8), .enable("false")) multiplexer_1 (
    .in0(subtractor_8_1_s), .in1({A[6:0], LSB}), .out(R), .sel(subtractor_8_1_bo));

  // Notes on the sheet:
  //   Remainder Generator
endmodule

// DIV
module DIVISOR_8 (
  input  [7:0] A,
  input  [7:0] B,
  output [7:0] R,
  output [7:0] Q,
  output Z
);

  wire or_1_out;
  wire [7:0] remainder_maker_1_r, remainder_maker_2_r, remainder_maker_3_r, remainder_maker_4_r,
       remainder_maker_5_r, remainder_maker_6_r, remainder_maker_7_r, remainder_maker_8_q;

  REMAINDER_MAKER remainder_maker_1 (
    .LSB(A[7]), .A({8{1'b0}}), .B(B), .Q(remainder_maker_8_q[7]), .R(remainder_maker_1_r));
  REMAINDER_MAKER remainder_maker_2 (
    .LSB(A[6]), .A(remainder_maker_1_r), .B(B), .Q(remainder_maker_8_q[6]), .R(remainder_maker_2_r));
  or or_1 (or_1_out, B[0], B[1], B[2], B[3], B[4], B[5], B[6], B[7]);
  REMAINDER_MAKER remainder_maker_3 (
    .LSB(A[4]), .A(remainder_maker_4_r), .B(B), .Q(remainder_maker_8_q[4]), .R(remainder_maker_3_r));
  REMAINDER_MAKER remainder_maker_4 (
    .LSB(A[5]), .A(remainder_maker_2_r), .B(B), .Q(remainder_maker_8_q[5]), .R(remainder_maker_4_r));
  not not_1 (Z, or_1_out);
  REMAINDER_MAKER remainder_maker_5 (
    .LSB(A[3]), .A(remainder_maker_3_r), .B(B), .Q(remainder_maker_8_q[3]), .R(remainder_maker_5_r));
  assign Q = or_1_out ? remainder_maker_8_q : 8'bz;  // Controlled_Buffer controlled_buffer_1
  REMAINDER_MAKER remainder_maker_6 (
    .LSB(A[2]), .A(remainder_maker_5_r), .B(B), .Q(remainder_maker_8_q[2]), .R(remainder_maker_6_r));
  REMAINDER_MAKER remainder_maker_7 (
    .LSB(A[1]), .A(remainder_maker_6_r), .B(B), .Q(remainder_maker_8_q[1]), .R(remainder_maker_7_r));
  REMAINDER_MAKER remainder_maker_8 (.LSB(A[0]), .A(remainder_maker_7_r), .B(B), .Q(remainder_maker_8_q[0]), .R(R));

  // Notes on the sheet:
  //   8-Bit Divisor
endmodule
