// Logisim project FLOAT_PROCESSOR.circ as structural Verilog
module main (
  input  ENABLE,
  input  [7:0] DIVIDEND,
  input  [7:0] DIVISOR,
  input  [7:0] in_4,
  input  [7:0] in_5,
  input  [7:0] in_6,
  input  [7:0] in_7,
  input  [7:0] in_8,
  input  [7:0] in_9,
  input  [7:0] in_10,
  input  [7:0] in_11
);

  wire fixed_divisor_1_clk, fixed_divisor_1_clr, fixed_divisor_1_we, RESET_out;
  wire [6:0] fixed_divisor_1_data;
  wire [7:0] fixed_divisor_1_f, float_encoder_1_f, float_mul_1_c, float_mul_2_c, float_mul_3_c, float_mul_4_c;

  // Probe on in_4
  // Probe on in_6
  // Probe on in_8
  // Probe on in_10
  Button RESET (.out(RESET_out));
  // Probe on float_mul_1_c
  // Probe on float_mul_1_c
  FLOAT_MUL float_mul_1 (.A(in_4), .B(in_6), .C(float_mul_1_c));
  // Probe on float_mul_2_c
  // Probe on float_mul_2_c
  FLOAT_MUL float_mul_2 (.A(in_8), .B(in_10), .C(float_mul_2_c));
  // Probe on DIVIDEND
  // Probe on DIVISOR
  FIXED_DIVISOR fixed_divisor_1 (
    .A(ENABLE), .R(RESET_out), .X(DIVIDEND), .Y(DIVISOR), .F(fixed_divisor_1_f), .DATA(fixed_divisor_1_data),
    .WE(fixed_divisor_1_we), .CLK(fixed_divisor_1_clk), .CLR(fixed_divisor_1_clr));
  TTY tty_1 (
    .data(fixed_divisor_1_data), .clk(fixed_divisor_1_clk), .we(fixed_divisor_1_we), .clr(fixed_divisor_1_clr));
  FLOAT_ENCODER float_encoder_1 (.A(DIVIDEND), .B(DIVISOR), .CLK(RESET_out), .F(float_encoder_1_f));
  // Probe on fixed_divisor_1_f
  // Probe on float_encoder_1_f
  // Probe on in_5
  // Probe on in_7
  // Probe on in_9
  // Probe on in_11
  // Probe on float_mul_3_c
  // Probe on float_mul_3_c
  FLOAT_MUL float_mul_3 (.A(in_5), .B(in_7), .C(float_mul_3_c));
  // Probe on float_mul_4_c
  // Probe on float_mul_4_c
  FLOAT_MUL float_mul_4 (.A(in_9), .B(in_11), .C(float_mul_4_c));

  // Notes on the sheet:
  //   _____
  //   =
  //   Q3.5 Value
  //   Float8 Value
endmodule

// DEC_DIV
module DECIMAL_DIV (
  input  A,
  input  R,
  input  [7:0] X,
  input  [7:0] Y,
  output [23:0] F,
  output [6:0] DATA,
  output CLK,
  output WE,
  output CLR
);

  wire and_2_out, comparator_1_gt, comparator_2_eq, counter_1_carry, counter_2_carry, demultiplexer_1_out0,
       demultiplexer_1_out1, demultiplexer_1_out2, demultiplexer_1_out3, not_1_out, or_1_out, or_2_out,
       or_3_out, or_4_out;
  wire [1:0] counter_1_q;
  wire [7:0] counter_2_q, divisor_8_1_q, divisor_8_1_r, multiplexer_1_out, multiplyer_1_p, register_1_q,
       register_2_q;
  wire [15:0] bit_extender_1_out, bit_extender_2_out, cla_adder_16_1_s, multiplexer_2_out, multiplier_1_out;

  Clock clock_1 (.out(CLK));
  Demultiplexer #(.select(2), .enable("false")) demultiplexer_1 (
    .out0(demultiplexer_1_out0), .out1(demultiplexer_1_out1), .out2(demultiplexer_1_out2),
    .out3(demultiplexer_1_out3), .in(A), .sel(counter_1_q));
  Counter #(.width(2), .max('h3), .ongoal("stay")) counter_1 (
    .load(1'b0), .count(A), .Q(counter_1_q), .carry(counter_1_carry), .clk(CLK), .clr(R));  // open: D
  Comparator comparator_1 (.a(counter_2_q), .b(8'h1), .gt(comparator_1_gt));  // open: eq, lt
  Comparator comparator_2 (.a(counter_2_q), .b(8'h1), .eq(comparator_2_eq));  // open: gt, lt
  or or_1 (or_1_out, demultiplexer_1_out1, demultiplexer_1_out3);
  Counter #(.max('h3), .ongoal("stay")) counter_2 (
    .load(1'b0), .count(counter_1_carry), .Q(counter_2_q), .carry(counter_2_carry), .clk(CLK), .clr(R));  // open: D
  not not_1 (not_1_out, counter_2_carry);
  or or_2 (or_2_out, demultiplexer_1_out0, demultiplexer_1_out1, demultiplexer_1_out3);
  or or_3 (or_3_out, demultiplexer_1_out1, demultiplexer_1_out2, demultiplexer_1_out3);
  and and_1 (WE, not_1_out, or_3_out);
  Multiplexer #(.width(8), .enable("false")) multiplexer_1 (
    .in0(X), .in1(multiplyer_1_p), .out(multiplexer_1_out), .sel(or_1_out));
  Register register_1 (.D(multiplexer_1_out), .en(or_2_out), .Q(register_1_q), .clk(CLK), .clr(R));
  Register register_2 (.D(Y), .en(or_2_out), .Q(register_2_q), .clk(CLK), .clr(R));
  assign bit_extender_1_out = {{8{1'b0}}, divisor_8_1_q};  // Bit_Extender bit_extender_1
  or or_4 (or_4_out, comparator_1_gt, comparator_2_eq);
  DIVISOR_8 divisor_8_1 (.A(register_1_q), .B(register_2_q), .R(divisor_8_1_r), .Q(divisor_8_1_q));  // open: Z
  Register #(.width(16)) register_3 (.D(multiplexer_2_out), .Q(F[15:0]), .clk(and_2_out), .clr(R));  // open: en
  Multiplexer #(.width(16), .enable("false")) multiplexer_2 (
    .in0(bit_extender_1_out), .in1(cla_adder_16_1_s), .out(multiplexer_2_out), .sel(demultiplexer_1_out3));
  and and_2 (and_2_out, or_4_out, CLK, not_1_out);
  Register register_4 (.D(divisor_8_1_q), .Q(F[23:16]), .clk(demultiplexer_1_out2), .clr(R));  // open: en
  Multiplier #(.width(16)) multiplier_1 (.a(F[15:0]), .b(16'ha), .out(multiplier_1_out));  // open: cin, cout
  CLA_ADDER_16 cla_adder_16_1 (
    .Ci(1'b0), .A(bit_extender_2_out), .B(multiplier_1_out), .S(cla_adder_16_1_s));  // open: Co
  Multiplexer #(.width(7), .enable("false")) multiplexer_3 (
    .in0(7'b0101110), .in1({3'b011, divisor_8_1_q[3:0]}), .out(DATA), .sel(or_1_out));
  MULTIPLYER multiplyer_1 (.A(divisor_8_1_r[3:0]), .B(4'b1010), .P(multiplyer_1_p));
  assign bit_extender_2_out = {{8{1'b0}}, divisor_8_1_q};  // Bit_Extender bit_extender_2

  assign CLR = R;

  // Notes on the sheet:
  //   A
  //   R
  //   CLK
  //   Decimal Iterative Divisor
endmodule

// FIX_DIV
module FIXED_DIVISOR (
  input  A,
  input  R,
  input  [7:0] X,
  input  [7:0] Y,
  output [6:0] DATA,
  output [7:0] F,
  output WE,
  output CLK,
  output CLR
);

  wire counter_1_carry, counter_2_carry, demultiplexer_1_out0, demultiplexer_1_out1, demultiplexer_1_out2,
       demultiplexer_1_out3, not_1_out, or_1_out, or_2_out, or_3_out;
  wire [1:0] counter_1_q;
  wire [7:0] divisor_8_1_q, divisor_8_1_r, multiplexer_1_out, multiplyer_1_p, register_1_q, register_2_q;

  Demultiplexer #(.select(2), .enable("false")) demultiplexer_1 (
    .out0(demultiplexer_1_out0), .out1(demultiplexer_1_out1), .out2(demultiplexer_1_out2),
    .out3(demultiplexer_1_out3), .in(A), .sel(counter_1_q));
  Counter #(.width(2), .max('h3), .ongoal("stay")) counter_1 (
    .load(1'b0), .count(A), .Q(counter_1_q), .carry(counter_1_carry), .clk(CLK), .clr(R));  // open: D
  Multiplexer #(.width(8), .enable("false")) multiplexer_1 (
    .in0(X), .in1(multiplyer_1_p), .out(multiplexer_1_out), .sel(or_1_out));
  Clock clock_1 (.out(CLK));
  or or_1 (or_1_out, demultiplexer_1_out1, demultiplexer_1_out3);
  Counter #(.max('h3), .ongoal("stay")) counter_2 (
    .load(1'b0), .count(counter_1_carry), .carry(counter_2_carry), .clk(CLK), .clr(R));  // open: D, Q
  not not_1 (not_1_out, counter_2_carry);
  Register register_1 (.D(multiplexer_1_out), .en(or_3_out), .Q(register_1_q), .clk(CLK), .clr(R));
  Register register_2 (.D(Y), .en(or_3_out), .Q(register_2_q), .clk(CLK), .clr(R));
  or or_2 (or_2_out, demultiplexer_1_out1, demultiplexer_1_out2, demultiplexer_1_out3);
  or or_3 (or_3_out, demultiplexer_1_out0, demultiplexer_1_out1, demultiplexer_1_out3);
  and and_1 (WE, not_1_out, or_2_out);
  DIVISOR_8 divisor_8_1 (.A(register_1_q), .B(register_2_q), .R(divisor_8_1_r), .Q(divisor_8_1_q));  // open: Z
  MULTIPLYER multiplyer_1 (.A(divisor_8_1_r[3:0]), .B(4'b1010), .P(multiplyer_1_p));
  Multiplexer #(.width(7), .enable("false")) multiplexer_2 (
    .in0(7'b0101110), .in1({3'b011, divisor_8_1_q[3:0]}), .out(DATA), .sel(or_1_out));
  FIXED_ENCODER fixed_encoder_1 (
    .A(divisor_8_1_r), .B(register_2_q), .C(divisor_8_1_q), .Q(F), .CLK(demultiplexer_1_out2), .R(R));

  assign CLR = R;

  // Notes on the sheet:
  //   A
  //   R
  //   CLK
  //   Fixed-Point Divisor
endmodule

// FIX
module FIXED_ENCODER (
  input  [7:0] A,
  input  [7:0] B,
  input  [7:0] C,
  input  CLK,
  input  R,
  output [7:0] Q
);

  wire [4:0] remainder_maker_5_q;
  wire [7:0] remainder_maker_1_r, remainder_maker_2_r, remainder_maker_3_r, remainder_maker_4_r;

  REMAINDER_MAKER remainder_maker_1 (.LSB(1'b0), .A(A), .B(B), .Q(remainder_maker_5_q[4]), .R(remainder_maker_1_r));
  REMAINDER_MAKER remainder_maker_2 (
    .LSB(1'b0), .A(remainder_maker_1_r), .B(B), .Q(remainder_maker_5_q[3]), .R(remainder_maker_2_r));
  REMAINDER_MAKER remainder_maker_3 (
    .LSB(1'b0), .A(remainder_maker_4_r), .B(B), .Q(remainder_maker_5_q[1]), .R(remainder_maker_3_r));
  REMAINDER_MAKER remainder_maker_4 (
    .LSB(1'b0), .A(remainder_maker_2_r), .B(B), .Q(remainder_maker_5_q[2]), .R(remainder_maker_4_r));
  REMAINDER_MAKER remainder_maker_5 (
    .LSB(1'b0), .A(remainder_maker_3_r), .B(B), .Q(remainder_maker_5_q[0]));  // open: R
  Register register_1 (.D({C[2:0], remainder_maker_5_q}), .Q(Q), .clk(CLK), .clr(R));  // open: en

  // Notes on the sheet:
  //   Q3.5 Fixed-Point Encoder
endmodule

// FLP_DIV
module FLOAT_ENCODER (
  input  [7:0] A,
  input  [7:0] B,
  input  CLK,
  output [7:0] F
);

  wire [2:0] normalizer_1_e;
  wire [3:0] bit_extender_1_out, cla_adder_1_s;
  wire [7:0] divisor_8_1_q, divisor_8_1_r, fixed_encoder_1_q, normalizer_1_m;

  // Probe on A
  // Probe on B
  DIVISOR_8 divisor_8_1 (.A(A), .B(B), .R(divisor_8_1_r), .Q(divisor_8_1_q));  // open: Z
  FIXED_ENCODER fixed_encoder_1 (
    .A(divisor_8_1_r), .B(B), .C(divisor_8_1_q), .Q(fixed_encoder_1_q), .CLK(CLK));  // open: R
  xor xor_1 (F[7], B[7], A[7]);
  NORMALIZER normalizer_1 (
    .I(fixed_encoder_1_q), .M({normalizer_1_m[7:5], F[3:0], normalizer_1_m[0]}), .E(normalizer_1_e));
  // Probe on fixed_encoder_1_q
  // Probe on {normalizer_1_m[7:5], F[3:0], normalizer_1_m[0]}
  // Probe on normalizer_1_e
  assign bit_extender_1_out = {{1{1'b0}}, normalizer_1_e};  // Bit_Extender bit_extender_1
  CLA_ADDER cla_adder_1 (.Ci(1'b0), .A(bit_extender_1_out), .B(4'b0011), .S(cla_adder_1_s));  // open: Co
  Bit_Extender #(.in_width(4), .out_width(3)) bit_extender_2 (.in(cla_adder_1_s), .out(F[6:4]));

  // Notes on the sheet:
  //   Float8 Encoder
  //   BIAS
  //   FIXED-POINT
  //   MANTISSA
  //   EXPOENTE REAL
endmodule

// SHT
module POINT_SHIFTER (
  input  [7:0] A,
  input  PN0,
  input  PN1,
  input  PN2,
  input  PN3,
  output [7:0] R,
  output N0,
  output N1,
  output N2,
  output N3,
  output SIGN
);

  wire comparator_1_eq, comparator_1_gt, comparator_2_eq, nor_1_out, not_1_out;
  wire [1:0] nand_1_out;
  wire [7:0] shifter_1_out, shifter_2_out;

  Shifter #(.shift("lr")) shifter_1 (.in(A), .\dist (3'b001), .out(shifter_1_out));
  Shifter shifter_2 (.in(A), .\dist (3'b001), .out(shifter_2_out));
  not not_1 (not_1_out, comparator_1_eq);
  Comparator #(.width(3), .mode("unsigned")) comparator_1 (
    .a(A[7:5]), .b(3'b001), .gt(comparator_1_gt), .eq(comparator_1_eq), .lt(SIGN));
  nor nor_1 (nor_1_out, PN0, PN1, PN2, PN3);
  Multiplexer #(.select(2), .width(8), .enable("false")) multiplexer_1 (
    .in0(shifter_1_out), .in1(A), .in2({8{1'b0}}), .in3(shifter_2_out), .out(R), .sel(nand_1_out));
  nand nand_1 (nand_1_out[0], comparator_1_gt, not_1_out);
  and and_1 (nand_1_out[1], SIGN, not_1_out);
  Comparator #(.width(3), .mode("unsigned")) comparator_2 (
    .a(R[7:5]), .b(3'b001), .eq(comparator_2_eq));  // open: gt, lt
  and and_2 (N0, comparator_2_eq, nor_1_out);

  assign N1 = PN0;
  assign N2 = PN1;
  assign N3 = PN2;

  // Notes on the sheet:
  //   Point Shifter
endmodule

// NORM
module NORMALIZER (
  input  [7:0] I,
  output [7:0] M,
  output [2:0] E
);

  wire comparator_1_eq, or_1_out, point_shifter_1_n1, point_shifter_1_n2, point_shifter_1_n3,
       point_shifter_1_sign, point_shifter_2_n1, point_shifter_2_n2, point_shifter_2_n3,
       point_shifter_2_sign, point_shifter_3_n1, point_shifter_3_n2, point_shifter_3_n3,
       point_shifter_3_sign, point_shifter_4_sign;
  wire [1:0] bit_extender_1_out;
  wire [2:0] log_2_1_o;
  wire [3:0] bit_extender_2_out, cla_adder_1_s, cla_adder_2_s, multiplexer_2_out, multiplexer_3_out,
       not_1_out, point_shifter_1_n0;
  wire [7:0] point_shifter_1_r, point_shifter_2_r, point_shifter_3_r, point_shifter_4_r;

  POINT_SHIFTER point_shifter_1 (
    .A(I), .PN0(1'b0), .PN1(1'b0), .PN2(1'b0), .PN3(1'b0), .R(point_shifter_1_r), .N0(point_shifter_1_n0[0]),
    .N1(point_shifter_1_n1), .N2(point_shifter_1_n2), .N3(point_shifter_1_n3), .SIGN(point_shifter_1_sign));
  POINT_SHIFTER point_shifter_2 (
    .A(point_shifter_1_r), .PN0(point_shifter_1_n0[0]), .PN1(point_shifter_1_n1), .PN2(point_shifter_1_n2),
    .PN3(point_shifter_1_n3), .R(point_shifter_2_r), .N0(point_shifter_1_n0[1]), .N1(point_shifter_2_n1),
    .N2(point_shifter_2_n2), .N3(point_shifter_2_n3), .SIGN(point_shifter_2_sign));
  LOG_2 log_2_1 (.I({4'b0000, point_shifter_1_n0}), .O(log_2_1_o));
  POINT_SHIFTER point_shifter_3 (
    .A(point_shifter_2_r), .PN0(point_shifter_1_n0[1]), .PN1(point_shifter_2_n1), .PN2(point_shifter_2_n2),
    .PN3(point_shifter_2_n3), .R(point_shifter_3_r), .N0(point_shifter_1_n0[2]), .N1(point_shifter_3_n1),
    .N2(point_shifter_3_n2), .N3(point_shifter_3_n3), .SIGN(point_shifter_3_sign));
  Bit_Extender #(.in_width(3), .out_width(2)) bit_extender_1 (.in(log_2_1_o), .out(bit_extender_1_out));
  assign bit_extender_2_out = {{1{1'b0}}, log_2_1_o};  // Bit_Extender bit_extender_2
  Multiplexer #(.select(2), .width(8), .enable("false")) multiplexer_1 (
    .in0(point_shifter_1_r), .in1(point_shifter_2_r), .in2(point_shifter_3_r), .in3(point_shifter_4_r),
    .out(M), .sel(bit_extender_1_out));
  POINT_SHIFTER point_shifter_4 (
    .A(point_shifter_3_r), .PN0(point_shifter_1_n0[2]), .PN1(point_shifter_3_n1), .PN2(point_shifter_3_n2),
    .PN3(point_shifter_3_n3), .R(point_shifter_4_r), .N0(point_shifter_1_n0[3]), .SIGN(point_shifter_4_sign));  // open: N1, N2, N3
  CLA_ADDER cla_adder_1 (.Ci(1'b0), .A(bit_extender_2_out), .B(4'b0001), .S(cla_adder_1_s));  // open: Co
  Comparator #(.width(3)) comparator_1 (.a(I[7:5]), .b(3'b001), .eq(comparator_1_eq));  // open: gt, lt
  or or_1 (or_1_out, point_shifter_4_sign, point_shifter_3_sign, point_shifter_2_sign, point_shifter_1_sign);
  assign not_1_out = ~multiplexer_2_out;  // NOT_Gate not_1, 4 bits wide
  Multiplexer #(.width(4), .enable("false")) multiplexer_2 (
    .in0(cla_adder_1_s), .in1(4'b0000), .out(multiplexer_2_out), .sel(comparator_1_eq));
  Bit_Extender #(.in_width(4), .out_width(3)) bit_extender_3 (.in(multiplexer_3_out), .out(E));
  Multiplexer #(.width(4), .enable("false")) multiplexer_3 (
    .in0(multiplexer_2_out), .in1(cla_adder_2_s), .out(multiplexer_3_out), .sel(or_1_out));
  CLA_ADDER cla_adder_2 (.Ci(1'b0), .A(not_1_out), .B(4'b0001), .S(cla_adder_2_s));  // open: Co

  // Notes on the sheet:
  //   Normalizer
endmodule

// LOG2
module LOG_2 (
  input  [7:0] I,
  output [2:0] O
);

  or or_1 (O[0], I[1], I[3], I[5], I[7]);
  or or_2 (O[1], I[2], I[3], I[6], I[7]);
  or or_3 (O[2], I[4], I[5], I[6], I[7]);

  // Notes on the sheet:
  //   Log2 Circuit
endmodule

// FMUL
module FLOAT_MUL (
  input  [7:0] A,
  input  [7:0] B,
  output [7:0] C
);

  wire [2:0] normalizer_1_e;
  wire [3:0] bit_extender_3_out, bit_extender_4_out, bit_extender_6_out, bit_extender_7_out, cla_adder_1_s,
       cla_adder_2_s;
  wire [7:0] bit_extender_1_out, bit_extender_2_out, bit_extender_5_out, normalizer_1_m, subtractor_8_1_s;
  wire [15:0] multiplyer_8_1_p;

  assign bit_extender_1_out = {{3{1'b0}}, {1'b1, A[3:0]}};  // Bit_Extender bit_extender_1
  MULTIPLYER_8 multiplyer_8_1 (.A(bit_extender_1_out), .B(bit_extender_2_out), .P(multiplyer_8_1_p));
  assign bit_extender_2_out = {{3{1'b0}}, {1'b1, B[3:0]}};  // Bit_Extender bit_extender_2
  assign bit_extender_3_out = {{1{1'b0}}, A[6:4]};  // Bit_Extender bit_extender_3
  CLA_ADDER cla_adder_1 (.Ci(1'b0), .A(bit_extender_3_out), .B(bit_extender_4_out), .S(cla_adder_1_s));  // open: Co
  assign bit_extender_4_out = {{1{1'b0}}, B[6:4]};  // Bit_Extender bit_extender_4
  xor xor_1 (C[7], A[7], B[7]);
  assign bit_extender_5_out = {{4{1'b0}}, cla_adder_1_s};  // Bit_Extender bit_extender_5
  NORMALIZER normalizer_1 (
    .I(multiplyer_8_1_p[10:3]), .M({normalizer_1_m[7:5], C[3:0], normalizer_1_m[0]}), .E(normalizer_1_e));
  assign bit_extender_6_out = {{1{1'b0}}, normalizer_1_e};  // Bit_Extender bit_extender_6
  SUBTRACTOR_8 subtractor_8_1 (.Bi(1'b0), .A(bit_extender_5_out), .B(8'h3), .S(subtractor_8_1_s));  // open: Bo
  Bit_Extender #(.out_width(4)) bit_extender_7 (.in(subtractor_8_1_s), .out(bit_extender_7_out));
  CLA_ADDER cla_adder_2 (.Ci(1'b0), .A(bit_extender_6_out), .B(bit_extender_7_out), .S(cla_adder_2_s));  // open: Co
  Bit_Extender #(.in_width(4), .out_width(3)) bit_extender_8 (.in(cla_adder_2_s), .out(C[6:4]));

  // Notes on the sheet:
  //   Float8 Multiplyer
endmodule
