// Logisim project MULTIPLYER.circ as structural Verilog: 4 circuits, main circuit main
module main (
  input  [3:0] in_1,
  input  [3:0] in_2,
  output [7:0] out_3
);

  MULTIPLYER multiplyer_1 (.A(in_1), .B(in_2), .P(out_3));
endmodule

// PROD
module PROD_GENERATOR (
  input  [3:0] A,
  input  [3:0] B,
  output [3:0] P1,
  output [3:0] P2,
  output [3:0] P3,
  output [3:0] P4
);

  and and_1 (P1[0], A[0], B[0]);
  and and_2 (P1[1], A[1], B[0]);
  and and_3 (P1[2], A[2], B[0]);
  and and_4 (P1[3], A[3], B[0]);
  and and_5 (P2[0], A[0], B[1]);
  and and_6 (P2[1], A[1], B[1]);
  and and_7 (P2[2], A[2], B[1]);
  and and_8 (P2[3], A[3], B[1]);
  and and_9 (P3[0], A[0], B[2]);
  and and_10 (P3[1], A[1], B[2]);
  and and_11 (P3[2], A[2], B[2]);
  and and_12 (P3[3], A[3], B[2]);
  and and_13 (P4[0], A[0], B[3]);
  and and_14 (P4[1], A[1], B[3]);
  and and_15 (P4[2], A[2], B[3]);
  and and_16 (P4[3], A[3], B[3]);

  // Notes on the sheet:
  //   A
  //   B
  //   4-Bit Product Generator
  //   P1..P4
endmodule

// MUL
module MULTIPLYER (
  input  [3:0] A,
  input  [3:0] B,
  output [7:0] P
);

  wire [3:0] prod_generator_1_p2, prod_generator_1_p3, prod_generator_1_p4;
  wire [3:1] cla_adder_1_s, cla_adder_2_s, prod_generator_1_p1;
  wire [3:3] cla_adder_1_co, cla_adder_2_co;

  PROD_GENERATOR prod_generator_1 (
    .A(A), .B(B), .P1({prod_generator_1_p1, P[0]}), .P2(prod_generator_1_p2), .P3(prod_generator_1_p3),
    .P4(prod_generator_1_p4));
  CLA_ADDER cla_adder_1 (
    .Ci(1'b0), .A({1'b0, prod_generator_1_p1}), .B(prod_generator_1_p2), .S({cla_adder_1_s, P[1]}),
    .Co(cla_adder_1_co[3]));
  CLA_ADDER cla_adder_2 (
    .Ci(1'b0), .A({cla_adder_1_co[3], cla_adder_1_s}), .B(prod_generator_1_p3), .S({cla_adder_2_s, P[2]}),
    .Co(cla_adder_2_co[3]));
  CLA_ADDER cla_adder_3 (
    .Ci(1'b0), .A({cla_adder_2_co[3], cla_adder_2_s}), .B(prod_generator_1_p4), .S(P[6:3]), .Co(P[7]));

  // Notes on the sheet:
  //   4-Bit Multiplyer
endmodule

module MULTIPLYER_8 (
  input  [7:0] A,
  input  [7:0] B,
  output [15:0] P
);

  wire cla_adder_8_1_co, cla_adder_16_1_co;
  wire [7:0] cla_adder_8_1_s, multiplyer_1_p, multiplyer_2_p, multiplyer_3_p, multiplyer_4_p;
  wire [15:0] cla_adder_16_1_s;

  // Probe on A
  // Probe on B
  MULTIPLYER multiplyer_1 (.A(A[3:0]), .B(B[3:0]), .P(multiplyer_1_p));
  MULTIPLYER multiplyer_2 (.A(A[7:4]), .B(B[3:0]), .P(multiplyer_2_p));
  MULTIPLYER multiplyer_3 (.A(A[3:0]), .B(B[7:4]), .P(multiplyer_3_p));
  MULTIPLYER multiplyer_4 (.A(A[7:4]), .B(B[7:4]), .P(multiplyer_4_p));
  CLA_ADDER_8 cla_adder_8_1 (
    .Ci(1'b0), .A(multiplyer_2_p), .B(multiplyer_3_p), .S(cla_adder_8_1_s), .Co(cla_adder_8_1_co));
  CLA_ADDER_16 cla_adder_16_1 (
    .Ci(cla_adder_8_1_co), .A({4'b0000, cla_adder_8_1_s, 4'b0000}), .B({multiplyer_4_p, {8{1'b0}}}),
    .S(cla_adder_16_1_s), .Co(cla_adder_16_1_co));
  CLA_ADDER_16 cla_adder_16_2 (
    .Ci(cla_adder_16_1_co), .A({{8{1'b0}}, multiplyer_1_p}), .B(cla_adder_16_1_s), .S(P));  // open: Co
  // Probe on P

  // Notes on the sheet:
  //   AL
  //   AH
  //   BL
  //   BH
  //   8-Bit Multiplyer
  //   Z0
  //   Z1
  //   Z2
  //   Z3
endmodule
