// Logisim project npux.circ as structural Verilog: 7 circuits, main circuit main
module main (
  input  [31:0] in_1,
  input  [31:0] in_2,
  input  [31:0] in_3,
  input  [31:0] in_4,
  input  [31:0] in_5,
  input  [31:0] in_6,
  input  [31:0] in_7,
  input  [31:0] in_8,
  output [31:0] out_9
);

  wire clock_1_out, comparator_1_eq, edge_detector_1_clk_o;
  wire [11:0] bit_extender_1_out;
  wire [31:0] adder_1_out, inputs_o0, inputs_o1, inputs_o2, inputs_o3, inputs_o4, inputs_o5, inputs_o6,
       inputs_o7, multiplexer_1_out, neuron_0_1_y, neuron_0_y, neuron_1_1_y, neuron_1_y, neuron_2_1_y,
       neuron_2_y, neuron_3_y, neuron_4_y, register_1_q, weight_0_1_o0, weight_0_1_o1, weight_0_1_o2,
       weight_0_1_o3, weight_0_1_o4, weight_0_1_o5, weight_0_1_o6, weight_0_1_o7, weight_0_2_o0,
       weight_0_2_o1, weight_0_2_o2, weight_0_2_o3, weight_0_2_o4, weight_0_2_o5, weight_0_2_o6,
       weight_0_2_o7, weight_0_o0, weight_0_o1, weight_0_o2, weight_0_o3, weight_0_o4, weight_0_o5,
       weight_0_o6, weight_0_o7, weight_1_1_o0, weight_1_1_o1, weight_1_1_o2, weight_1_1_o3, weight_1_1_o4,
       weight_1_1_o5, weight_1_1_o6, weight_1_1_o7, weight_1_o0, weight_1_o1, weight_1_o2, weight_1_o3,
       weight_1_o4, weight_1_o5, weight_1_o6, weight_1_o7, weight_2_1_o0, weight_2_1_o1, weight_2_1_o2,
       weight_2_1_o3, weight_2_1_o4, weight_2_1_o5, weight_2_1_o6, weight_2_1_o7, weight_2_o0, weight_2_o1,
       weight_2_o2, weight_2_o3, weight_2_o4, weight_2_o5, weight_2_o6, weight_2_o7, weight_3_o0,
       weight_3_o1, weight_3_o2, weight_3_o3, weight_3_o4, weight_3_o5, weight_3_o6, weight_3_o7,
       weight_4_o0, weight_4_o1, weight_4_o2, weight_4_o3, weight_4_o4, weight_4_o5, weight_4_o6, weight_4_o7;

  Clock clock_1 (.out(clock_1_out));
  Multiplexer #(.width(32)) multiplexer_1 (.in0(32'h1), .in1(32'h3001), .out(multiplexer_1_out), .sel(comparator_1_eq));
  Comparator #(.mode("unsigned"), .width(12)) comparator_1 (
    .a({12{1'b1}}), .b(bit_extender_1_out), .eq(comparator_1_eq));  // open: gt, lt
  Adder #(.width(32)) adder_1 (.a(multiplexer_1_out), .b(register_1_q), .out(adder_1_out));  // open: cin, cout
  Edge_Detector edge_detector_1 (.CLK_I(clock_1_out), .CLK_O(edge_detector_1_clk_o));
  Bit_Extender #(.in_width(32), .out_width(12)) bit_extender_1 (.in(register_1_q), .out(bit_extender_1_out));
  Register #(.width(32)) register_1 (
    .D(adder_1_out), .en(1'b1), .Q(register_1_q), .clk(edge_detector_1_clk_o));  // open: clr
  Tensors inputs (
    .CLK(clock_1_out), .I0(in_1), .I1(in_2), .I2(in_3), .I3(in_4), .I4(in_5), .I5(in_6), .I6(in_7),
    .I7(in_8), .O0(inputs_o0), .O1(inputs_o1), .O2(inputs_o2), .O3(inputs_o3), .O4(inputs_o4),
    .O5(inputs_o5), .O6(inputs_o6), .O7(inputs_o7));
  Weights weight_0 (
    .CLK(clock_1_out), .i0(inputs_o0), .i1(inputs_o1), .i2(inputs_o2), .i3(inputs_o3), .i4(inputs_o4),
    .i5(inputs_o5), .i6(inputs_o6), .i7(inputs_o7), .Bias(32'h3f9c28f6), .O0(weight_0_o0), .O1(weight_0_o1),
    .O2(weight_0_o2), .O3(weight_0_o3), .O4(weight_0_o4), .O5(weight_0_o5), .O6(weight_0_o6), .O7(weight_0_o7));
  Weights weight_1 (
    .CLK(clock_1_out), .i0(inputs_o0), .i1(inputs_o1), .i2(inputs_o2), .i3(inputs_o3), .i4(inputs_o4),
    .i5(inputs_o5), .i6(inputs_o6), .i7(inputs_o7), .Bias(32'h400851ec), .O0(weight_1_o0), .O1(weight_1_o1),
    .O2(weight_1_o2), .O3(weight_1_o3), .O4(weight_1_o4), .O5(weight_1_o5), .O6(weight_1_o6), .O7(weight_1_o7));
  Weights weight_2 (
    .CLK(clock_1_out), .i0(inputs_o0), .i1(inputs_o1), .i2(inputs_o2), .i3(inputs_o3), .i4(inputs_o4),
    .i5(inputs_o5), .i6(inputs_o6), .i7(inputs_o7), .Bias(32'h405eb852), .O0(weight_2_o0), .O1(weight_2_o1),
    .O2(weight_2_o2), .O3(weight_2_o3), .O4(weight_2_o4), .O5(weight_2_o5), .O6(weight_2_o6), .O7(weight_2_o7));
  Weights weight_3 (
    .CLK(clock_1_out), .i0(inputs_o0), .i1(inputs_o1), .i2(inputs_o2), .i3(inputs_o3), .i4(inputs_o4),
    .i5(inputs_o5), .i6(inputs_o6), .i7(inputs_o7), .Bias(32'h402ae148), .O0(weight_3_o0), .O1(weight_3_o1),
    .O2(weight_3_o2), .O3(weight_3_o3), .O4(weight_3_o4), .O5(weight_3_o5), .O6(weight_3_o6), .O7(weight_3_o7));
  Weights weight_4 (
    .CLK(clock_1_out), .i0(inputs_o0), .i1(inputs_o1), .i2(inputs_o2), .i3(inputs_o3), .i4(inputs_o4),
    .i5(inputs_o5), .i6(inputs_o6), .i7(inputs_o7), .Bias(32'h409051ec), .O0(weight_4_o0), .O1(weight_4_o1),
    .O2(weight_4_o2), .O3(weight_4_o3), .O4(weight_4_o4), .O5(weight_4_o5), .O6(weight_4_o6), .O7(weight_4_o7));
  Neuron neuron_0 (
    .S0(weight_0_o0), .S1(weight_0_o1), .S2(weight_0_o2), .S3(weight_0_o3), .S4(weight_0_o4),
    .S5(weight_0_o5), .S6(weight_0_o6), .S7(weight_0_o7), .Y(neuron_0_y));
  Neuron neuron_1 (
    .S0(weight_1_o0), .S1(weight_1_o1), .S2(weight_1_o2), .S3(weight_1_o3), .S4(weight_1_o4),
    .S5(weight_1_o5), .S6(weight_1_o6), .S7(weight_1_o7), .Y(neuron_1_y));
  Neuron neuron_2 (
    .S0(weight_2_o0), .S1(weight_2_o1), .S2(weight_2_o2), .S3(weight_2_o3), .S4(weight_2_o4),
    .S5(weight_2_o5), .S6(weight_2_o6), .S7(weight_2_o7), .Y(neuron_2_y));
  Neuron neuron_3 (
    .S0(weight_3_o0), .S1(weight_3_o1), .S2(weight_3_o2), .S3(weight_3_o3), .S4(weight_3_o4),
    .S5(weight_3_o5), .S6(weight_3_o6), .S7(weight_3_o7), .Y(neuron_3_y));
  Neuron neuron_4 (
    .S0(weight_4_o0), .S1(weight_4_o1), .S2(weight_4_o2), .S3(weight_4_o3), .S4(weight_4_o4),
    .S5(weight_4_o5), .S6(weight_4_o6), .S7(weight_4_o7), .Y(neuron_4_y));
  Weights weight_0_1 (
    .CLK(clock_1_out), .i0(neuron_0_y), .i1(neuron_1_y), .i2(neuron_2_y), .i3(neuron_3_y), .i4(neuron_4_y),
    .i5({32{1'b0}}), .i6({32{1'b0}}), .i7({32{1'b0}}), .Bias(32'h3f9c28f6), .O0(weight_0_1_o0),
    .O1(weight_0_1_o1), .O2(weight_0_1_o2), .O3(weight_0_1_o3), .O4(weight_0_1_o4), .O5(weight_0_1_o5),
    .O6(weight_0_1_o6), .O7(weight_0_1_o7));
  Weights weight_1_1 (
    .CLK(clock_1_out), .i0(neuron_0_y), .i1(neuron_1_y), .i2(neuron_2_y), .i3(neuron_3_y), .i4(neuron_4_y),
    .i5({32{1'b0}}), .i6({32{1'b0}}), .i7({32{1'b0}}), .Bias(32'h400851ec), .O0(weight_1_1_o0),
    .O1(weight_1_1_o1), .O2(weight_1_1_o2), .O3(weight_1_1_o3), .O4(weight_1_1_o4), .O5(weight_1_1_o5),
    .O6(weight_1_1_o6), .O7(weight_1_1_o7));
  Weights weight_2_1 (
    .CLK(clock_1_out), .i0(neuron_0_y), .i1(neuron_1_y), .i2(neuron_2_y), .i3(neuron_3_y), .i4(neuron_4_y),
    .i5({32{1'b0}}), .i6({32{1'b0}}), .i7({32{1'b0}}), .Bias(32'h405eb852), .O0(weight_2_1_o0),
    .O1(weight_2_1_o1), .O2(weight_2_1_o2), .O3(weight_2_1_o3), .O4(weight_2_1_o4), .O5(weight_2_1_o5),
    .O6(weight_2_1_o6), .O7(weight_2_1_o7));
  Neuron neuron_0_1 (
    .S0(weight_0_1_o0), .S1(weight_0_1_o1), .S2(weight_0_1_o2), .S3(weight_0_1_o3), .S4(weight_0_1_o4),
    .S5(weight_0_1_o5), .S6(weight_0_1_o6), .S7(weight_0_1_o7), .Y(neuron_0_1_y));
  Neuron neuron_1_1 (
    .S0(weight_1_1_o0), .S1(weight_1_1_o1), .S2(weight_1_1_o2), .S3(weight_1_1_o3), .S4(weight_1_1_o4),
    .S5(weight_1_1_o5), .S6(weight_1_1_o6), .S7(weight_1_1_o7), .Y(neuron_1_1_y));
  Neuron neuron_2_1 (
    .S0(weight_2_1_o0), .S1(weight_2_1_o1), .S2(weight_2_1_o2), .S3(weight_2_1_o3), .S4(weight_2_1_o4),
    .S5(weight_2_1_o5), .S6(weight_2_1_o6), .S7(weight_2_1_o7), .Y(neuron_2_1_y));
  Weights weight_0_2 (
    .CLK(clock_1_out), .i0(neuron_0_1_y), .i1(neuron_1_1_y), .i2(neuron_2_1_y), .i3({32{1'b0}}),
    .i4({32{1'b0}}), .i5({32{1'b0}}), .i6({32{1'b0}}), .i7({32{1'b0}}), .Bias(32'h4148f5c3),
    .O0(weight_0_2_o0), .O1(weight_0_2_o1), .O2(weight_0_2_o2), .O3(weight_0_2_o3), .O4(weight_0_2_o4),
    .O5(weight_0_2_o5), .O6(weight_0_2_o6), .O7(weight_0_2_o7));
  Neuron neuron_0_2 (
    .S0(weight_0_2_o0), .S1(weight_0_2_o1), .S2(weight_0_2_o2), .S3(weight_0_2_o3), .S4(weight_0_2_o4),
    .S5(weight_0_2_o5), .S6(weight_0_2_o6), .S7(weight_0_2_o7), .Y(out_9));
endmodule

module Tensors (
  input  CLK,
  input  [31:0] I0,
  input  [31:0] I1,
  input  [31:0] I2,
  input  [31:0] I3,
  input  [31:0] I4,
  input  [31:0] I5,
  input  [31:0] I6,
  input  [31:0] I7,
  output [31:0] O0,
  output [31:0] O1,
  output [31:0] O2,
  output [31:0] O3,
  output [31:0] O4,
  output [31:0] O5,
  output [31:0] O6,
  output [31:0] O7
);

  Register #(.width(32)) register_1 (.D(I0), .Q(O0), .clk(CLK));  // open: en, clr
  Register #(.width(32)) register_2 (.D(I1), .Q(O1), .clk(CLK));  // open: en, clr
  Register #(.width(32)) register_3 (.D(I2), .Q(O2), .clk(CLK));  // open: en, clr
  Register #(.width(32)) register_4 (.D(I3), .Q(O3), .clk(CLK));  // open: en, clr
  Register #(.width(32)) register_5 (.D(I4), .Q(O4), .clk(CLK));  // open: en, clr
  Register #(.width(32)) register_6 (.D(I5), .Q(O5), .clk(CLK));  // open: en, clr
  Register #(.width(32)) register_7 (.D(I6), .Q(O6), .clk(CLK));  // open: en, clr
  Register #(.width(32)) register_8 (.D(I7), .Q(O7), .clk(CLK));  // open: en, clr
endmodule

module Neuron (
  input  [31:0] S0,
  input  [31:0] S1,
  input  [31:0] S2,
  input  [31:0] S3,
  input  [31:0] S4,
  input  [31:0] S5,
  input  [31:0] S6,
  input  [31:0] S7,
  output [31:0] Y
);

  wire [31:0] fpadder_1_out, fpadder_2_out, fpadder_3_out, fpadder_4_out, fpadder_5_out, fpadder_6_out,
       fpadder_7_out;

  FPAdder fpadder_1 (.a(S0), .b(S1), .out(fpadder_1_out));
  FPAdder fpadder_2 (.a(S2), .b(S3), .out(fpadder_2_out));
  FPAdder fpadder_3 (.a(S4), .b(S5), .out(fpadder_3_out));
  FPAdder fpadder_4 (.a(S6), .b(S7), .out(fpadder_4_out));
  FPAdder fpadder_5 (.a(fpadder_1_out), .b(fpadder_2_out), .out(fpadder_5_out));
  FPAdder fpadder_6 (.a(fpadder_5_out), .b(fpadder_7_out), .out(fpadder_6_out));
  FPAdder fpadder_7 (.a(fpadder_3_out), .b(fpadder_4_out), .out(fpadder_7_out));
  ReLU activator (.X(fpadder_6_out), .Y(Y));
endmodule

module Weights (
  input  CLK,
  input  [31:0] i0,
  input  [31:0] i1,
  input  [31:0] i2,
  input  [31:0] i3,
  input  [31:0] i4,
  input  [31:0] i5,
  input  [31:0] i6,
  input  [31:0] i7,
  input  [31:0] Bias,
  output [31:0] O0,
  output [31:0] O1,
  output [31:0] O2,
  output [31:0] O3,
  output [31:0] O4,
  output [31:0] O5,
  output [31:0] O6,
  output [31:0] O7
);

  wire undriven;
  wire [31:0] weights_o0, weights_o1, weights_o2, weights_o3, weights_o4, weights_o5, weights_o6, weights_o7,
       Xavier_Initializer_o0, Xavier_Initializer_o1, Xavier_Initializer_o2, Xavier_Initializer_o3,
       Xavier_Initializer_o4, Xavier_Initializer_o5, Xavier_Initializer_o6, Xavier_Initializer_o7;

  Randomizer Xavier_Initializer (
    .Bias(Bias), .in_2(undriven), .O0(Xavier_Initializer_o0), .O1(Xavier_Initializer_o1),
    .O2(Xavier_Initializer_o2), .O3(Xavier_Initializer_o3), .O4(Xavier_Initializer_o4),
    .O5(Xavier_Initializer_o5), .O6(Xavier_Initializer_o6), .O7(Xavier_Initializer_o7));
  Tensors weights (
    .CLK(CLK), .I0(Xavier_Initializer_o0), .I1(Xavier_Initializer_o1), .I2(Xavier_Initializer_o2),
    .I3(Xavier_Initializer_o3), .I4(Xavier_Initializer_o4), .I5(Xavier_Initializer_o5),
    .I6(Xavier_Initializer_o6), .I7(Xavier_Initializer_o7), .O0(weights_o0), .O1(weights_o1),
    .O2(weights_o2), .O3(weights_o3), .O4(weights_o4), .O5(weights_o5), .O6(weights_o6), .O7(weights_o7));
  FPMultiplier fpmultiplier_1 (.a(i0), .b(weights_o0), .out(O0));
  FPMultiplier fpmultiplier_2 (.a(i1), .b(weights_o1), .out(O1));
  FPMultiplier fpmultiplier_3 (.a(i2), .b(weights_o2), .out(O2));
  FPMultiplier fpmultiplier_4 (.a(i3), .b(weights_o3), .out(O3));
  FPMultiplier fpmultiplier_5 (.a(i4), .b(weights_o4), .out(O4));
  FPMultiplier fpmultiplier_6 (.a(i5), .b(weights_o5), .out(O5));
  FPMultiplier fpmultiplier_7 (.a(i6), .b(weights_o6), .out(O6));
  FPMultiplier fpmultiplier_8 (.a(i7), .b(weights_o7), .out(O7));
endmodule

module Randomizer (
  input  [31:0] Bias,
  input  in_2,
  output [31:0] O0,
  output [31:0] O1,
  output [31:0] O2,
  output [31:0] O3,
  output [31:0] O4,
  output [31:0] O5,
  output [31:0] O6,
  output [31:0] O7
);

  wire [31:0] undriven, undriven_2, undriven_3, undriven_4, undriven_5, undriven_6, undriven_7, undriven_8;

  Random #(.seed(1004840133), .width(32)) random_1 ();  // open: clk, next, out, clr
  // Random #(.seed(1004845500), .width(32)) random_2: pin names not known; wires that end beside it: in_2, in_2
  // Random #(.seed(1004855500), .width(32)) random_3: pin names not known; wires that end beside it: in_2, in_2
  // Random #(.seed(1004830500), .width(32)) random_4: pin names not known; wires that end beside it: in_2, in_2
  // Random #(.seed(1004810100), .width(32)) random_5: pin names not known; wires that end beside it: in_2, in_2
  // Random #(.seed(1004910100), .width(32)) random_6: pin names not known; wires that end beside it: in_2, in_2
  // Random #(.seed(1004610100), .width(32)) random_7: pin names not known; wires that end beside it: in_2, in_2
  // Random #(.seed(1005520300), .width(32)) random_8: pin names not known; wires that end beside it: in_2, in_2
  FPMultiplier fpmultiplier_1 (.a(Bias), .b(undriven), .out(O0));
  FPMultiplier fpmultiplier_2 (.a(Bias), .b(undriven_2), .out(O1));
  FPMultiplier fpmultiplier_3 (.a(Bias), .b(undriven_3), .out(O2));
  FPMultiplier fpmultiplier_4 (.a(Bias), .b(undriven_4), .out(O3));
  FPMultiplier fpmultiplier_5 (.a(Bias), .b(undriven_5), .out(O4));
  FPMultiplier fpmultiplier_6 (.a(Bias), .b(undriven_6), .out(O5));
  FPMultiplier fpmultiplier_7 (.a(Bias), .b(undriven_7), .out(O6));
  FPMultiplier fpmultiplier_8 (.a(Bias), .b(undriven_8), .out(O7));
endmodule

module ReLU (
  input  [31:0] X,
  output [31:0] Y
);

  wire comparator_1_gt, not_1_out;

  Comparator #(.width(32)) comparator_1 (.a({32{1'b0}}), .b(X), .gt(comparator_1_gt));  // open: eq, lt
  Multiplexer #(.width(32)) multiplexer_1 (.in0({32{1'b0}}), .in1(X), .out(Y), .sel(not_1_out));
  not not_1 (not_1_out, comparator_1_gt);
endmodule

module Edge_Detector (
  input  CLK_I,
  output CLK_O
);

  wire and_1_out, nand_1_out, not_1_out, not_2_out;

  not not_1 (not_1_out, CLK_I);
  not not_2 (not_2_out, CLK_I);
  and and_1 (and_1_out, not_2_out, CLK_I);
  nand nand_1 (nand_1_out, not_1_out, CLK_I);
  Multiplexer multiplexer_1 (.in0(nand_1_out), .in1(and_1_out), .out(CLK_O), .sel(CLK_I));
endmodule
