// Logisim project WR80X_1.6.2.circ as structural Verilog: 43 circuits, main circuit main
module main (
  input  [7:0] P7_IN,
  input  OVERFLOW,
  input  DEBUG,
  input  TRANSFER,
  output [7:0] P7_OUT
);

  wire and_1_out, DB_out, i0_out, i1_out, i2_out, i3_out, not_1_out, not_2_out, ON_out,
       ram_controller_1_ram_sel_ld, ram_controller_1_ram_str, ram_controller_1_rom_sel_ld, RS_out,
       transfer_circuit_1_cpu_on, transfer_circuit_1_rom, transfer_circuit_1_sel, transfer_circuit_1_str,
       tty_controller_1_clk, tty_controller_1_en, wr80_arch_1_clear, wr80_arch_1_clk_out, wr80_arch_1_in_acc,
       wr80_arch_1_p3s, wr80_arch_1_p6s, wr80_arch_1_p7s;
  wire [2:0] wr80_arch_1_p2s;
  wire [3:0] graph_decoder_1_count, graph_decoder_1_count_2, register_1_q, register_1_q_2;
  wire [6:0] keyboard_1_data, tty_controller_1_data;
  wire [7:0] bit_extender_1_out, controlled_buffer_1_out, ram_1_data, ram_2_data, ram_controller_1_o0,
       rom_1_data, transfer_circuit_1_data, wr80_arch_1_p2_out, wr80_arch_1_p3_out, wr80_arch_1_p6_out;
  wire [11:0] transfer_circuit_1_addr, wr80_arch_1_p0_p1;
  wire [15:0] wr80_arch_1_p4_p5;
  wire [31:0] graph_decoder_1_l0, graph_decoder_1_l1, graph_decoder_1_l2, graph_decoder_1_l3,
       graph_decoder_1_l4, graph_decoder_1_l5, graph_decoder_1_l6, graph_decoder_1_l7, graph_decoder_1_l8,
       graph_decoder_1_l9, graph_decoder_1_l10, graph_decoder_1_l11, graph_decoder_1_l12,
       graph_decoder_1_l13, graph_decoder_1_l14, graph_decoder_1_l15, graph_decoder_1_l16,
       graph_decoder_1_l17, graph_decoder_1_l18, graph_decoder_1_l19, graph_decoder_1_l20,
       graph_decoder_1_l21, graph_decoder_1_l22, graph_decoder_1_l23, graph_decoder_1_l24,
       graph_decoder_1_l25, graph_decoder_1_l26, graph_decoder_1_l27, graph_decoder_1_l28,
       graph_decoder_1_l29, graph_decoder_1_l30, graph_decoder_1_l31;

  Button RS (.out(RS_out));
  Button ON (.out(ON_out));
  Button DB (.out(DB_out));
  Button i0 (.out(i0_out));
  Button i1 (.out(i1_out));
  Button i2 (.out(i2_out));
  Button i3 (.out(i3_out));
  Hex_Digit_Display hex_digit_display_1 (.value(register_1_q_2));  // open: dp
  WR80_Arch wr80_arch_1 (
    .RS(RS_out), .ON(ON_out), .CLK_EXT(1'b0), .CLKIN_EN(1'b1), .OVER_EN(OVERFLOW),
    .CLK_OUT(wr80_arch_1_clk_out), .P3S(wr80_arch_1_p3s), .P2S(wr80_arch_1_p2s[0]),
    .MEM_EN(wr80_arch_1_p2s[1]), .ROM_ACCESS(wr80_arch_1_p2s[2]), .P2_OUT(wr80_arch_1_p2_out),
    .P2_IN(ram_controller_1_o0), .P3_OUT(wr80_arch_1_p3_out), .P3_IN(bit_extender_1_out), .DBG_ON(DEBUG),
    .STEP_IN(DB_out), .I0(i0_out), .I1(i1_out), .I2(i2_out), .I3(i3_out), .IN_ACC(wr80_arch_1_in_acc),
    .VDD(transfer_circuit_1_cpu_on), .P0_P1(wr80_arch_1_p0_p1), .P4_P5(wr80_arch_1_p4_p5),
    .P6_OUT(wr80_arch_1_p6_out), .P6_IN(ram_2_data), .P7_OUT(P7_OUT), .P7_IN(P7_IN), .P6S(wr80_arch_1_p6s),
    .P7S(wr80_arch_1_p7s), .CLEAR(wr80_arch_1_clear));
  Hex_Digit_Display hex_digit_display_2 (.value(register_1_q));  // open: dp
  Register register_1 (
    .D(wr80_arch_1_p2_out), .Q({register_1_q_2, register_1_q}), .clk(wr80_arch_1_clk_out));  // open: en, clr
  TTY_Controller tty_controller_1 (
    .tty_data(wr80_arch_1_p3_out), .tty_wr(wr80_arch_1_p3s), .tty_clk(wr80_arch_1_clk_out), .tty_on(ON_out),
    .data(tty_controller_1_data), .clk(tty_controller_1_clk), .en(tty_controller_1_en));
  TTY tty_1 (
    .data(tty_controller_1_data), .clk(tty_controller_1_clk), .we(tty_controller_1_en),
    .clr(wr80_arch_1_clear));
  Keyboard keyboard_1 (.clk(wr80_arch_1_in_acc), .clr(wr80_arch_1_clear), .data(keyboard_1_data));  // open: re, avail
  transfer_circuit transfer_circuit_1 (
    .A(wr80_arch_1_p0_p1), .ADDR(transfer_circuit_1_addr), .SEL(transfer_circuit_1_sel),
    .STR(transfer_circuit_1_str), .CPU_D(wr80_arch_1_p2_out), .ROM_D(controlled_buffer_1_out),
    .DATA(transfer_circuit_1_data), .CPU_ON(transfer_circuit_1_cpu_on), .RAM_STR(ram_controller_1_ram_str),
    .CLK_OUT(wr80_arch_1_clk_out), .ROM_SEL(ram_controller_1_rom_sel_ld), .ROM(transfer_circuit_1_rom),
    .T_ON(TRANSFER));
  RAM #(.addrWidth(12), .bus("separate")) ram_1 (
    .addr(transfer_circuit_1_addr), .din(transfer_circuit_1_data), .data(ram_1_data),
    .str(transfer_circuit_1_sel), .sel(ram_controller_1_ram_sel_ld), .clk(transfer_circuit_1_str),
    .ld(ram_controller_1_ram_sel_ld));  // open: clr
  RAM_Controller ram_controller_1 (
    .ROM_ACC(wr80_arch_1_p2s[2]), .MEM_EN(wr80_arch_1_p2s[1]), .P2S(wr80_arch_1_p2s[0]),
    .D7(controlled_buffer_1_out[7]), .D6(controlled_buffer_1_out[6]), .D5(controlled_buffer_1_out[5]),
    .D4(controlled_buffer_1_out[4]), .D3(controlled_buffer_1_out[3]), .D2(controlled_buffer_1_out[2]),
    .D1(controlled_buffer_1_out[1]), .D0(controlled_buffer_1_out[0]),
    .ROM_SEL_LD(ram_controller_1_rom_sel_ld), .RAM_SEL_LD(ram_controller_1_ram_sel_ld),
    .RAM_STR(ram_controller_1_ram_str), .O7(ram_controller_1_o0[7]), .O6(ram_controller_1_o0[6]),
    .O5(ram_controller_1_o0[5]), .O4(ram_controller_1_o0[4]), .O3(ram_controller_1_o0[3]),
    .O2(ram_controller_1_o0[2]), .O1(ram_controller_1_o0[1]), .O0(ram_controller_1_o0[0]));
  ROM #(.addrWidth(12)) rom_1 (.addr(transfer_circuit_1_addr), .data(rom_1_data), .sel(transfer_circuit_1_rom));
  assign bit_extender_1_out = {{1{1'b0}}, keyboard_1_data};  // Bit_Extender bit_extender_1
  not not_1 (not_1_out, wr80_arch_1_clk_out);
  assign controlled_buffer_1_out = not_2_out ? ram_1_data : 8'bz;  // Controlled_Buffer controlled_buffer_1
  assign controlled_buffer_1_out = transfer_circuit_1_rom ? rom_1_data : 8'bz;  // Controlled_Buffer controlled_buffer_2
  not not_2 (not_2_out, transfer_circuit_1_rom);
  and and_1 (and_1_out, wr80_arch_1_p6s, not_1_out);
  graph_decoder graph_decoder_1 (
    .CLK(and_1_out), .L0(graph_decoder_1_l0), .L8(graph_decoder_1_l8), .L16(graph_decoder_1_l16),
    .L24(graph_decoder_1_l24), .L1(graph_decoder_1_l1), .L9(graph_decoder_1_l9), .L17(graph_decoder_1_l17),
    .L25(graph_decoder_1_l25), .L2(graph_decoder_1_l2), .L10(graph_decoder_1_l10), .L18(graph_decoder_1_l18),
    .L26(graph_decoder_1_l26), .L3(graph_decoder_1_l3), .L11(graph_decoder_1_l11), .L19(graph_decoder_1_l19),
    .L27(graph_decoder_1_l27), .L4(graph_decoder_1_l4), .L12(graph_decoder_1_l12), .L20(graph_decoder_1_l20),
    .L28(graph_decoder_1_l28), .L5(graph_decoder_1_l5), .L13(graph_decoder_1_l13), .L21(graph_decoder_1_l21),
    .L29(graph_decoder_1_l29), .L6(graph_decoder_1_l6), .L14(graph_decoder_1_l14), .L22(graph_decoder_1_l22),
    .L30(graph_decoder_1_l30), .L7(graph_decoder_1_l7), .L15(graph_decoder_1_l15), .L23(graph_decoder_1_l23),
    .L31(graph_decoder_1_l31), .DATA(wr80_arch_1_p6_out), .YX(wr80_arch_1_p4_p5), .CLR(wr80_arch_1_clear),
    .COUNTER(wr80_arch_1_p7s), .Count({graph_decoder_1_count_2, graph_decoder_1_count}));
  DotMatrix #(.inputtype("row"), .matrixcols(32), .matrixrows(32)) dotmatrix_1 (
    .row0(graph_decoder_1_l0), .row1(graph_decoder_1_l1), .row2(graph_decoder_1_l2),
    .row3(graph_decoder_1_l3), .row4(graph_decoder_1_l4), .row5(graph_decoder_1_l5),
    .row6(graph_decoder_1_l6), .row7(graph_decoder_1_l7), .row8(graph_decoder_1_l8),
    .row9(graph_decoder_1_l9), .row10(graph_decoder_1_l10), .row11(graph_decoder_1_l11),
    .row12(graph_decoder_1_l12), .row13(graph_decoder_1_l13), .row14(graph_decoder_1_l14),
    .row15(graph_decoder_1_l15), .row16(graph_decoder_1_l16), .row17(graph_decoder_1_l17),
    .row18(graph_decoder_1_l18), .row19(graph_decoder_1_l19), .row20(graph_decoder_1_l20),
    .row21(graph_decoder_1_l21), .row22(graph_decoder_1_l22), .row23(graph_decoder_1_l23),
    .row24(graph_decoder_1_l24), .row25(graph_decoder_1_l25), .row26(graph_decoder_1_l26),
    .row27(graph_decoder_1_l27), .row28(graph_decoder_1_l28), .row29(graph_decoder_1_l29),
    .row30(graph_decoder_1_l30), .row31(graph_decoder_1_l31));
  RAM #(.addrWidth(16), .bus("separate")) ram_2 (
    .addr(wr80_arch_1_p4_p5), .din(wr80_arch_1_p6_out), .data(ram_2_data), .str(1'b1), .clk(and_1_out),
    .ld(1'b1), .clr(wr80_arch_1_clear));  // open: sel
  Hex_Digit_Display hex_digit_display_3 (.value(graph_decoder_1_count_2));  // open: dp
  Hex_Digit_Display hex_digit_display_4 (.value(graph_decoder_1_count));  // open: dp

  // Notes on the sheet:
  //   KEYBOARD
  //   RAM
  //   ROM
  //   GAME POINTS
endmodule

// Decoder
module instruction_decode (
  input  RS,
  input  DE,
  input  CLK,
  input  [7:0] IN_INST,
  input  EX,
  output [2:0] ExtBits2,
  output [25:0] ExtBits,
  output CLR,
  output [19:0] OUT_INST,
  output JUMP_LOW,
  output JUMP_HIGH,
  output [7:0] OUT_ADDR,
  output _2_byte,
  output CALL
);

  wire ADD_out, and_1_out, AND_2_out, and_3_out, and_4_out, and_5_out, and_6_out, and_7_out, and_8_out,
       and_9_out, and_10_out, and_11_out, and_12_out, and_13_out, and_14_out, and_15_out, and_16_out,
       and_17_out, and_18_out, BT_out, d_ff_16_q, d_ff_17_q, extender_1_call_tmp, IN_out, JC_out, JP_out,
       JZ_out, LD_out, nor_1_out, not_1_out, not_2_out, not_3_out, not_4_out, not_5_out, NOT_6_out,
       not_7_out, not_8_out, not_9_out, not_10_out, not_11_out, not_12_out, not_13_out, or_1_out, OR_2_out,
       or_3_out, or_5_out, or_6_out, OUT_out, SHL_out, SHR_out, ST_out, SUB_out, XOR_out;

  not not_1 (not_1_out, IN_INST[7]);
  and and_1 (and_1_out, RS, or_1_out);
  not not_2 (not_2_out, IN_INST[4]);
  not not_3 (not_3_out, IN_INST[5]);
  not not_4 (not_4_out, IN_INST[6]);
  or or_1 (or_1_out, OUT_ADDR[7], OUT_ADDR[6], OUT_ADDR[5], OUT_ADDR[4], OUT_ADDR[3], OUT_ADDR[2], OUT_ADDR[1], OUT_ADDR[0]);
  not not_5 (not_5_out, IN_INST[3]);
  and AND_2 (AND_2_out, not_1_out, not_4_out, not_3_out, not_2_out, and_11_out);
  and OR_2 (OR_2_out, not_1_out, not_4_out, not_3_out, IN_INST[4], and_11_out);
  and NOT_6 (NOT_6_out, not_1_out, not_4_out, IN_INST[5], not_2_out, and_11_out);
  and XOR (XOR_out, not_1_out, not_4_out, IN_INST[5], IN_INST[4], and_11_out);
  and ADD (ADD_out, not_1_out, IN_INST[6], not_3_out, not_2_out, and_11_out);
  and SUB (SUB_out, not_1_out, IN_INST[6], not_3_out, IN_INST[4], and_11_out);
  and ST (ST_out, not_1_out, IN_INST[6], IN_INST[5], not_2_out, and_11_out);
  and LD (LD_out, not_1_out, IN_INST[6], IN_INST[5], IN_INST[4], and_11_out);
  RX_selector rx_selector_1 (
    .CLEAR(and_1_out), .CLK(DE), .EN(and_10_out), .B2(IN_INST[2]), .B1(IN_INST[1]), .B0(IN_INST[0]),
    .R0(OUT_ADDR[0]), .R1(OUT_ADDR[1]), .R2(OUT_ADDR[2]), .R3(OUT_ADDR[3]), .R4(OUT_ADDR[4]),
    .R5(OUT_ADDR[5]), .R6(OUT_ADDR[6]), .R7(OUT_ADDR[7]));
  LED led_1 (.in(AND_2_out));
  and and_3 (and_3_out, AND_2_out, not_5_out);
  LED led_2 (.in(OR_2_out));
  and and_4 (and_4_out, OR_2_out, not_5_out);
  LED led_3 (.in(NOT_6_out));
  and and_5 (and_5_out, NOT_6_out, not_5_out);
  LED led_4 (.in(XOR_out));
  and and_6 (and_6_out, XOR_out, not_5_out);
  LED led_5 (.in(ADD_out));
  and and_7 (and_7_out, ADD_out, not_5_out);
  LED led_6 (.in(SUB_out));
  and and_8 (and_8_out, SUB_out, not_5_out);
  LED led_7 (.in(ST_out));
  LED led_8 (.in(LD_out));
  and and_9 (and_9_out, LD_out, not_5_out);
  and and_10 (and_10_out, and_11_out, nor_1_out);
  D_Flip_Flop #(.trigger("falling")) d_ff_1 (.clk(DE), .D(and_3_out), .Q(OUT_INST[0]));  // open: Qn, preset, en, reset
  D_Flip_Flop #(.trigger("falling")) d_ff_2 (.clk(DE), .D(and_4_out), .Q(OUT_INST[1]));  // open: Qn, preset, en, reset
  D_Flip_Flop #(.trigger("falling")) d_ff_3 (.clk(DE), .D(and_5_out), .Q(OUT_INST[2]));  // open: Qn, preset, en, reset
  D_Flip_Flop #(.trigger("falling")) d_ff_4 (.clk(DE), .D(and_6_out), .Q(OUT_INST[3]));  // open: Qn, preset, en, reset
  D_Flip_Flop #(.trigger("falling")) d_ff_5 (.clk(DE), .D(and_7_out), .Q(OUT_INST[4]));  // open: Qn, preset, en, reset
  D_Flip_Flop #(.trigger("falling")) d_ff_6 (.clk(DE), .D(and_8_out), .Q(OUT_INST[5]));  // open: Qn, preset, en, reset
  or or_3 (or_3_out, SUB_out, LD_out);
  D_Flip_Flop #(.trigger("falling")) d_ff_7 (.clk(DE), .D(ST_out), .Q(OUT_INST[6]));  // open: Qn, preset, en, reset
  D_Flip_Flop #(.trigger("falling")) d_ff_8 (.clk(DE), .D(and_9_out), .Q(OUT_INST[7]));  // open: Qn, preset, en, reset
  and and_11 (and_11_out, DE, not_11_out);
  not not_7 (not_7_out, IN_INST[5]);
  not not_8 (not_8_out, IN_INST[4]);
  not not_9 (not_9_out, IN_INST[6]);
  not not_10 (not_10_out, CLK);
  nor nor_1 (nor_1_out, JC_out, JZ_out, JP_out);
  not not_11 (not_11_out, or_5_out);
  and IN (IN_out, IN_INST[7], not_9_out, not_7_out, not_8_out, and_11_out);
  and OUT (OUT_out, IN_INST[7], not_9_out, not_7_out, IN_INST[4], and_11_out);
  and SHR (SHR_out, IN_INST[7], not_9_out, IN_INST[5], not_8_out, and_11_out);
  and SHL (SHL_out, IN_INST[7], not_9_out, IN_INST[5], IN_INST[4], and_11_out);
  and BT (BT_out, IN_INST[7], IN_INST[6], not_7_out, not_8_out, and_11_out);
  and JC (JC_out, IN_INST[7], IN_INST[6], not_7_out, IN_INST[4], and_11_out);
  and JZ (JZ_out, IN_INST[7], IN_INST[6], IN_INST[5], not_8_out, and_11_out);
  and JP (JP_out, IN_INST[7], IN_INST[6], IN_INST[5], IN_INST[4], and_11_out);
  and and_12 (and_12_out, DE, not_10_out);
  LED led_9 (.in(IN_out));
  and and_13 (and_13_out, IN_out, not_5_out);
  LED led_10 (.in(OUT_out));
  and and_14 (and_14_out, OUT_out, not_5_out);
  LED led_11 (.in(SHR_out));
  and and_15 (and_15_out, SHR_out, not_5_out);
  LED led_12 (.in(SHL_out));
  and and_16 (and_16_out, SHL_out, not_5_out);
  LED led_13 (.in(BT_out));
  extender extender_1 (
    .DE(DE), .ADDR(IN_INST[3:0]), .AND(AND_2_out), .OR(OR_2_out), .FE(RS), .ExtOut(ExtBits), .NOT(NOT_6_out),
    .SUBLD(or_3_out), .CALL_TMP(extender_1_call_tmp), .CALL_FIX(CALL), .XOR(XOR_out), .ADD(ADD_out),
    .CLR(CLR), .IN(IN_out), .OUT(OUT_out), .SHR(SHR_out), .JUMP_CALL(d_ff_17_q), .STD(OUT_INST[19]),
    .SHL(SHL_out), .ExtOut2(ExtBits2));
  D_Flip_Flop #(.trigger("falling")) d_ff_9 (
    .clk(and_11_out), .D(and_13_out), .Q(OUT_INST[8]), .reset(and_18_out));  // open: Qn, preset, en
  D_Flip_Flop #(.trigger("falling")) d_ff_10 (
    .clk(and_11_out), .D(and_14_out), .Q(OUT_INST[9]), .reset(and_18_out));  // open: Qn, preset, en
  D_Flip_Flop #(.trigger("falling")) d_ff_11 (
    .clk(and_11_out), .D(and_15_out), .Q(OUT_INST[10]));  // open: Qn, preset, en, reset
  D_Flip_Flop #(.trigger("falling")) d_ff_12 (
    .clk(and_11_out), .D(and_16_out), .Q(OUT_INST[11]));  // open: Qn, preset, en, reset
  D_Flip_Flop #(.trigger("falling")) d_ff_13 (
    .clk(and_11_out), .D(BT_out), .Q(OUT_INST[12]));  // open: Qn, preset, en, reset
  D_Flip_Flop d_ff_14 (.clk(and_12_out), .D(JC_out), .Q(OUT_INST[16]), .reset(and_17_out));  // open: Qn, preset, en
  D_Flip_Flop d_ff_15 (.clk(and_12_out), .D(JZ_out), .Q(OUT_INST[17]), .reset(and_17_out));  // open: Qn, preset, en
  D_Flip_Flop d_ff_16 (.clk(and_12_out), .D(JP_out), .Q(d_ff_16_q), .reset(and_17_out));  // open: Qn, preset, en
  D_Flip_Flop d_ff_17 (
    .clk(and_12_out), .D(extender_1_call_tmp), .Q(d_ff_17_q), .reset(and_17_out));  // open: Qn, preset, en
  not not_12 (not_12_out, CLK);
  and and_17 (and_17_out, RS, not_12_out, or_5_out);
  or or_4 (OUT_INST[18], d_ff_16_q, d_ff_17_q);
  and and_18 (and_18_out, RS, or_6_out);
  or or_5 (or_5_out, d_ff_17_q, OUT_INST[16], OUT_INST[17], d_ff_16_q);
  or or_6 (or_6_out, OUT_INST[8], OUT_INST[9]);
  not not_13 (not_13_out, CLK);
  and and_19 (JUMP_LOW, EX, not_13_out, or_5_out);
  and and_20 (JUMP_HIGH, and_12_out, or_5_out);
  or or_7 (_2_byte, JP_out, JZ_out, JC_out, or_5_out, OUT_INST[19]);

  assign OUT_INST[15:13] = OUT_INST[18:16];

  // Notes on the sheet:
  //   Instruction Decoder
endmodule

// Instruction_Register
module instruction_register (
  input  EN,
  input  RS,
  input  CLK,
  input  DE,
  input  [7:0] IR_IN,
  output [7:0] IR_OUT,
  output SBITCALL
);

  D_Flip_Flop #(.trigger("high")) d_ff_1 (.clk(EN), .D(IR_IN[7]), .Q(IR_OUT[7]), .reset(RS));  // open: Qn, preset, en
  D_Flip_Flop #(.trigger("high")) d_ff_2 (.clk(EN), .D(IR_IN[6]), .Q(IR_OUT[6]), .reset(RS));  // open: Qn, preset, en
  D_Flip_Flop #(.trigger("high")) d_ff_3 (.clk(EN), .D(IR_IN[5]), .Q(IR_OUT[5]), .reset(RS));  // open: Qn, preset, en
  D_Flip_Flop #(.trigger("high")) d_ff_4 (.clk(EN), .D(IR_IN[4]), .Q(IR_OUT[4]), .reset(RS));  // open: Qn, preset, en
  D_Flip_Flop d_ff_5 (.clk(DE), .D(IR_OUT[5]), .Q(SBITCALL));  // open: Qn, preset, en, reset
  D_Flip_Flop #(.trigger("high")) d_ff_6 (.clk(EN), .D(IR_IN[3]), .Q(IR_OUT[3]), .reset(RS));  // open: Qn, preset, en
  D_Flip_Flop #(.trigger("high")) d_ff_7 (.clk(EN), .D(IR_IN[2]), .Q(IR_OUT[2]), .reset(RS));  // open: Qn, preset, en
  D_Flip_Flop #(.trigger("high")) d_ff_8 (.clk(EN), .D(IR_IN[1]), .Q(IR_OUT[1]), .reset(RS));  // open: Qn, preset, en
  D_Flip_Flop #(.trigger("high")) d_ff_9 (.clk(EN), .D(IR_IN[0]), .Q(IR_OUT[0]), .reset(RS));  // open: Qn, preset, en
endmodule

// Control
module control_circuit (
  input  VDD,
  input  ON,
  input  RESET,
  input  CLK_EXT,
  input  CLKIN_EN,
  input  OVERFLOW_EN,
  input  DEBUG_ON,
  input  STEP_INTO,
  input  I3,
  input  I2,
  input  I1,
  input  I0,
  input  [11:0] PC_IN,
  input  [11:0] INTR,
  input  PC_W,
  input  [7:0] P2,
  input  _2_byte,
  input  [25:0] ExtBits,
  input  [3:0] SR,
  input  [7:0] DR_IN,
  input  [7:0] RX_IN,
  input  [2:0] ExtBits2,
  output CLK_GEN,
  output CLK_INT,
  output [11:0] PC_OUT,
  output [3:0] SR_OUT,
  output SR_SIG,
  output [11:0] DR_OUT,
  output INTS_OUT,
  output RS,
  output INTS_CLK,
  output FE,
  output INT_STEP1,
  output DE,
  output [11:0] INTR_OUT,
  output EX,
  output WR
);

  wire and_1_out, and_2_out, and_3_out, and_4_out, and_5_out, and_6_out, and_7_out, and_8_out, and_9_out,
       and_10_out, and_11_out, assync_input_1_out_4, assync_input_1_out_5, assync_input_2_out_4,
       assync_input_2_out_5, assync_input_3_out_4, assync_input_3_out_5, assync_input_4_out_4,
       assync_input_4_out_5, assync_input_5_out_4, assync_input_5_out_5, assync_input_6_out_4,
       assync_input_6_out_5, assync_input_7_out_4, assync_input_7_out_5, assync_input_8_out_4,
       assync_input_8_out_5, assync_input_9_out_4, assync_input_9_out_5, assync_input_10_out_4,
       assync_input_10_out_5, assync_input_11_out_4, assync_input_11_out_5, assync_input_12_out_4,
       assync_input_12_out_5, clock_1_out, d_ff_1_q, delay_1_out, delay_2_out, interrupt_circuit_1_pc_lock,
       interrupt_circuit_1_pc_write, interrupt_circuit_1_sign1, interrupt_circuit_1_sign2, nand_1_out,
       not_1_out, not_2_out, not_3_out, not_4_out, not_5_out, not_6_out, or_1_out, or_2_out, or_3_out,
       or_5_out, or_6_out, or_7_out, or_8_out, or_10_out, switcher_12_1_out_14, switcher_12_1_out_15,
       switcher_12_1_out_16, switcher_12_1_out_17, switcher_12_1_out_18, switcher_12_1_out_19,
       switcher_12_1_out_20, switcher_12_1_out_21, switcher_12_1_out_22, switcher_12_1_out_23,
       switcher_12_1_out_24, switcher_12_1_out_25, t_ff_1_q, t_ff_2_q, t_ff_2_qn, t_ff_3_q, t_ff_3_qn,
       t_ff_4_qn, t_ff_5_qn, t_ff_6_q, t_ff_7_qn, t_ff_8_qn, t_ff_9_qn, t_ff_10_qn, t_ff_11_qn, t_ff_12_qn,
       t_ff_13_qn, t_ff_14_qn, t_ff_15_qn, t_ff_16_qn, t_ff_17_q;
  wire [11:0] interrupt_circuit_1_addr_out;

  Clock clock_1 (.out(clock_1_out));
  or or_1 (or_1_out, DEBUG_ON, SR[2]);
  or or_2 (or_2_out, STEP_INTO, WR);
  not not_1 (not_1_out, CLKIN_EN);
  and and_1 (and_1_out, CLK_EXT, not_1_out);
  and and_2 (and_2_out, CLKIN_EN, clock_1_out, not_2_out);
  not not_2 (not_2_out, or_1_out);
  T_Flip_Flop #(.trigger("falling")) t_ff_1 (
    .clk(or_2_out), .T(or_1_out), .Q(t_ff_1_q));  // open: Qn, preset, reset, en
  or or_3 (or_3_out, and_1_out, and_3_out, and_2_out);
  and and_3 (and_3_out, clock_1_out, or_1_out, t_ff_1_q);
  and and_4 (and_4_out, or_1_out, CLKIN_EN, clock_1_out);
  interrupt_circuit interrupt_circuit_1 (
    .CLK(clock_1_out), .FE(FE), .INTE(SR[3]), .I3(I3), .I2(I2), .I1(I1), .I0(I0), .P0_P1(INTR),
    .INTS(ExtBits[0]), .P2(P2), .PC_LOCK(interrupt_circuit_1_pc_lock),
    .PC_WRITE(interrupt_circuit_1_pc_write), .INTS_OUT(INTS_OUT), .INTS_CLK(INTS_CLK), .INT_STEP1(INT_STEP1),
    .INTR_OUT(INTR_OUT), .ADDR_OUT(interrupt_circuit_1_addr_out), .SIGN1(interrupt_circuit_1_sign1),
    .SIGN2(interrupt_circuit_1_sign2), .JUMP(_2_byte), .DI(ExtBits[1]));
  D_Flip_Flop d_ff_1 (.clk(ON), .D(1'b1), .Q(d_ff_1_q));  // open: Qn, preset, en, reset
  or or_4 (CLK_INT, and_2_out, and_4_out);
  assign CLK_GEN = d_ff_1_q ? or_3_out : 1'bz;  // Controlled_Buffer controlled_buffer_1
  not not_3 (not_3_out, clock_1_out);
  and and_5 (and_5_out, VDD, d_ff_1_q, nand_1_out, interrupt_circuit_1_pc_lock);
  nand nand_1 (nand_1_out, OVERFLOW_EN, d_ff_1_q, t_ff_17_q);
  or or_5 (or_5_out, interrupt_circuit_1_pc_lock, INT_STEP1, EX);
  and and_6 (and_6_out, INTS_OUT, INTS_CLK);
  delay delay_1 (.Delay(clock_1_out), .Clear(and_7_out), .OUT(delay_1_out));
  and and_7 (and_7_out, not_3_out, EX);
  T_Flip_Flop t_ff_2 (
    .clk(or_3_out), .T(and_5_out), .Q(t_ff_2_q), .Qn(t_ff_2_qn), .reset(RESET), .en(and_5_out));  // open: preset
  or or_6 (or_6_out, RESET, ON);
  delay delay_2 (.Delay(and_6_out), .Clear(or_5_out), .OUT(delay_2_out));
  and and_8 (and_8_out, _2_byte, EX, delay_1_out);
  T_Flip_Flop t_ff_3 (
    .clk(t_ff_2_qn), .T(and_5_out), .Q(t_ff_3_q), .Qn(t_ff_3_qn), .reset(RESET), .en(and_5_out));  // open: preset
  or or_7 (or_7_out, and_8_out, t_ff_3_qn);
  T_Flip_Flop t_ff_4 (
    .clk(or_7_out), .T(and_5_out), .Q(PC_OUT[0]), .Qn(t_ff_4_qn), .preset(assync_input_1_out_4),
    .reset(assync_input_1_out_5), .en(and_5_out));
  assync_input assync_input_1 (
    .in_1(or_8_out), .in_2(switcher_12_1_out_14), .in_3(RESET), .out_4(assync_input_1_out_4),
    .out_5(assync_input_1_out_5));
  stages_selector stages_selector_1 (.B1(t_ff_3_q), .B0(t_ff_2_q), .FE(FE), .DE(DE), .EX(EX), .WR(WR));
  T_Flip_Flop t_ff_5 (
    .clk(t_ff_4_qn), .T(and_5_out), .Q(PC_OUT[1]), .Qn(t_ff_5_qn), .preset(assync_input_2_out_4),
    .reset(assync_input_2_out_5), .en(and_5_out));
  assync_input assync_input_2 (
    .in_1(or_8_out), .in_2(switcher_12_1_out_15), .in_3(RESET), .out_4(assync_input_2_out_4),
    .out_5(assync_input_2_out_5));
  T_Flip_Flop #(.trigger("falling")) t_ff_6 (
    .clk(or_3_out), .T(d_ff_1_q), .Q(t_ff_6_q), .preset(or_6_out));  // open: Qn, reset, en
  or or_8 (or_8_out, and_9_out, or_10_out, interrupt_circuit_1_pc_write);
  T_Flip_Flop t_ff_7 (
    .clk(t_ff_5_qn), .T(and_5_out), .Q(PC_OUT[2]), .Qn(t_ff_7_qn), .preset(assync_input_3_out_4),
    .reset(assync_input_3_out_5), .en(and_5_out));
  assync_input assync_input_3 (
    .in_1(or_8_out), .in_2(switcher_12_1_out_16), .in_3(RESET), .out_4(assync_input_3_out_4),
    .out_5(assync_input_3_out_5));
  and and_9 (and_9_out, t_ff_6_q, PC_W);
  or or_9 (RS, and_8_out, FE);
  T_Flip_Flop t_ff_8 (
    .clk(t_ff_7_qn), .T(and_5_out), .Q(PC_OUT[3]), .Qn(t_ff_8_qn), .preset(assync_input_4_out_4),
    .reset(assync_input_4_out_5), .en(and_5_out));
  assync_input assync_input_4 (
    .in_1(or_8_out), .in_2(switcher_12_1_out_17), .in_3(RESET), .out_4(assync_input_4_out_4),
    .out_5(assync_input_4_out_5));
  switcher_12 switcher_12_1 (
    .in_1(and_10_out), .in_2(PC_IN[0]), .in_3(PC_IN[1]), .in_4(PC_IN[2]), .in_5(PC_IN[3]), .in_6(PC_IN[4]),
    .in_7(PC_IN[5]), .in_8(PC_IN[6]), .in_9(PC_IN[7]), .in_10(PC_IN[8]), .in_11(PC_IN[9]), .in_12(PC_IN[10]),
    .in_13(PC_IN[11]), .out_14(switcher_12_1_out_14), .out_15(switcher_12_1_out_15),
    .out_16(switcher_12_1_out_16), .out_17(switcher_12_1_out_17), .out_18(switcher_12_1_out_18),
    .out_19(switcher_12_1_out_19), .out_20(switcher_12_1_out_20), .out_21(switcher_12_1_out_21),
    .out_22(switcher_12_1_out_22), .out_23(switcher_12_1_out_23), .out_24(switcher_12_1_out_24),
    .out_25(switcher_12_1_out_25));
  and and_10 (and_10_out, not_4_out, not_5_out);
  T_Flip_Flop t_ff_9 (
    .clk(t_ff_8_qn), .T(and_5_out), .Q(PC_OUT[4]), .Qn(t_ff_9_qn), .preset(assync_input_5_out_4),
    .reset(assync_input_5_out_5), .en(and_5_out));
  assync_input assync_input_5 (
    .in_1(or_8_out), .in_2(switcher_12_1_out_18), .in_3(RESET), .out_4(assync_input_5_out_4),
    .out_5(assync_input_5_out_5));
  not not_4 (not_4_out, or_10_out);
  not not_5 (not_5_out, interrupt_circuit_1_pc_write);
  T_Flip_Flop t_ff_10 (
    .clk(t_ff_9_qn), .T(and_5_out), .Q(PC_OUT[5]), .Qn(t_ff_10_qn), .preset(assync_input_6_out_4),
    .reset(assync_input_6_out_5), .en(and_5_out));
  assync_input assync_input_6 (
    .in_1(or_8_out), .in_2(switcher_12_1_out_19), .in_3(RESET), .out_4(assync_input_6_out_4),
    .out_5(assync_input_6_out_5));
  switcher_12 switcher_12_2 (
    .in_1(interrupt_circuit_1_pc_write), .in_2(interrupt_circuit_1_addr_out[0]),
    .in_3(interrupt_circuit_1_addr_out[1]), .in_4(interrupt_circuit_1_addr_out[2]),
    .in_5(interrupt_circuit_1_addr_out[3]), .in_6(interrupt_circuit_1_addr_out[4]),
    .in_7(interrupt_circuit_1_addr_out[5]), .in_8(interrupt_circuit_1_addr_out[6]),
    .in_9(interrupt_circuit_1_addr_out[7]), .in_10(interrupt_circuit_1_addr_out[8]),
    .in_11(interrupt_circuit_1_addr_out[9]), .in_12(interrupt_circuit_1_addr_out[10]),
    .in_13(interrupt_circuit_1_addr_out[11]), .out_14(switcher_12_1_out_14), .out_15(switcher_12_1_out_15),
    .out_16(switcher_12_1_out_16), .out_17(switcher_12_1_out_17), .out_18(switcher_12_1_out_18),
    .out_19(switcher_12_1_out_19), .out_20(switcher_12_1_out_20), .out_21(switcher_12_1_out_21),
    .out_22(switcher_12_1_out_22), .out_23(switcher_12_1_out_23), .out_24(switcher_12_1_out_24),
    .out_25(switcher_12_1_out_25));
  T_Flip_Flop t_ff_11 (
    .clk(t_ff_10_qn), .T(and_5_out), .Q(PC_OUT[6]), .Qn(t_ff_11_qn), .preset(assync_input_7_out_4),
    .reset(assync_input_7_out_5), .en(and_5_out));
  assync_input assync_input_7 (
    .in_1(or_8_out), .in_2(switcher_12_1_out_20), .in_3(RESET), .out_4(assync_input_7_out_4),
    .out_5(assync_input_7_out_5));
  T_Flip_Flop t_ff_12 (
    .clk(t_ff_11_qn), .T(and_5_out), .Q(PC_OUT[7]), .Qn(t_ff_12_qn), .preset(assync_input_8_out_4),
    .reset(assync_input_8_out_5), .en(and_5_out));
  assync_input assync_input_8 (
    .in_1(or_8_out), .in_2(switcher_12_1_out_21), .in_3(RESET), .out_4(assync_input_8_out_4),
    .out_5(assync_input_8_out_5));
  switcher_12 switcher_12_3 (
    .in_1(or_10_out), .in_2(DR_OUT[0]), .in_3(DR_OUT[1]), .in_4(DR_OUT[2]), .in_5(DR_OUT[3]),
    .in_6(DR_OUT[4]), .in_7(DR_OUT[5]), .in_8(DR_OUT[6]), .in_9(DR_OUT[7]), .in_10(DR_OUT[8]),
    .in_11(DR_OUT[9]), .in_12(DR_OUT[10]), .in_13(DR_OUT[11]), .out_14(switcher_12_1_out_14),
    .out_15(switcher_12_1_out_15), .out_16(switcher_12_1_out_16), .out_17(switcher_12_1_out_17),
    .out_18(switcher_12_1_out_18), .out_19(switcher_12_1_out_19), .out_20(switcher_12_1_out_20),
    .out_21(switcher_12_1_out_21), .out_22(switcher_12_1_out_22), .out_23(switcher_12_1_out_23),
    .out_24(switcher_12_1_out_24), .out_25(switcher_12_1_out_25));
  or or_10 (or_10_out, ExtBits[15], ExtBits[18]);
  T_Flip_Flop t_ff_13 (
    .clk(t_ff_12_qn), .T(and_5_out), .Q(PC_OUT[8]), .Qn(t_ff_13_qn), .preset(assync_input_9_out_4),
    .reset(assync_input_9_out_5), .en(and_5_out));
  assync_input assync_input_9 (
    .in_1(or_8_out), .in_2(switcher_12_1_out_22), .in_3(RESET), .out_4(assync_input_9_out_4),
    .out_5(assync_input_9_out_5));
  T_Flip_Flop t_ff_14 (
    .clk(t_ff_13_qn), .T(and_5_out), .Q(PC_OUT[9]), .Qn(t_ff_14_qn), .preset(assync_input_10_out_4),
    .reset(assync_input_10_out_5), .en(and_5_out));
  assync_input assync_input_10 (
    .in_1(or_8_out), .in_2(switcher_12_1_out_23), .in_3(RESET), .out_4(assync_input_10_out_4),
    .out_5(assync_input_10_out_5));
  not not_6 (not_6_out, PC_W);
  T_Flip_Flop t_ff_15 (
    .clk(t_ff_14_qn), .T(and_5_out), .Q(PC_OUT[10]), .Qn(t_ff_15_qn), .preset(assync_input_11_out_4),
    .reset(assync_input_11_out_5));  // open: en
  assync_input assync_input_11 (
    .in_1(or_8_out), .in_2(switcher_12_1_out_24), .in_3(RESET), .out_4(assync_input_11_out_4),
    .out_5(assync_input_11_out_5));
  T_Flip_Flop t_ff_16 (
    .clk(t_ff_15_qn), .T(and_5_out), .Q(PC_OUT[11]), .Qn(t_ff_16_qn), .preset(assync_input_12_out_4),
    .reset(assync_input_12_out_5));  // open: en
  assync_input assync_input_12 (
    .in_1(or_8_out), .in_2(switcher_12_1_out_25), .in_3(RESET), .out_4(assync_input_12_out_4),
    .out_5(assync_input_12_out_5));
  T_Flip_Flop t_ff_17 (
    .clk(t_ff_16_qn), .T(and_11_out), .Q(t_ff_17_q), .reset(RESET), .en(and_5_out));  // open: Qn, preset
  and and_11 (and_11_out, and_5_out, not_6_out);
  stack_circuit stack_circuit_1 (
    .PC_IN(PC_OUT), .SR_IN(SR), .EI_CLK(delay_2_out), .ON(ON), .SYNC_1(interrupt_circuit_1_sign1),
    .SYNC_2(interrupt_circuit_1_sign2), .WRITE(INT_STEP1), .CLK(clock_1_out), .EX(EX), .WR(WR),
    .IRET(ExtBits[15]), .PUSHB(ExtBits[8]), .POPB(ExtBits[9]), .PC_OUT(DR_OUT), .SR_OUT(SR_OUT),
    .SR_W(SR_SIG), .PUSHS(ExtBits[10]), .POPS(ExtBits[11]), .SBP(ExtBits[12]), .ABP(ExtBits[13]),
    .SSP(ExtBits[14]), .DR_IN(DR_IN), .PUSHD(ExtBits[16]), .POPD(ExtBits[17]), .CALL(ExtBits[19]),
    .RET(ExtBits[18]), .PUSH(ExtBits[20]), .POP(ExtBits[21]), .RX_IN(RX_IN), .SBW(ExtBits[22]));
endmodule

// IN
module assync_input (
  input  in_1,
  input  in_2,
  input  in_3,
  output out_4,
  output out_5
);

  wire and_2_out, not_1_out;

  not not_1 (not_1_out, in_2);
  and and_1 (out_4, in_1, in_2);
  and and_2 (and_2_out, in_1, not_1_out);
  or or_1 (out_5, and_2_out, in_3);
endmodule

// pipe
module stages_selector (
  input  B1,
  input  B0,
  output FE,
  output DE,
  output EX,
  output WR
);

  wire not_1_out, not_2_out, not_3_out, not_4_out;

  not not_1 (not_1_out, B0);
  not not_2 (not_2_out, B1);
  not not_3 (not_3_out, B1);
  not not_4 (not_4_out, B0);
  and and_1 (FE, not_1_out, not_2_out);
  and and_2 (DE, not_3_out, B0);
  and and_3 (EX, not_4_out, B1);
  and and_4 (WR, B0, B1);
endmodule

// Control_Unit
module control_unit (
  input  VDD,
  input  I0,
  input  I1,
  input  I2,
  input  I3,
  input  ON,
  input  RS,
  input  CLK_EXT,
  input  CLKIN_EN,
  input  OVER_EN,
  input  PC_W,
  input  DBG,
  input  STEP,
  input  [11:0] INTR,
  input  [7:0] P2_INPUT,
  input  [11:0] PC_IN,
  input  [7:0] IR_IN,
  input  [3:0] SR_IN,
  input  [7:0] DR_IN,
  input  [7:0] RX_IN,
  output CLK_OUT,
  output FE,
  output EX,
  output WR,
  output [11:0] PC_OUT,
  output [11:0] INTR_OUT,
  output INTS_OUT,
  output INTS_CLK,
  output CLR,
  output [19:0] INST_OUT,
  output [7:0] REG_OUT,
  output JUMP_LOW,
  output JUMP_HIGH,
  output [25:0] ExtBits,
  output INT_STEP1,
  output [7:0] IR_OUT,
  output [3:0] SR_OUT,
  output SR_SIG,
  output [11:0] DR_OUT,
  output CALL,
  output SBIT,
  output [2:0] ExtBits2
);

  wire control_circuit_1_clk_gen, control_circuit_1_de, control_circuit_1_fe, instruction_decode_1__2_byte;

  control_circuit control_circuit_1 (
    .ON(ON), .RESET(RS), .CLK_EXT(CLK_EXT), .CLKIN_EN(CLKIN_EN), .OVERFLOW_EN(OVER_EN), .PC_IN(PC_IN),
    .CLK_GEN(control_circuit_1_clk_gen), .CLK_INT(CLK_OUT), .PC_OUT(PC_OUT), .RS(FE),
    .DE(control_circuit_1_de), .EX(EX), .WR(WR), .PC_W(PC_W), .DEBUG_ON(DBG), .STEP_INTO(STEP), .I0(I0),
    .I1(I1), .I2(I2), .I3(I3), .INTR(INTR), .INTR_OUT(INTR_OUT), .INTS_OUT(INTS_OUT), .INTS_CLK(INTS_CLK),
    .INT_STEP1(INT_STEP1), .P2(P2_INPUT), .SR(SR_IN), .SR_OUT(SR_OUT), .SR_SIG(SR_SIG),
    ._2_byte(instruction_decode_1__2_byte), .ExtBits(ExtBits), .DR_IN(DR_IN), .DR_OUT(DR_OUT), .RX_IN(RX_IN),
    .VDD(VDD), .FE(control_circuit_1_fe), .ExtBits2(ExtBits2));
  instruction_register instruction_register_1 (
    .EN(FE), .RS(RS), .CLK(control_circuit_1_clk_gen), .IR_IN(IR_IN), .IR_OUT(IR_OUT), .SBITCALL(SBIT),
    .DE(control_circuit_1_de));
  instruction_decode instruction_decode_1 (
    .RS(control_circuit_1_fe), .DE(control_circuit_1_de), .OUT_INST(INST_OUT), .JUMP_LOW(JUMP_LOW),
    .JUMP_HIGH(JUMP_HIGH), .OUT_ADDR(REG_OUT), .IN_INST(IR_OUT), ._2_byte(instruction_decode_1__2_byte),
    .ExtBits(ExtBits), .CALL(CALL), .CLR(CLR), .CLK(control_circuit_1_clk_gen), .EX(EX), .ExtBits2(ExtBits2));

  // Notes on the sheet:
  //   Control Unit Architecture
endmodule

// RW Control
module rw_controller (
  input  CARRY,
  input  ZERO,
  input  WRITE,
  input  EXEC,
  input  CLK_IN,
  input  [19:0] INST_IN,
  input  [7:0] PX_SIGN,
  input  [25:0] ExtBits,
  input  [2:0] ExtBits2,
  output PC_W,
  output CONTROL_W,
  output P3_W,
  output P2_W,
  output PX_W,
  output PX_R,
  output RAM_RW,
  output DATA_W,
  output DR_H,
  output DR_L,
  output SR_C,
  output SR_Z,
  output GPR_W,
  output IDC_W,
  output INC_W
);

  wire and_9_out, and_10_out, and_11_out, and_12_out, and_13_out, and_14_out, and_16_out, IN_P0_out,
       IN_P1_out, IN_P2_out, IN_P3_out, IN_P4_out, IN_P5_out, IN_P6_out, IN_P7_out, nor_1_out, nor_2_out,
       nor_3_out, nor_4_out, nor_5_out, nor_6_out, not_1_out, not_2_out, or_1_out, or_2_out, or_3_out,
       or_4_out, or_5_out, or_6_out, or_7_out, or_9_out, or_12_out, or_13_out, or_14_out, or_15_out,
       or_16_out, OUT_P0_out, OUT_P1_out, OUT_P2_out, OUT_P3_out, OUT_P4_out, OUT_P5_out, OUT_P6_out,
       OUT_P7_out;

  and and_1 (DR_H, not_1_out, DR_L);
  and and_2 (DR_L, nor_1_out, nor_2_out, and_11_out, WRITE);
  and and_3 (SR_C, nor_4_out, nor_3_out, WRITE, and_11_out);
  and and_4 (SR_Z, WRITE, nor_4_out, and_11_out);
  and and_5 (PC_W, or_1_out, WRITE);
  not not_1 (not_1_out, INST_IN[6]);
  not nor_1 (nor_1_out, or_5_out);  // NOR_Gate
  nor nor_2 (nor_2_out, INST_IN[7], INST_IN[9], INST_IN[12], or_4_out, ExtBits2[2]);
  nor nor_3 (nor_3_out, INST_IN[0], INST_IN[1], INST_IN[2], INST_IN[3], INST_IN[8]);
  nor nor_4 (nor_4_out, ExtBits[25], INST_IN[7], or_3_out, ExtBits2[2], INST_IN[9], or_4_out, INST_IN[8]);
  and and_6 (GPR_W, WRITE, or_2_out);
  and and_7 (IDC_W, WRITE, ExtBits2[2]);
  and and_8 (INC_W, WRITE, or_5_out);
  or or_1 (or_1_out, and_9_out, and_10_out, INST_IN[18]);
  or or_2 (or_2_out, INST_IN[7], or_3_out, ExtBits[21]);
  and and_9 (and_9_out, CARRY, INST_IN[16]);
  and and_10 (and_10_out, ZERO, INST_IN[17]);
  or or_3 (or_3_out, ExtBits[23], ExtBits[24]);
  and and_11 (and_11_out, nor_5_out, nor_6_out);
  or or_4 (or_4_out, INST_IN[13], INST_IN[14], INST_IN[15], INST_IN[16], INST_IN[17], INST_IN[18]);
  nor nor_5 (nor_5_out, ExtBits[0], ExtBits[1], ExtBits[2], ExtBits[3], ExtBits[4], ExtBits[5], ExtBits[6], ExtBits[7], ExtBits[8], ExtBits[9], ExtBits[10], ExtBits[11], ExtBits[14], ExtBits[15]);
  nor nor_6 (nor_6_out, ExtBits[16], ExtBits[18], ExtBits[19], ExtBits[20], ExtBits[21], ExtBits[22], ExtBits2[2]);
  or or_5 (or_5_out, ExtBits2[0], ExtBits2[1]);
  and OUT_P3 (OUT_P3_out, WRITE, PX_SIGN[3], INST_IN[9]);
  and OUT_P2 (OUT_P2_out, WRITE, PX_SIGN[2], INST_IN[9]);
  and IN_P3 (IN_P3_out, INST_IN[8], PX_SIGN[3], EXEC);
  and IN_P2 (IN_P2_out, INST_IN[8], PX_SIGN[2], EXEC);
  and IN_P0 (IN_P0_out, INST_IN[8], PX_SIGN[0], EXEC);
  and OUT_P0 (OUT_P0_out, WRITE, PX_SIGN[0], INST_IN[9]);
  and OUT_P4 (OUT_P4_out, WRITE, INST_IN[9], PX_SIGN[4]);
  or or_6 (or_6_out, OUT_P4_out, OUT_P5_out);
  and OUT_P5 (OUT_P5_out, WRITE, INST_IN[9], PX_SIGN[5]);
  and OUT_P6 (OUT_P6_out, WRITE, INST_IN[9], PX_SIGN[6]);
  or or_7 (or_7_out, OUT_P6_out, OUT_P7_out);
  and OUT_P7 (OUT_P7_out, WRITE, INST_IN[9], PX_SIGN[7]);
  not not_2 (not_2_out, CLK_IN);
  and and_12 (and_12_out, WRITE, INST_IN[9]);
  or or_8 (PX_W, OUT_P2_out, OUT_P3_out, or_9_out, or_14_out, or_7_out);
  or or_9 (or_9_out, IN_P3_out, IN_P2_out, or_16_out);
  and IN_P1 (IN_P1_out, INST_IN[8], PX_SIGN[1], EXEC);
  and OUT_P1 (OUT_P1_out, WRITE, PX_SIGN[1], INST_IN[9]);
  and and_13 (and_13_out, EXEC, not_2_out);
  or or_10 (P3_W, OUT_P3_out, OUT_P7_out);
  or or_11 (P2_W, OUT_P2_out, OUT_P6_out);
  or or_12 (or_12_out, or_9_out, OUT_P3_out, OUT_P2_out, IN_P0_out, IN_P1_out);
  or or_13 (or_13_out, IN_P2_out, OUT_P2_out);
  or or_14 (or_14_out, OUT_P1_out, OUT_P0_out, or_6_out);
  and IN_P4 (IN_P4_out, EXEC, INST_IN[8], PX_SIGN[4]);
  or or_15 (or_15_out, IN_P4_out, IN_P5_out);
  and IN_P5 (IN_P5_out, EXEC, INST_IN[8], PX_SIGN[5]);
  and IN_P6 (IN_P6_out, INST_IN[8], EXEC, PX_SIGN[6]);
  or or_16 (or_16_out, IN_P6_out, IN_P7_out);
  and IN_P7 (IN_P7_out, INST_IN[8], EXEC, PX_SIGN[7]);
  and and_14 (and_14_out, and_13_out, INST_IN[8]);
  and and_15 (RAM_RW, not_2_out, or_13_out);
  and and_16 (and_16_out, INST_IN[8], WRITE);
  or or_17 (CONTROL_W, and_16_out, and_14_out, and_12_out);
  or or_18 (PX_R, OUT_P7_out, OUT_P6_out, or_12_out, or_15_out);
  or or_19 (DATA_W, P3_W, P2_W, or_14_out);
endmodule

// Registers Bank
module register_bank (
  input  DR_H,
  input  DR_L,
  input  RS,
  input  SR_C,
  input  SR_Z,
  input  GPR_R,
  input  GPR_W,
  input  [25:0] ExtBits,
  input  [11:0] REG_DATA,
  input  [3:0] SR_DATA,
  input  [3:0] SR_IN,
  input  SR_W,
  input  CONTROL_W,
  input  PX_W,
  input  PX_R,
  input  RAM_RW,
  input  P2_W,
  input  [11:0] DR_IN,
  input  P3_W,
  input  OUT_INT,
  input  PS_C,
  input  INT_STEP1,
  input  [11:0] INT_PXIN,
  input  [7:0] EXT_PXIN,
  input  [7:0] ASSYNC_RX_IN,
  input  IDC_W,
  input  [2:0] ExtBits2,
  input  [11:0] INTR_IN,
  input  INTS_IN,
  input  INTS_CLK,
  input  [7:0] RX_SIGN,
  input  [7:0] IR_IN,
  input  INC_W,
  input  CLOCK,
  output [7:0] DR_OUT,
  output [7:0] RX_OUT,
  output CARRY,
  output ZERO,
  output [3:0] SR_OUT,
  output [7:0] P0_OUT,
  output [7:0] P1_OUT,
  output [7:0] P4_OUT,
  output [7:0] P5_OUT,
  output [7:0] PX_OUT,
  output [1:0] IDC_SEL
);

  wire and_1_out, and_2_out, and_3_out, and_4_out, and_5_out, and_6_out, and_7_out, and_8_out, and_9_out,
       and_10_out, and_11_out, controlled_buffer_13_out, controlled_buffer_14_out, demultiplexer_1_out0,
       demultiplexer_1_out1, demultiplexer_1_out2, nor_1_out, nor_2_out, not_1_out, not_2_out, not_3_out,
       not_4_out, not_5_out, not_6_out, not_7_out, not_8_out, not_9_out, not_10_out, or_1_out, or_2_out,
       or_3_out, or_4_out, or_5_out, or_6_out, or_7_out, or_8_out, or_9_out, or_10_out, or_11_out, or_12_out,
       or_13_out, or_14_out, or_15_out, or_16_out, or_17_out, or_18_out, or_19_out, or_20_out, or_21_out,
       or_22_out, or_23_out, or_24_out, or_25_out, or_26_out, or_27_out;
  wire [2:0] bit_extender_3_out, controlled_buffer_9_out, multiplexer_2_out;
  wire [3:0] multiplexer_1_out;
  wire [5:0] IDC_Register_q;
  wire [7:0] bit_extender_2_out, controlled_buffer_1_out, controlled_buffer_3_out, demultiplexer_2_out0;
  wire [11:0] bit_extender_1_out, controlled_buffer_5_out, controlled_buffer_7_out, controlled_buffer_11_out;

  and and_1 (and_1_out, DR_H, or_2_out);
  assign controlled_buffer_1_out = not_1_out ? controlled_buffer_3_out : 8'bz;  // Controlled_Buffer controlled_buffer_1
  not not_1 (not_1_out, and_1_out);
  assign controlled_buffer_1_out = and_1_out ? 8'h1 : 8'bz;  // Controlled_Buffer controlled_buffer_2
  assign controlled_buffer_3_out = not_2_out ? RX_SIGN : 8'bz;  // Controlled_Buffer controlled_buffer_3
  not not_2 (not_2_out, or_3_out);
  assign controlled_buffer_3_out = or_3_out ? demultiplexer_2_out0 : 8'bz;  // Controlled_Buffer controlled_buffer_4
  or or_1 (or_1_out, ExtBits[21], ExtBits[13], ExtBits[17], ExtBits[12]);
  assign controlled_buffer_5_out = not_3_out ? REG_DATA : 12'bz;  // Controlled_Buffer controlled_buffer_5
  not not_3 (not_3_out, or_1_out);
  assign controlled_buffer_5_out = or_1_out ? DR_IN : 12'bz;  // Controlled_Buffer controlled_buffer_6
  or or_2 (or_2_out, ExtBits[23], or_15_out, ExtBits[24]);
  assign bit_extender_1_out = {{4{1'b0}}, ASSYNC_RX_IN};  // Bit_Extender bit_extender_1
  or or_3 (or_3_out, ExtBits2[0], ExtBits2[1]);
  not not_4 (not_4_out, CLOCK);
  or or_4 (or_4_out, DR_H, and_10_out);
  or or_5 (or_5_out, and_10_out, DR_L);
  or or_6 (or_6_out, RS, ExtBits[7], ExtBits[6]);
  or or_7 (or_7_out, RS, ExtBits[7]);
  or or_8 (or_8_out, and_6_out, GPR_W);
  assign controlled_buffer_7_out = not_5_out ? controlled_buffer_5_out : 12'bz;  // Controlled_Buffer controlled_buffer_7
  not not_5 (not_5_out, or_2_out);
  assign controlled_buffer_7_out = or_2_out ? bit_extender_1_out : 12'bz;  // Controlled_Buffer controlled_buffer_8
  Register #(.trigger("falling")) IDC_Register (
    .D(bit_extender_2_out), .Q({IDC_SEL, IDC_Register_q}), .clk(and_2_out));  // open: en, clr
  and and_2 (and_2_out, IDC_W, ExtBits2[2]);
  and and_3 (and_3_out, INC_W, not_4_out);
  or or_9 (or_9_out, and_3_out, and_4_out);
  and and_4 (and_4_out, INC_W, CLOCK);
  nor nor_1 (nor_1_out, CLOCK, INC_W);
  or or_10 (or_10_out, nor_1_out, or_15_out);
  user_register user_register_1 (
    .R(GPR_R), .W(or_8_out), .B7(controlled_buffer_7_out[7]), .B6(controlled_buffer_7_out[6]),
    .B5(controlled_buffer_7_out[5]), .B4(controlled_buffer_7_out[4]), .B3(controlled_buffer_7_out[3]),
    .B2(controlled_buffer_7_out[2]), .B1(controlled_buffer_7_out[1]), .B0(controlled_buffer_7_out[0]),
    .RS(or_7_out), .R0(controlled_buffer_1_out[0]), .R1(controlled_buffer_1_out[1]),
    .R2(controlled_buffer_1_out[2]), .R3(controlled_buffer_1_out[3]), .R4(controlled_buffer_1_out[4]),
    .R5(controlled_buffer_1_out[5]), .R6(controlled_buffer_1_out[6]), .R7(controlled_buffer_1_out[7]),
    .O0(RX_OUT[0]), .O1(RX_OUT[1]), .O2(RX_OUT[2]), .O3(RX_OUT[3]), .O4(RX_OUT[4]), .O5(RX_OUT[5]),
    .O6(RX_OUT[6]), .O7(RX_OUT[7]));
  Bit_Extender #(.in_width(12), .out_width(8)) bit_extender_2 (.in(controlled_buffer_7_out), .out(bit_extender_2_out));
  Demultiplexer #(.select(2)) demultiplexer_1 (
    .out0(demultiplexer_1_out0), .out1(demultiplexer_1_out1), .out2(demultiplexer_1_out2), .in(or_3_out),
    .sel(IDC_SEL));  // open: out3, en
  D_Flip_Flop #(.trigger("falling")) d_ff_1 (
    .clk(or_4_out), .D(controlled_buffer_5_out[7]), .Q(DR_OUT[7]), .reset(or_6_out));  // open: Qn, preset, en
  Multiplexer #(.width(4)) multiplexer_1 (
    .in0(SR_IN), .in1(SR_DATA), .out(multiplexer_1_out), .sel(not_6_out));  // open: en
  not not_6 (not_6_out, ExtBits[15]);
  Demultiplexer #(.select(3)) demultiplexer_2 (
    .out0(demultiplexer_2_out0[0]), .out1(demultiplexer_2_out0[1]), .out2(demultiplexer_2_out0[2]),
    .out3(demultiplexer_2_out0[3]), .out4(demultiplexer_2_out0[4]), .out5(demultiplexer_2_out0[5]),
    .out6(demultiplexer_2_out0[6]), .out7(demultiplexer_2_out0[7]), .in(or_3_out), .sel(multiplexer_2_out));  // open: en
  Multiplexer #(.width(3)) multiplexer_2 (
    .in0(IDC_Register_q[2:0]), .in1(IDC_Register_q[5:3]), .out(multiplexer_2_out), .sel(or_10_out));  // open: en
  Bit_Extender #(.out_width(3)) bit_extender_3 (.in(IR_IN), .out(bit_extender_3_out));
  not not_7 (not_7_out, or_25_out);
  D_Flip_Flop #(.trigger("falling")) d_ff_2 (
    .clk(or_4_out), .D(controlled_buffer_5_out[6]), .Q(DR_OUT[6]), .reset(or_6_out));  // open: Qn, preset, en
  D_Flip_Flop #(.trigger("falling")) d_ff_3 (
    .clk(or_4_out), .D(controlled_buffer_5_out[5]), .Q(DR_OUT[5]), .reset(or_6_out));  // open: Qn, preset, en
  and and_5 (and_5_out, SR_C, ExtBits[0]);
  or or_11 (or_11_out, RAM_RW, INT_STEP1);
  or or_12 (or_12_out, PX_R, demultiplexer_1_out0, INT_STEP1);
  or or_13 (or_13_out, PX_W, and_7_out, INT_STEP1);
  or or_14 (or_14_out, CONTROL_W, INT_STEP1);
  and and_6 (and_6_out, demultiplexer_1_out1, or_9_out);
  and and_7 (and_7_out, demultiplexer_1_out0, or_9_out);
  assign controlled_buffer_9_out = not_8_out ? bit_extender_3_out : 3'bz;  // Controlled_Buffer controlled_buffer_9
  not not_8 (not_8_out, or_3_out);
  assign controlled_buffer_9_out = or_3_out ? multiplexer_2_out : 3'bz;  // Controlled_Buffer controlled_buffer_10
  and and_8 (and_8_out, or_25_out, and_3_out, ExtBits2[0]);
  or or_15 (or_15_out, and_8_out, and_9_out);
  and and_9 (and_9_out, not_7_out, and_3_out, ExtBits2[1]);
  D_Flip_Flop #(.trigger("falling")) d_ff_4 (
    .clk(or_4_out), .D(controlled_buffer_5_out[4]), .Q(DR_OUT[4]), .reset(or_6_out));  // open: Qn, preset, en
  or or_16 (or_16_out, SR_C, SR_W);
  D_Flip_Flop #(.trigger("falling")) d_ff_5 (
    .clk(or_17_out), .D(or_19_out), .Q(SR_OUT[3]), .reset(or_18_out));  // open: Qn, preset, en
  or or_17 (or_17_out, and_5_out, SR_W);
  and and_10 (and_10_out, or_9_out, demultiplexer_1_out2);
  D_Flip_Flop #(.trigger("falling")) d_ff_6 (
    .clk(or_5_out), .D(controlled_buffer_5_out[3]), .Q(DR_OUT[3]), .reset(or_6_out));  // open: Qn, preset, en
  nor nor_2 (nor_2_out, ExtBits[18], ExtBits[15]);
  or or_18 (or_18_out, or_7_out, ExtBits[1]);
  or or_19 (or_19_out, ExtBits[0], multiplexer_1_out[3]);
  or or_20 (or_20_out, multiplexer_1_out[2], ExtBits[2]);
  D_Flip_Flop #(.trigger("falling")) d_ff_7 (
    .clk(or_5_out), .D(controlled_buffer_5_out[2]), .Q(DR_OUT[2]), .reset(or_6_out));  // open: Qn, preset, en
  or or_21 (or_21_out, SR_W, SR_Z);
  and and_11 (and_11_out, or_16_out, nor_2_out);
  D_Flip_Flop d_ff_8 (.Q(SR_OUT[2]), .preset(or_20_out), .reset(or_22_out));  // open: clk, D, Qn, en
  or or_22 (or_22_out, or_7_out, ExtBits[3]);
  not not_9 (not_9_out, INTS_IN);
  or or_23 (or_23_out, or_13_out, INTS_IN);
  or or_24 (or_24_out, OUT_INT, and_7_out);
  assign controlled_buffer_11_out = not_10_out ? INT_PXIN : 12'bz;  // Controlled_Buffer controlled_buffer_11
  not not_10 (not_10_out, or_15_out);
  assign controlled_buffer_11_out = or_15_out ? bit_extender_1_out : 12'bz;  // Controlled_Buffer controlled_buffer_12
  D_Flip_Flop #(.trigger("falling")) d_ff_9 (
    .clk(or_5_out), .D(controlled_buffer_5_out[1]), .Q(DR_OUT[1]), .reset(or_6_out));  // open: Qn, preset, en
  D_Flip_Flop #(.trigger("falling")) d_ff_10 (
    .clk(or_21_out), .D(multiplexer_1_out[1]), .Q(SR_OUT[1]), .reset(or_7_out));  // open: Qn, preset, en
  or or_25 (or_25_out, multiplexer_1_out[0], ExtBits[4]);
  or or_26 (or_26_out, or_7_out, ExtBits[5]);
  assign controlled_buffer_13_out = not_9_out ? controlled_buffer_9_out[1] : 1'bz;  // Controlled_Buffer controlled_buffer_13
  assign controlled_buffer_14_out = not_9_out ? controlled_buffer_9_out[0] : 1'bz;  // Controlled_Buffer controlled_buffer_14
  assign controlled_buffer_13_out = INTS_IN ? 1'b0 : 1'bz;  // Controlled_Buffer controlled_buffer_15
  assign controlled_buffer_14_out = INTS_IN ? INTS_CLK : 1'bz;  // Controlled_Buffer controlled_buffer_16
  switcher_12 switcher_12_1 (
    .in_1(or_24_out), .in_2(controlled_buffer_11_out[0]), .in_3(controlled_buffer_11_out[1]),
    .in_4(controlled_buffer_11_out[2]), .in_5(controlled_buffer_11_out[3]),
    .in_6(controlled_buffer_11_out[4]), .in_7(controlled_buffer_11_out[5]),
    .in_8(controlled_buffer_11_out[6]), .in_9(controlled_buffer_11_out[7]), .out_14(EXT_PXIN[0]),
    .out_15(EXT_PXIN[1]), .out_16(EXT_PXIN[2]), .out_17(EXT_PXIN[3]), .out_18(EXT_PXIN[4]),
    .out_19(EXT_PXIN[5]), .out_20(EXT_PXIN[6]), .out_21(EXT_PXIN[7]));  // open: in_10, in_11, in_12, in_13, out_22, out_23, out_24, out_25
  mux_switcher mux_switcher_1 (
    .ON(INTS_IN), .ADDR(INTS_CLK), .DATA1(INTR_IN[11:8]), .DATA2(INTR_IN[7:0]), .b7(EXT_PXIN[7]),
    .b6(EXT_PXIN[6]), .b5(EXT_PXIN[5]), .b4(EXT_PXIN[4]), .b3(EXT_PXIN[3]), .b2(EXT_PXIN[2]),
    .b1(EXT_PXIN[1]), .b0(EXT_PXIN[0]));
  D_Flip_Flop #(.trigger("falling")) d_ff_11 (
    .clk(or_5_out), .D(controlled_buffer_5_out[0]), .Q(DR_OUT[0]), .reset(or_6_out));  // open: Qn, preset, en
  D_Flip_Flop #(.trigger("falling")) d_ff_12 (
    .clk(and_11_out), .D(or_25_out), .Q(CARRY), .reset(or_26_out));  // open: Qn, preset, en
  or or_27 (or_27_out, INT_STEP1, controlled_buffer_13_out);
  port_registers port_registers_1 (
    .P0_7(P3_W), .P0_6(P2_W), .P0_5(or_11_out), .RS(or_7_out), .R(or_12_out), .W(or_23_out),
    .P0_S(or_14_out), .A1(or_27_out), .A0(controlled_buffer_14_out), .B7(EXT_PXIN[7]), .B6(EXT_PXIN[6]),
    .B5(EXT_PXIN[5]), .B4(EXT_PXIN[4]), .B3(EXT_PXIN[3]), .B2(EXT_PXIN[2]), .B1(EXT_PXIN[1]),
    .B0(EXT_PXIN[0]), .P0(P0_OUT), .P1(P1_OUT), .out_24(PX_OUT[7]), .out_25(PX_OUT[6]), .out_26(PX_OUT[5]),
    .out_27(PX_OUT[4]), .out_28(PX_OUT[3]), .out_29(PX_OUT[2]), .out_30(PX_OUT[1]), .out_31(PX_OUT[0]),
    .PS_C(PS_C), .A2(controlled_buffer_9_out[2]), .P4(P4_OUT), .P5(P5_OUT));

  assign SR_OUT[0] = CARRY;
  assign ZERO = SR_OUT[1];
endmodule

module user_register (
  input  R,
  input  W,
  input  B7,
  input  B6,
  input  B5,
  input  B4,
  input  B3,
  input  B2,
  input  B1,
  input  B0,
  input  RS,
  input  R0,
  input  R1,
  input  R2,
  input  R3,
  input  R4,
  input  R5,
  input  R6,
  input  R7,
  output O0,
  output O1,
  output O2,
  output O3,
  output O4,
  output O5,
  output O6,
  output O7
);

  wire and_1_out, and_2_out, and_3_out, and_4_out, and_5_out, and_6_out, and_7_out, and_8_out, and_9_out,
       and_10_out, and_11_out, and_12_out, and_13_out, and_14_out, and_15_out, and_16_out, d_ff_1_q,
       d_ff_2_q, d_ff_3_q, d_ff_4_q, d_ff_5_q, d_ff_6_q, d_ff_7_q, d_ff_8_q, d_ff_9_q, d_ff_10_q, d_ff_11_q,
       d_ff_12_q, d_ff_13_q, d_ff_14_q, d_ff_15_q, d_ff_16_q, d_ff_17_q, d_ff_18_q, d_ff_19_q, d_ff_20_q,
       d_ff_21_q, d_ff_22_q, d_ff_23_q, d_ff_24_q, d_ff_25_q, d_ff_26_q, d_ff_27_q, d_ff_28_q, d_ff_29_q,
       d_ff_30_q, d_ff_31_q, d_ff_32_q, d_ff_33_q, d_ff_34_q, d_ff_35_q, d_ff_36_q, d_ff_37_q, d_ff_38_q,
       d_ff_39_q, d_ff_40_q, d_ff_41_q, d_ff_42_q, d_ff_43_q, d_ff_44_q, d_ff_45_q, d_ff_46_q, d_ff_47_q,
       d_ff_48_q, d_ff_49_q, d_ff_50_q, d_ff_51_q, d_ff_52_q, d_ff_53_q, d_ff_54_q, d_ff_55_q, d_ff_56_q,
       d_ff_57_q, d_ff_58_q, d_ff_59_q, d_ff_60_q, d_ff_61_q, d_ff_62_q, d_ff_63_q, d_ff_64_q;

  and and_1 (and_1_out, W, R0);
  and and_2 (and_2_out, W, R1);
  and and_3 (and_3_out, W, R2);
  and and_4 (and_4_out, W, R3);
  and and_5 (and_5_out, W, R4);
  and and_6 (and_6_out, W, R5);
  and and_7 (and_7_out, W, R6);
  and and_8 (and_8_out, W, R7);
  D_Flip_Flop d_ff_1 (.clk(and_1_out), .D(B7), .Q(d_ff_1_q), .reset(RS));  // open: Qn, preset, en
  D_Flip_Flop d_ff_2 (.clk(and_2_out), .D(B7), .Q(d_ff_2_q), .reset(RS));  // open: Qn, preset, en
  D_Flip_Flop #(.trigger("falling")) d_ff_3 (
    .clk(and_3_out), .D(B7), .Q(d_ff_3_q), .reset(RS));  // open: Qn, preset, en
  D_Flip_Flop #(.trigger("falling")) d_ff_4 (
    .clk(and_4_out), .D(B7), .Q(d_ff_4_q), .reset(RS));  // open: Qn, preset, en
  D_Flip_Flop #(.trigger("falling")) d_ff_5 (
    .clk(and_5_out), .D(B7), .Q(d_ff_5_q), .reset(RS));  // open: Qn, preset, en
  D_Flip_Flop #(.trigger("falling")) d_ff_6 (
    .clk(and_6_out), .D(B7), .Q(d_ff_6_q), .reset(RS));  // open: Qn, preset, en
  D_Flip_Flop #(.trigger("falling")) d_ff_7 (
    .clk(and_7_out), .D(B7), .Q(d_ff_7_q), .reset(RS));  // open: Qn, preset, en
  D_Flip_Flop #(.trigger("falling")) d_ff_8 (
    .clk(and_8_out), .D(B7), .Q(d_ff_8_q), .reset(RS));  // open: Qn, preset, en
  D_Flip_Flop d_ff_9 (.clk(and_1_out), .D(B6), .Q(d_ff_9_q), .reset(RS));  // open: Qn, preset, en
  D_Flip_Flop d_ff_10 (.clk(and_2_out), .D(B6), .Q(d_ff_10_q), .reset(RS));  // open: Qn, preset, en
  D_Flip_Flop #(.trigger("falling")) d_ff_11 (
    .clk(and_3_out), .D(B6), .Q(d_ff_11_q), .reset(RS));  // open: Qn, preset, en
  D_Flip_Flop #(.trigger("falling")) d_ff_12 (
    .clk(and_4_out), .D(B6), .Q(d_ff_12_q), .reset(RS));  // open: Qn, preset, en
  D_Flip_Flop #(.trigger("falling")) d_ff_13 (
    .clk(and_5_out), .D(B6), .Q(d_ff_13_q), .reset(RS));  // open: Qn, preset, en
  D_Flip_Flop #(.trigger("falling")) d_ff_14 (
    .clk(and_6_out), .D(B6), .Q(d_ff_14_q), .reset(RS));  // open: Qn, preset, en
  D_Flip_Flop #(.trigger("falling")) d_ff_15 (
    .clk(and_7_out), .D(B6), .Q(d_ff_15_q), .reset(RS));  // open: Qn, preset, en
  D_Flip_Flop #(.trigger("falling")) d_ff_16 (
    .clk(and_8_out), .D(B6), .Q(d_ff_16_q), .reset(RS));  // open: Qn, preset, en
  D_Flip_Flop d_ff_17 (.clk(and_1_out), .D(B5), .Q(d_ff_17_q), .reset(RS));  // open: Qn, preset, en
  D_Flip_Flop d_ff_18 (.clk(and_2_out), .D(B5), .Q(d_ff_18_q), .reset(RS));  // open: Qn, preset, en
  D_Flip_Flop #(.trigger("falling")) d_ff_19 (
    .clk(and_3_out), .D(B5), .Q(d_ff_19_q), .reset(RS));  // open: Qn, preset, en
  D_Flip_Flop #(.trigger("falling")) d_ff_20 (
    .clk(and_4_out), .D(B5), .Q(d_ff_20_q), .reset(RS));  // open: Qn, preset, en
  D_Flip_Flop #(.trigger("falling")) d_ff_21 (
    .clk(and_5_out), .D(B5), .Q(d_ff_21_q), .reset(RS));  // open: Qn, preset, en
  D_Flip_Flop #(.trigger("falling")) d_ff_22 (
    .clk(and_6_out), .D(B5), .Q(d_ff_22_q), .reset(RS));  // open: Qn, preset, en
  D_Flip_Flop #(.trigger("falling")) d_ff_23 (
    .clk(and_7_out), .D(B5), .Q(d_ff_23_q), .reset(RS));  // open: Qn, preset, en
  D_Flip_Flop #(.trigger("falling")) d_ff_24 (
    .clk(and_8_out), .D(B5), .Q(d_ff_24_q), .reset(RS));  // open: Qn, preset, en
  D_Flip_Flop d_ff_25 (.clk(and_1_out), .D(B4), .Q(d_ff_25_q), .reset(RS));  // open: Qn, preset, en
  D_Flip_Flop d_ff_26 (.clk(and_2_out), .D(B4), .Q(d_ff_26_q), .reset(RS));  // open: Qn, preset, en
  D_Flip_Flop #(.trigger("falling")) d_ff_27 (
    .clk(and_3_out), .D(B4), .Q(d_ff_27_q), .reset(RS));  // open: Qn, preset, en
  D_Flip_Flop #(.trigger("falling")) d_ff_28 (
    .clk(and_4_out), .D(B4), .Q(d_ff_28_q), .reset(RS));  // open: Qn, preset, en
  D_Flip_Flop #(.trigger("falling")) d_ff_29 (
    .clk(and_5_out), .D(B4), .Q(d_ff_29_q), .reset(RS));  // open: Qn, preset, en
  D_Flip_Flop #(.trigger("falling")) d_ff_30 (
    .clk(and_6_out), .D(B4), .Q(d_ff_30_q), .reset(RS));  // open: Qn, preset, en
  D_Flip_Flop #(.trigger("falling")) d_ff_31 (
    .clk(and_7_out), .D(B4), .Q(d_ff_31_q), .reset(RS));  // open: Qn, preset, en
  D_Flip_Flop #(.trigger("falling")) d_ff_32 (
    .clk(and_8_out), .D(B4), .Q(d_ff_32_q), .reset(RS));  // open: Qn, preset, en
  D_Flip_Flop d_ff_33 (.clk(and_1_out), .D(B3), .Q(d_ff_33_q), .reset(RS));  // open: Qn, preset, en
  D_Flip_Flop d_ff_34 (.clk(and_2_out), .D(B3), .Q(d_ff_34_q), .reset(RS));  // open: Qn, preset, en
  D_Flip_Flop #(.trigger("falling")) d_ff_35 (
    .clk(and_3_out), .D(B3), .Q(d_ff_35_q), .reset(RS));  // open: Qn, preset, en
  D_Flip_Flop #(.trigger("falling")) d_ff_36 (
    .clk(and_4_out), .D(B3), .Q(d_ff_36_q), .reset(RS));  // open: Qn, preset, en
  D_Flip_Flop #(.trigger("falling")) d_ff_37 (
    .clk(and_5_out), .D(B3), .Q(d_ff_37_q), .reset(RS));  // open: Qn, preset, en
  D_Flip_Flop #(.trigger("falling")) d_ff_38 (
    .clk(and_6_out), .D(B3), .Q(d_ff_38_q), .reset(RS));  // open: Qn, preset, en
  D_Flip_Flop #(.trigger("falling")) d_ff_39 (
    .clk(and_7_out), .D(B3), .Q(d_ff_39_q), .reset(RS));  // open: Qn, preset, en
  D_Flip_Flop #(.trigger("falling")) d_ff_40 (
    .clk(and_8_out), .D(B3), .Q(d_ff_40_q), .reset(RS));  // open: Qn, preset, en
  D_Flip_Flop d_ff_41 (.clk(and_1_out), .D(B2), .Q(d_ff_41_q), .reset(RS));  // open: Qn, preset, en
  D_Flip_Flop d_ff_42 (.clk(and_2_out), .D(B2), .Q(d_ff_42_q), .reset(RS));  // open: Qn, preset, en
  D_Flip_Flop #(.trigger("falling")) d_ff_43 (
    .clk(and_3_out), .D(B2), .Q(d_ff_43_q), .reset(RS));  // open: Qn, preset, en
  D_Flip_Flop #(.trigger("falling")) d_ff_44 (
    .clk(and_4_out), .D(B2), .Q(d_ff_44_q), .reset(RS));  // open: Qn, preset, en
  D_Flip_Flop #(.trigger("falling")) d_ff_45 (
    .clk(and_5_out), .D(B2), .Q(d_ff_45_q), .reset(RS));  // open: Qn, preset, en
  D_Flip_Flop #(.trigger("falling")) d_ff_46 (
    .clk(and_6_out), .D(B2), .Q(d_ff_46_q), .reset(RS));  // open: Qn, preset, en
  D_Flip_Flop #(.trigger("falling")) d_ff_47 (
    .clk(and_7_out), .D(B2), .Q(d_ff_47_q), .reset(RS));  // open: Qn, preset, en
  D_Flip_Flop #(.trigger("falling")) d_ff_48 (
    .clk(and_8_out), .D(B2), .Q(d_ff_48_q), .reset(RS));  // open: Qn, preset, en
  D_Flip_Flop d_ff_49 (.clk(and_1_out), .D(B1), .Q(d_ff_49_q), .reset(RS));  // open: Qn, preset, en
  D_Flip_Flop d_ff_50 (.clk(and_2_out), .D(B1), .Q(d_ff_50_q), .reset(RS));  // open: Qn, preset, en
  D_Flip_Flop #(.trigger("falling")) d_ff_51 (
    .clk(and_3_out), .D(B1), .Q(d_ff_51_q), .reset(RS));  // open: Qn, preset, en
  D_Flip_Flop #(.trigger("falling")) d_ff_52 (
    .clk(and_4_out), .D(B1), .Q(d_ff_52_q), .reset(RS));  // open: Qn, preset, en
  D_Flip_Flop #(.trigger("falling")) d_ff_53 (
    .clk(and_5_out), .D(B1), .Q(d_ff_53_q), .reset(RS));  // open: Qn, preset, en
  D_Flip_Flop #(.trigger("falling")) d_ff_54 (
    .clk(and_6_out), .D(B1), .Q(d_ff_54_q), .reset(RS));  // open: Qn, preset, en
  D_Flip_Flop #(.trigger("falling")) d_ff_55 (
    .clk(and_7_out), .D(B1), .Q(d_ff_55_q), .reset(RS));  // open: Qn, preset, en
  D_Flip_Flop #(.trigger("falling")) d_ff_56 (
    .clk(and_8_out), .D(B1), .Q(d_ff_56_q), .reset(RS));  // open: Qn, preset, en
  D_Flip_Flop d_ff_57 (.clk(and_1_out), .D(B0), .Q(d_ff_57_q), .reset(RS));  // open: Qn, preset, en
  D_Flip_Flop d_ff_58 (.clk(and_2_out), .D(B0), .Q(d_ff_58_q), .reset(RS));  // open: Qn, preset, en
  D_Flip_Flop #(.trigger("falling")) d_ff_59 (
    .clk(and_3_out), .D(B0), .Q(d_ff_59_q), .reset(RS));  // open: Qn, preset, en
  D_Flip_Flop #(.trigger("falling")) d_ff_60 (
    .clk(and_4_out), .D(B0), .Q(d_ff_60_q), .reset(RS));  // open: Qn, preset, en
  D_Flip_Flop #(.trigger("falling")) d_ff_61 (
    .clk(and_5_out), .D(B0), .Q(d_ff_61_q), .reset(RS));  // open: Qn, preset, en
  D_Flip_Flop #(.trigger("falling")) d_ff_62 (
    .clk(and_6_out), .D(B0), .Q(d_ff_62_q), .reset(RS));  // open: Qn, preset, en
  D_Flip_Flop #(.trigger("falling")) d_ff_63 (
    .clk(and_7_out), .D(B0), .Q(d_ff_63_q), .reset(RS));  // open: Qn, preset, en
  D_Flip_Flop #(.trigger("falling")) d_ff_64 (
    .clk(and_8_out), .D(B0), .Q(d_ff_64_q), .reset(RS));  // open: Qn, preset, en
  and and_9 (and_9_out, R, R0);
  and and_10 (and_10_out, R, R1);
  and and_11 (and_11_out, R, R2);
  and and_12 (and_12_out, R, R3);
  and and_13 (and_13_out, R, R4);
  and and_14 (and_14_out, R, R5);
  and and_15 (and_15_out, R, R6);
  and and_16 (and_16_out, R, R7);
  switcher switcher_1 (
    .EN(and_9_out), .in_2(d_ff_57_q), .in_3(d_ff_49_q), .in_4(d_ff_41_q), .in_5(d_ff_33_q), .in_6(d_ff_25_q),
    .in_7(d_ff_17_q), .in_8(d_ff_9_q), .in_9(d_ff_1_q), .out_10(O0), .out_11(O1), .out_12(O2), .out_13(O3),
    .out_14(O4), .out_15(O5), .out_16(O6), .out_17(O7));
  switcher switcher_2 (
    .EN(and_10_out), .in_2(d_ff_58_q), .in_3(d_ff_50_q), .in_4(d_ff_42_q), .in_5(d_ff_34_q),
    .in_6(d_ff_26_q), .in_7(d_ff_18_q), .in_8(d_ff_10_q), .in_9(d_ff_2_q), .out_10(O0), .out_11(O1),
    .out_12(O2), .out_13(O3), .out_14(O4), .out_15(O5), .out_16(O6), .out_17(O7));
  switcher switcher_3 (
    .EN(and_11_out), .in_2(d_ff_59_q), .in_3(d_ff_51_q), .in_4(d_ff_43_q), .in_5(d_ff_35_q),
    .in_6(d_ff_27_q), .in_7(d_ff_19_q), .in_8(d_ff_11_q), .in_9(d_ff_3_q), .out_10(O0), .out_11(O1),
    .out_12(O2), .out_13(O3), .out_14(O4), .out_15(O5), .out_16(O6), .out_17(O7));
  switcher switcher_4 (
    .EN(and_12_out), .in_2(d_ff_60_q), .in_3(d_ff_52_q), .in_4(d_ff_44_q), .in_5(d_ff_36_q),
    .in_6(d_ff_28_q), .in_7(d_ff_20_q), .in_8(d_ff_12_q), .in_9(d_ff_4_q), .out_10(O0), .out_11(O1),
    .out_12(O2), .out_13(O3), .out_14(O4), .out_15(O5), .out_16(O6), .out_17(O7));
  switcher switcher_5 (
    .EN(and_13_out), .in_2(d_ff_61_q), .in_3(d_ff_53_q), .in_4(d_ff_45_q), .in_5(d_ff_37_q),
    .in_6(d_ff_29_q), .in_7(d_ff_21_q), .in_8(d_ff_13_q), .in_9(d_ff_5_q), .out_10(O0), .out_11(O1),
    .out_12(O2), .out_13(O3), .out_14(O4), .out_15(O5), .out_16(O6), .out_17(O7));
  switcher switcher_6 (
    .EN(and_14_out), .in_2(d_ff_62_q), .in_3(d_ff_54_q), .in_4(d_ff_46_q), .in_5(d_ff_38_q),
    .in_6(d_ff_30_q), .in_7(d_ff_22_q), .in_8(d_ff_14_q), .in_9(d_ff_6_q), .out_10(O0), .out_11(O1),
    .out_12(O2), .out_13(O3), .out_14(O4), .out_15(O5), .out_16(O6), .out_17(O7));
  switcher switcher_7 (
    .EN(and_15_out), .in_2(d_ff_63_q), .in_3(d_ff_55_q), .in_4(d_ff_47_q), .in_5(d_ff_39_q),
    .in_6(d_ff_31_q), .in_7(d_ff_23_q), .in_8(d_ff_15_q), .in_9(d_ff_7_q), .out_10(O0), .out_11(O1),
    .out_12(O2), .out_13(O3), .out_14(O4), .out_15(O5), .out_16(O6), .out_17(O7));
  switcher switcher_8 (
    .EN(and_16_out), .in_2(d_ff_64_q), .in_3(d_ff_56_q), .in_4(d_ff_48_q), .in_5(d_ff_40_q),
    .in_6(d_ff_32_q), .in_7(d_ff_24_q), .in_8(d_ff_16_q), .in_9(d_ff_8_q), .out_10(O0), .out_11(O1),
    .out_12(O2), .out_13(O3), .out_14(O4), .out_15(O5), .out_16(O6), .out_17(O7));
endmodule

module switcher (
  input  EN,
  input  in_2,
  input  in_3,
  input  in_4,
  input  in_5,
  input  in_6,
  input  in_7,
  input  in_8,
  input  in_9,
  output out_10,
  output out_11,
  output out_12,
  output out_13,
  output out_14,
  output out_15,
  output out_16,
  output out_17
);

  assign out_10 = EN ? in_2 : 1'bz;  // Controlled_Buffer controlled_buffer_1
  assign out_11 = EN ? in_3 : 1'bz;  // Controlled_Buffer controlled_buffer_2
  assign out_12 = EN ? in_4 : 1'bz;  // Controlled_Buffer controlled_buffer_3
  assign out_13 = EN ? in_5 : 1'bz;  // Controlled_Buffer controlled_buffer_4
  assign out_14 = EN ? in_6 : 1'bz;  // Controlled_Buffer controlled_buffer_5
  assign out_15 = EN ? in_7 : 1'bz;  // Controlled_Buffer controlled_buffer_6
  assign out_16 = EN ? in_8 : 1'bz;  // Controlled_Buffer controlled_buffer_7
  assign out_17 = EN ? in_9 : 1'bz;  // Controlled_Buffer controlled_buffer_8
endmodule

module switcher_12 (
  input  in_1,
  input  in_2,
  input  in_3,
  input  in_4,
  input  in_5,
  input  in_6,
  input  in_7,
  input  in_8,
  input  in_9,
  input  in_10,
  input  in_11,
  input  in_12,
  input  in_13,
  output out_14,
  output out_15,
  output out_16,
  output out_17,
  output out_18,
  output out_19,
  output out_20,
  output out_21,
  output out_22,
  output out_23,
  output out_24,
  output out_25
);

  assign out_14 = in_1 ? in_2 : 1'bz;  // Controlled_Buffer controlled_buffer_1
  assign out_15 = in_1 ? in_3 : 1'bz;  // Controlled_Buffer controlled_buffer_2
  assign out_16 = in_1 ? in_4 : 1'bz;  // Controlled_Buffer controlled_buffer_3
  assign out_17 = in_1 ? in_5 : 1'bz;  // Controlled_Buffer controlled_buffer_4
  assign out_18 = in_1 ? in_6 : 1'bz;  // Controlled_Buffer controlled_buffer_5
  assign out_19 = in_1 ? in_7 : 1'bz;  // Controlled_Buffer controlled_buffer_6
  assign out_20 = in_1 ? in_8 : 1'bz;  // Controlled_Buffer controlled_buffer_7
  assign out_21 = in_1 ? in_9 : 1'bz;  // Controlled_Buffer controlled_buffer_8
  assign out_22 = in_1 ? in_10 : 1'bz;  // Controlled_Buffer controlled_buffer_9
  assign out_23 = in_1 ? in_11 : 1'bz;  // Controlled_Buffer controlled_buffer_10
  assign out_24 = in_1 ? in_12 : 1'bz;  // Controlled_Buffer controlled_buffer_11
  assign out_25 = in_1 ? in_13 : 1'bz;  // Controlled_Buffer controlled_buffer_12
endmodule

// port_register
module port_registers (
  input  P0_7,
  input  P0_6,
  input  P0_5,
  input  RS,
  input  R,
  input  W,
  input  P0_S,
  input  A2,
  input  A1,
  input  A0,
  input  PS_C,
  input  B7,
  input  B6,
  input  B5,
  input  B4,
  input  B3,
  input  B2,
  input  B1,
  input  B0,
  output [7:0] P0,
  output [7:0] P1,
  output [7:0] P4,
  output [7:0] P5,
  output out_24,
  output out_25,
  output out_26,
  output out_27,
  output out_28,
  output out_29,
  output out_30,
  output out_31
);

  wire and_1_out, and_2_out, and_3_out, and_4_out, and_5_out, and_6_out, and_7_out, and_8_out, and_9_out,
       assync_input_1_out_4, assync_input_1_out_5, assync_input_2_out_4, assync_input_2_out_5,
       assync_input_3_out_4, assync_input_3_out_5, d_ff_3_q, d_ff_4_q, d_ff_7_q, d_ff_8_q, d_ff_11_q,
       d_ff_12_q, d_ff_15_q, d_ff_16_q, d_ff_19_q, d_ff_20_q, d_ff_23_q, d_ff_24_q, d_ff_27_q, d_ff_28_q,
       d_ff_31_q, d_ff_32_q, d_ff_35_q, d_ff_36_q, d_ff_39_q, d_ff_40_q, d_ff_43_q, d_ff_44_q, d_ff_47_q,
       d_ff_48_q, d_ff_51_q, d_ff_52_q, d_ff_55_q, d_ff_56_q, d_ff_59_q, d_ff_60_q, d_ff_63_q, d_ff_64_q,
       not_1_out, not_2_out, not_3_out, or_1_out, or_2_out, P0_R_out, P0_W_out, P1_R_out, P1_W_out, P2_R_out,
       P2_W_out, P3_R_out, P3_W_out, P4_R_out, P4_W_out, P5_R_out, P5_W_out, P6_R_out, P6_W_out, P7_R_out,
       P7_W_out;

  not not_1 (not_1_out, A0);
  not not_2 (not_2_out, A1);
  not not_3 (not_3_out, A2);
  and and_1 (and_1_out, not_3_out, not_2_out, not_1_out);
  and and_2 (and_2_out, not_3_out, not_2_out, A0);
  and and_3 (and_3_out, not_3_out, A1, not_1_out);
  and and_4 (and_4_out, not_3_out, A1, A0);
  and and_5 (and_5_out, A2, not_2_out, not_1_out);
  and and_6 (and_6_out, A2, not_2_out, A0);
  and and_7 (and_7_out, A2, A1, not_1_out);
  and and_8 (and_8_out, A2, A1, A0);
  and P0_R (P0_R_out, R, and_1_out);
  and P1_R (P1_R_out, R, and_2_out);
  and P2_R (P2_R_out, R, and_3_out);
  and P3_R (P3_R_out, R, and_4_out);
  and P0_W (P0_W_out, W, and_1_out);
  and P1_W (P1_W_out, W, and_2_out);
  and P2_W (P2_W_out, W, and_3_out);
  and P3_W (P3_W_out, W, and_4_out);
  and P4_R (P4_R_out, R, and_5_out);
  and P5_R (P5_R_out, R, and_6_out);
  and P6_R (P6_R_out, R, and_7_out);
  and P7_R (P7_R_out, R, and_8_out);
  and P4_W (P4_W_out, W, and_5_out);
  and P5_W (P5_W_out, W, and_6_out);
  and P6_W (P6_W_out, W, and_7_out);
  and P7_W (P7_W_out, W, and_8_out);
  assync_input assync_input_1 (
    .in_1(P0_S), .in_2(P0_7), .in_3(or_2_out), .out_4(assync_input_1_out_4), .out_5(assync_input_1_out_5));
  D_Flip_Flop #(.trigger("high")) d_ff_1 (
    .clk(P0_W_out), .D(B7), .Q(P0[7]), .preset(assync_input_1_out_4), .reset(assync_input_1_out_5));  // open: Qn, en
  assync_input assync_input_2 (
    .in_1(P0_S), .in_2(P0_6), .in_3(or_2_out), .out_4(assync_input_2_out_4), .out_5(assync_input_2_out_5));
  D_Flip_Flop #(.trigger("high")) d_ff_2 (.clk(P1_W_out), .D(B7), .Q(P1[7]), .reset(RS));  // open: Qn, preset, en
  D_Flip_Flop #(.trigger("high")) d_ff_3 (.clk(P2_W_out), .D(B7), .Q(d_ff_3_q), .reset(RS));  // open: Qn, preset, en
  D_Flip_Flop #(.trigger("high")) d_ff_4 (.clk(P3_W_out), .D(B7), .Q(d_ff_4_q), .reset(RS));  // open: Qn, preset, en
  D_Flip_Flop #(.trigger("high")) d_ff_5 (.clk(P4_W_out), .D(B7), .Q(P4[7]), .reset(RS));  // open: Qn, preset, en
  D_Flip_Flop #(.trigger("high")) d_ff_6 (.clk(P5_W_out), .D(B7), .Q(P5[7]), .reset(RS));  // open: Qn, preset, en
  D_Flip_Flop #(.trigger("high")) d_ff_7 (.clk(P6_W_out), .D(B7), .Q(d_ff_7_q), .reset(RS));  // open: Qn, preset, en
  D_Flip_Flop #(.trigger("high")) d_ff_8 (.clk(P7_W_out), .D(B7), .Q(d_ff_8_q), .reset(RS));  // open: Qn, preset, en
  or or_1 (or_1_out, P0[7], P0[6]);
  D_Flip_Flop #(.trigger("high")) d_ff_9 (
    .clk(P0_W_out), .D(B6), .Q(P0[6]), .preset(assync_input_2_out_4), .reset(assync_input_2_out_5));  // open: Qn, en
  assync_input assync_input_3 (
    .in_1(P0_S), .in_2(P0_5), .in_3(RS), .out_4(assync_input_3_out_4), .out_5(assync_input_3_out_5));
  D_Flip_Flop #(.trigger("high")) d_ff_10 (.clk(P1_W_out), .D(B6), .Q(P1[6]), .reset(RS));  // open: Qn, preset, en
  D_Flip_Flop #(.trigger("high")) d_ff_11 (.clk(P2_W_out), .D(B6), .Q(d_ff_11_q), .reset(RS));  // open: Qn, preset, en
  D_Flip_Flop #(.trigger("high")) d_ff_12 (.clk(P3_W_out), .D(B6), .Q(d_ff_12_q), .reset(RS));  // open: Qn, preset, en
  D_Flip_Flop #(.trigger("high")) d_ff_13 (.clk(P4_W_out), .D(B6), .Q(P4[6]), .reset(RS));  // open: Qn, preset, en
  D_Flip_Flop #(.trigger("high")) d_ff_14 (.clk(P5_W_out), .D(B6), .Q(P5[6]), .reset(RS));  // open: Qn, preset, en
  D_Flip_Flop #(.trigger("high")) d_ff_15 (.clk(P6_W_out), .D(B6), .Q(d_ff_15_q), .reset(RS));  // open: Qn, preset, en
  D_Flip_Flop #(.trigger("high")) d_ff_16 (.clk(P7_W_out), .D(B6), .Q(d_ff_16_q), .reset(RS));  // open: Qn, preset, en
  and and_9 (and_9_out, or_1_out, PS_C);
  D_Flip_Flop #(.trigger("high")) d_ff_17 (
    .clk(P0_W_out), .D(B5), .Q(P0[5]), .preset(assync_input_3_out_4), .reset(assync_input_3_out_5));  // open: Qn, en
  D_Flip_Flop #(.trigger("high")) d_ff_18 (.clk(P1_W_out), .D(B5), .Q(P1[5]), .reset(RS));  // open: Qn, preset, en
  D_Flip_Flop #(.trigger("high")) d_ff_19 (.clk(P2_W_out), .D(B5), .Q(d_ff_19_q), .reset(RS));  // open: Qn, preset, en
  D_Flip_Flop #(.trigger("high")) d_ff_20 (.clk(P3_W_out), .D(B5), .Q(d_ff_20_q), .reset(RS));  // open: Qn, preset, en
  D_Flip_Flop #(.trigger("high")) d_ff_21 (.clk(P4_W_out), .D(B5), .Q(P4[5]), .reset(RS));  // open: Qn, preset, en
  D_Flip_Flop #(.trigger("high")) d_ff_22 (.clk(P5_W_out), .D(B5), .Q(P5[5]), .reset(RS));  // open: Qn, preset, en
  D_Flip_Flop #(.trigger("high")) d_ff_23 (.clk(P6_W_out), .D(B5), .Q(d_ff_23_q), .reset(RS));  // open: Qn, preset, en
  D_Flip_Flop #(.trigger("high")) d_ff_24 (.clk(P7_W_out), .D(B5), .Q(d_ff_24_q), .reset(RS));  // open: Qn, preset, en
  or or_2 (or_2_out, and_9_out, RS);
  D_Flip_Flop #(.trigger("high")) d_ff_25 (.clk(P0_W_out), .D(B4), .Q(P0[4]), .reset(RS));  // open: Qn, preset, en
  D_Flip_Flop #(.trigger("high")) d_ff_26 (.clk(P1_W_out), .D(B4), .Q(P1[4]), .reset(RS));  // open: Qn, preset, en
  D_Flip_Flop #(.trigger("high")) d_ff_27 (.clk(P2_W_out), .D(B4), .Q(d_ff_27_q), .reset(RS));  // open: Qn, preset, en
  D_Flip_Flop #(.trigger("high")) d_ff_28 (.clk(P3_W_out), .D(B4), .Q(d_ff_28_q), .reset(RS));  // open: Qn, preset, en
  D_Flip_Flop #(.trigger("high")) d_ff_29 (.clk(P4_W_out), .D(B4), .Q(P4[4]), .reset(RS));  // open: Qn, preset, en
  D_Flip_Flop #(.trigger("high")) d_ff_30 (.clk(P5_W_out), .D(B4), .Q(P5[4]), .reset(RS));  // open: Qn, preset, en
  D_Flip_Flop #(.trigger("high")) d_ff_31 (.clk(P6_W_out), .D(B4), .Q(d_ff_31_q), .reset(RS));  // open: Qn, preset, en
  D_Flip_Flop #(.trigger("high")) d_ff_32 (.clk(P7_W_out), .D(B4), .Q(d_ff_32_q), .reset(RS));  // open: Qn, preset, en
  D_Flip_Flop #(.trigger("high")) d_ff_33 (.clk(P0_W_out), .D(B3), .Q(P0[3]), .reset(RS));  // open: Qn, preset, en
  D_Flip_Flop #(.trigger("high")) d_ff_34 (.clk(P1_W_out), .D(B3), .Q(P1[3]), .reset(RS));  // open: Qn, preset, en
  D_Flip_Flop #(.trigger("high")) d_ff_35 (.clk(P2_W_out), .D(B3), .Q(d_ff_35_q), .reset(RS));  // open: Qn, preset, en
  D_Flip_Flop #(.trigger("high")) d_ff_36 (.clk(P3_W_out), .D(B3), .Q(d_ff_36_q), .reset(RS));  // open: Qn, preset, en
  D_Flip_Flop #(.trigger("high")) d_ff_37 (.clk(P4_W_out), .D(B3), .Q(P4[3]), .reset(RS));  // open: Qn, preset, en
  D_Flip_Flop #(.trigger("high")) d_ff_38 (.clk(P5_W_out), .D(B3), .Q(P5[3]), .reset(RS));  // open: Qn, preset, en
  D_Flip_Flop #(.trigger("high")) d_ff_39 (.clk(P6_W_out), .D(B3), .Q(d_ff_39_q), .reset(RS));  // open: Qn, preset, en
  D_Flip_Flop #(.trigger("high")) d_ff_40 (.clk(P7_W_out), .D(B3), .Q(d_ff_40_q), .reset(RS));  // open: Qn, preset, en
  D_Flip_Flop #(.trigger("high")) d_ff_41 (.clk(P0_W_out), .D(B2), .Q(P0[2]), .reset(RS));  // open: Qn, preset, en
  D_Flip_Flop #(.trigger("high")) d_ff_42 (.clk(P1_W_out), .D(B2), .Q(P1[2]), .reset(RS));  // open: Qn, preset, en
  D_Flip_Flop #(.trigger("high")) d_ff_43 (.clk(P2_W_out), .D(B2), .Q(d_ff_43_q), .reset(RS));  // open: Qn, preset, en
  D_Flip_Flop #(.trigger("high")) d_ff_44 (.clk(P3_W_out), .D(B2), .Q(d_ff_44_q), .reset(RS));  // open: Qn, preset, en
  D_Flip_Flop #(.trigger("high")) d_ff_45 (.clk(P4_W_out), .D(B2), .Q(P4[2]), .reset(RS));  // open: Qn, preset, en
  D_Flip_Flop #(.trigger("high")) d_ff_46 (.clk(P5_W_out), .D(B2), .Q(P5[2]), .reset(RS));  // open: Qn, preset, en
  D_Flip_Flop #(.trigger("high")) d_ff_47 (.clk(P6_W_out), .D(B2), .Q(d_ff_47_q), .reset(RS));  // open: Qn, preset, en
  D_Flip_Flop #(.trigger("high")) d_ff_48 (.clk(P7_W_out), .D(B2), .Q(d_ff_48_q), .reset(RS));  // open: Qn, preset, en
  D_Flip_Flop #(.trigger("high")) d_ff_49 (.clk(P0_W_out), .D(B1), .Q(P0[1]), .reset(RS));  // open: Qn, preset, en
  D_Flip_Flop #(.trigger("high")) d_ff_50 (.clk(P1_W_out), .D(B1), .Q(P1[1]), .reset(RS));  // open: Qn, preset, en
  D_Flip_Flop #(.trigger("high")) d_ff_51 (.clk(P2_W_out), .D(B1), .Q(d_ff_51_q), .reset(RS));  // open: Qn, preset, en
  D_Flip_Flop #(.trigger("high")) d_ff_52 (.clk(P3_W_out), .D(B1), .Q(d_ff_52_q), .reset(RS));  // open: Qn, preset, en
  D_Flip_Flop #(.trigger("high")) d_ff_53 (.clk(P4_W_out), .D(B1), .Q(P4[1]), .reset(RS));  // open: Qn, preset, en
  D_Flip_Flop #(.trigger("high")) d_ff_54 (.clk(P5_W_out), .D(B1), .Q(P5[1]), .reset(RS));  // open: Qn, preset, en
  D_Flip_Flop #(.trigger("high")) d_ff_55 (.clk(P6_W_out), .D(B1), .Q(d_ff_55_q), .reset(RS));  // open: Qn, preset, en
  D_Flip_Flop #(.trigger("high")) d_ff_56 (.clk(P7_W_out), .D(B1), .Q(d_ff_56_q), .reset(RS));  // open: Qn, preset, en
  D_Flip_Flop #(.trigger("high")) d_ff_57 (.clk(P0_W_out), .D(B0), .Q(P0[0]), .reset(RS));  // open: Qn, preset, en
  D_Flip_Flop #(.trigger("high")) d_ff_58 (.clk(P1_W_out), .D(B0), .Q(P1[0]), .reset(RS));  // open: Qn, preset, en
  D_Flip_Flop #(.trigger("high")) d_ff_59 (.clk(P2_W_out), .D(B0), .Q(d_ff_59_q), .reset(RS));  // open: Qn, preset, en
  D_Flip_Flop #(.trigger("high")) d_ff_60 (.clk(P3_W_out), .D(B0), .Q(d_ff_60_q), .reset(RS));  // open: Qn, preset, en
  D_Flip_Flop #(.trigger("high")) d_ff_61 (.clk(P4_W_out), .D(B0), .Q(P4[0]), .reset(RS));  // open: Qn, preset, en
  D_Flip_Flop #(.trigger("high")) d_ff_62 (.clk(P5_W_out), .D(B0), .Q(P5[0]), .reset(RS));  // open: Qn, preset, en
  D_Flip_Flop #(.trigger("high")) d_ff_63 (.clk(P6_W_out), .D(B0), .Q(d_ff_63_q), .reset(RS));  // open: Qn, preset, en
  D_Flip_Flop #(.trigger("high")) d_ff_64 (.clk(P7_W_out), .D(B0), .Q(d_ff_64_q), .reset(RS));  // open: Qn, preset, en
  switcher switcher_1 (
    .EN(P2_R_out), .in_2(d_ff_59_q), .in_3(d_ff_51_q), .in_4(d_ff_43_q), .in_5(d_ff_35_q), .in_6(d_ff_27_q),
    .in_7(d_ff_19_q), .in_8(d_ff_11_q), .in_9(d_ff_3_q), .out_10(out_31), .out_11(out_30), .out_12(out_29),
    .out_13(out_28), .out_14(out_27), .out_15(out_26), .out_16(out_25), .out_17(out_24));
  switcher switcher_2 (
    .EN(P3_R_out), .in_2(d_ff_60_q), .in_3(d_ff_52_q), .in_4(d_ff_44_q), .in_5(d_ff_36_q), .in_6(d_ff_28_q),
    .in_7(d_ff_20_q), .in_8(d_ff_12_q), .in_9(d_ff_4_q), .out_10(out_31), .out_11(out_30), .out_12(out_29),
    .out_13(out_28), .out_14(out_27), .out_15(out_26), .out_16(out_25), .out_17(out_24));
  switcher switcher_3 (
    .EN(P6_R_out), .in_2(d_ff_63_q), .in_3(d_ff_55_q), .in_4(d_ff_47_q), .in_5(d_ff_39_q), .in_6(d_ff_31_q),
    .in_7(d_ff_23_q), .in_8(d_ff_15_q), .in_9(d_ff_7_q), .out_10(out_31), .out_11(out_30), .out_12(out_29),
    .out_13(out_28), .out_14(out_27), .out_15(out_26), .out_16(out_25), .out_17(out_24));
  switcher switcher_4 (
    .EN(P7_R_out), .in_2(d_ff_64_q), .in_3(d_ff_56_q), .in_4(d_ff_48_q), .in_5(d_ff_40_q), .in_6(d_ff_32_q),
    .in_7(d_ff_24_q), .in_8(d_ff_16_q), .in_9(d_ff_8_q), .out_10(out_31), .out_11(out_30), .out_12(out_29),
    .out_13(out_28), .out_14(out_27), .out_15(out_26), .out_16(out_25), .out_17(out_24));
  switcher switcher_5 (
    .EN(P0_R_out), .in_2(P0[0]), .in_3(P0[1]), .in_4(P0[2]), .in_5(P0[3]), .in_6(P0[4]), .in_7(P0[5]),
    .in_8(P0[6]), .in_9(P0[7]), .out_10(out_31), .out_11(out_30), .out_12(out_29), .out_13(out_28),
    .out_14(out_27), .out_15(out_26), .out_16(out_25), .out_17(out_24));
  switcher switcher_6 (
    .EN(P1_R_out), .in_2(P1[0]), .in_3(P1[1]), .in_4(P1[2]), .in_5(P1[3]), .in_6(P1[4]), .in_7(P1[5]),
    .in_8(P1[6]), .in_9(P1[7]), .out_10(out_31), .out_11(out_30), .out_12(out_29), .out_13(out_28),
    .out_14(out_27), .out_15(out_26), .out_16(out_25), .out_17(out_24));
  switcher switcher_7 (
    .EN(P4_R_out), .in_2(P4[0]), .in_3(P4[1]), .in_4(P4[2]), .in_5(P4[3]), .in_6(P4[4]), .in_7(P4[5]),
    .in_8(P4[6]), .in_9(P4[7]), .out_10(out_31), .out_11(out_30), .out_12(out_29), .out_13(out_28),
    .out_14(out_27), .out_15(out_26), .out_16(out_25), .out_17(out_24));
  switcher switcher_8 (
    .EN(P5_R_out), .in_2(P5[0]), .in_3(P5[1]), .in_4(P5[2]), .in_5(P5[3]), .in_6(P5[4]), .in_7(P5[5]),
    .in_8(P5[6]), .in_9(P5[7]), .out_10(out_31), .out_11(out_30), .out_12(out_29), .out_13(out_28),
    .out_14(out_27), .out_15(out_26), .out_16(out_25), .out_17(out_24));
endmodule

module ALU (
  input  EX,
  input  WR,
  input  [19:0] INST_IN,
  input  [7:0] DR_IN,
  input  [7:0] RX_IN,
  input  [7:0] IR_IN,
  input  [7:0] PX_IN,
  input  [11:0] PC_IN,
  input  [11:0] JMP_IN,
  input  [25:0] EXT_BITS,
  input  [2:0] EXT_BITS2,
  input  [1:0] IDC_SEL,
  input  CLOCK,
  output [11:0] ALU_OUT,
  output [3:0] STATUS_BIT,
  output [7:0] RX_OUT
);

  wire aritmethic_operations_1_carry_8, aritmethic_operations_1_carry_12, incrementer_1_borrow_out,
       incrementer_1_carry_out, shift_operations_1_shift_carry;
  wire [6:0] input_enable_1_ext_out;
  wire [7:0] input_enable_1_dr_out, input_enable_1_ir_out, input_enable_1_px_out, input_enable_1_rx_out,
       multiplierdivider_1_dr_out;
  wire [11:0] aritmethic_operations_1_adder_out, input_enable_1_jmp_out, input_enable_1_pc_out;
  wire [15:0] input_enable_1_inst_out;

  input_enable input_enable_1 (
    .EX(EX), .INST_IN(INST_IN), .DR_IN(DR_IN), .RX_IN(RX_IN), .IR_IN(IR_IN), .PX_IN(PX_IN), .PC_IN(PC_IN),
    .JMP_IN(JMP_IN), .DR_OUT(input_enable_1_dr_out), .RX_OUT(input_enable_1_rx_out),
    .IR_OUT(input_enable_1_ir_out), .PX_OUT(input_enable_1_px_out), .PC_OUT(input_enable_1_pc_out),
    .JMP_OUT(input_enable_1_jmp_out), .INST_OUT(input_enable_1_inst_out), .EXT_BITS(EXT_BITS),
    .EXT_OUT(input_enable_1_ext_out), .EXT_BITS2(EXT_BITS2));
  MultiplierDivider multiplierdivider_1 (
    .DR(input_enable_1_dr_out), .RX(input_enable_1_rx_out), .EXT_IN(input_enable_1_ext_out),
    .DR_OUT(multiplierdivider_1_dr_out), .RX_OUT(RX_OUT), .EX(EX));
  logical_operation logical_operation_1 (
    .DR_IN(input_enable_1_dr_out), .RX_IN(input_enable_1_rx_out), .LOGIC_OUT(multiplierdivider_1_dr_out),
    .INST_IN(input_enable_1_inst_out));
  shift_operations shift_operations_1 (
    .INST_IN(input_enable_1_inst_out), .DR_IN(input_enable_1_dr_out), .SHIFT_NUM(input_enable_1_ir_out),
    .SHIFT_OUT(multiplierdivider_1_dr_out), .SHIFT_CARRY(shift_operations_1_shift_carry));
  aritmethic_operations aritmethic_operations_1 (
    .INST_IN(input_enable_1_inst_out), .DR_IN(input_enable_1_dr_out), .PC_IN(input_enable_1_pc_out),
    .RX_IN(input_enable_1_rx_out), .JMP_IN(input_enable_1_jmp_out),
    .ADDER_OUT(aritmethic_operations_1_adder_out), .CARRY_8(aritmethic_operations_1_carry_8),
    .CARRY_12(aritmethic_operations_1_carry_12));
  move_operations move_operations_1 (
    .INST_IN(input_enable_1_inst_out), .ST_IN(input_enable_1_ir_out), .LD_IN(input_enable_1_dr_out),
    .IN_DATA(input_enable_1_px_out), .OUT_DATA(input_enable_1_dr_out), .MOVE_OUT(multiplierdivider_1_dr_out),
    .EXT_BIT(input_enable_1_ext_out), .STL_IN(input_enable_1_rx_out));
  incrementer incrementer_1 (
    .PX_IN(input_enable_1_px_out), .RX_IN(input_enable_1_rx_out), .DR_IN(input_enable_1_dr_out),
    .IDC_IN(IDC_SEL), .EXT_BITS2(EXT_BITS2), .CARRY_OUT(incrementer_1_carry_out),
    .INC_OUT(multiplierdivider_1_dr_out), .BORROW_OUT(incrementer_1_borrow_out), .CLK(CLOCK),
    .INC_OUTH(RX_OUT), .EX(EX));
  Status_Temp status_temp_1 (
    .INST_IN(input_enable_1_inst_out), .EX(EX), .SHT_CARRY(shift_operations_1_shift_carry),
    .CARRY_8(aritmethic_operations_1_carry_8), .CARRY_12(aritmethic_operations_1_carry_12), .RR_IN(ALU_OUT),
    .WR(WR), .COUT_8(STATUS_BIT[0]), .ZERO(STATUS_BIT[1]), .INC_CARRY(incrementer_1_carry_out),
    .DEC_BORROW(incrementer_1_borrow_out), .EXT_BITS2(EXT_BITS2));
  result_register result_register_1 (
    .EX(EX), .RR_12_IN(aritmethic_operations_1_adder_out), .RR_OUT(ALU_OUT),
    .RR_8_IN(multiplierdivider_1_dr_out));

  assign STATUS_BIT[3:2] = 2'b00;

  // Notes on the sheet:
  //   Aritmethic-Logical Unit
endmodule

// logical
module logical_operation (
  input  [7:0] DR_IN,
  input  [7:0] RX_IN,
  input  [15:0] INST_IN,
  output [7:0] LOGIC_OUT
);

  wire and_1_out, and_2_out, and_3_out, and_4_out, and_5_out, and_6_out, and_7_out, and_8_out, not_1_out,
       not_2_out, not_3_out, not_4_out, not_5_out, not_6_out, not_7_out, not_8_out, or_1_out, or_2_out,
       or_3_out, or_4_out, or_5_out, or_6_out, or_7_out, or_8_out, xor_1_out, xor_2_out, xor_3_out,
       xor_4_out, xor_5_out, xor_6_out, xor_7_out, xor_8_out;

  and and_1 (and_1_out, DR_IN[0], RX_IN[0]);
  and and_2 (and_2_out, DR_IN[1], RX_IN[1]);
  and and_3 (and_3_out, DR_IN[2], RX_IN[2]);
  and and_4 (and_4_out, DR_IN[3], RX_IN[3]);
  and and_5 (and_5_out, DR_IN[4], RX_IN[4]);
  and and_6 (and_6_out, DR_IN[5], RX_IN[5]);
  and and_7 (and_7_out, DR_IN[6], RX_IN[6]);
  and and_8 (and_8_out, DR_IN[7], RX_IN[7]);
  switcher switcher_1 (
    .EN(INST_IN[0]), .in_2(and_1_out), .in_3(and_2_out), .in_4(and_3_out), .in_5(and_4_out),
    .in_6(and_5_out), .in_7(and_6_out), .in_8(and_7_out), .in_9(and_8_out), .out_10(LOGIC_OUT[0]),
    .out_11(LOGIC_OUT[1]), .out_12(LOGIC_OUT[2]), .out_13(LOGIC_OUT[3]), .out_14(LOGIC_OUT[4]),
    .out_15(LOGIC_OUT[5]), .out_16(LOGIC_OUT[6]), .out_17(LOGIC_OUT[7]));
  or or_1 (or_1_out, DR_IN[0], RX_IN[0]);
  or or_2 (or_2_out, DR_IN[1], RX_IN[1]);
  or or_3 (or_3_out, DR_IN[2], RX_IN[2]);
  or or_4 (or_4_out, DR_IN[3], RX_IN[3]);
  or or_5 (or_5_out, DR_IN[4], RX_IN[4]);
  or or_6 (or_6_out, DR_IN[5], RX_IN[5]);
  or or_7 (or_7_out, DR_IN[6], RX_IN[6]);
  or or_8 (or_8_out, DR_IN[7], RX_IN[7]);
  switcher switcher_2 (
    .EN(INST_IN[1]), .in_2(or_1_out), .in_3(or_2_out), .in_4(or_3_out), .in_5(or_4_out), .in_6(or_5_out),
    .in_7(or_6_out), .in_8(or_7_out), .in_9(or_8_out), .out_10(LOGIC_OUT[0]), .out_11(LOGIC_OUT[1]),
    .out_12(LOGIC_OUT[2]), .out_13(LOGIC_OUT[3]), .out_14(LOGIC_OUT[4]), .out_15(LOGIC_OUT[5]),
    .out_16(LOGIC_OUT[6]), .out_17(LOGIC_OUT[7]));
  not not_1 (not_1_out, RX_IN[0]);
  not not_2 (not_2_out, RX_IN[1]);
  not not_3 (not_3_out, RX_IN[2]);
  not not_4 (not_4_out, RX_IN[3]);
  not not_5 (not_5_out, RX_IN[4]);
  not not_6 (not_6_out, RX_IN[5]);
  not not_7 (not_7_out, RX_IN[6]);
  not not_8 (not_8_out, RX_IN[7]);
  switcher switcher_3 (
    .EN(INST_IN[2]), .in_2(not_1_out), .in_3(not_2_out), .in_4(not_3_out), .in_5(not_4_out),
    .in_6(not_5_out), .in_7(not_6_out), .in_8(not_7_out), .in_9(not_8_out), .out_10(LOGIC_OUT[0]),
    .out_11(LOGIC_OUT[1]), .out_12(LOGIC_OUT[2]), .out_13(LOGIC_OUT[3]), .out_14(LOGIC_OUT[4]),
    .out_15(LOGIC_OUT[5]), .out_16(LOGIC_OUT[6]), .out_17(LOGIC_OUT[7]));
  xor xor_1 (xor_1_out, DR_IN[0], RX_IN[0]);
  xor xor_2 (xor_2_out, DR_IN[1], RX_IN[1]);
  xor xor_3 (xor_3_out, DR_IN[2], RX_IN[2]);
  xor xor_4 (xor_4_out, DR_IN[3], RX_IN[3]);
  xor xor_5 (xor_5_out, DR_IN[4], RX_IN[4]);
  xor xor_6 (xor_6_out, DR_IN[5], RX_IN[5]);
  xor xor_7 (xor_7_out, DR_IN[6], RX_IN[6]);
  xor xor_8 (xor_8_out, DR_IN[7], RX_IN[7]);
  switcher switcher_4 (
    .EN(INST_IN[3]), .in_2(xor_1_out), .in_3(xor_2_out), .in_4(xor_3_out), .in_5(xor_4_out),
    .in_6(xor_5_out), .in_7(xor_6_out), .in_8(xor_7_out), .in_9(xor_8_out), .out_10(LOGIC_OUT[0]),
    .out_11(LOGIC_OUT[1]), .out_12(LOGIC_OUT[2]), .out_13(LOGIC_OUT[3]), .out_14(LOGIC_OUT[4]),
    .out_15(LOGIC_OUT[5]), .out_16(LOGIC_OUT[6]), .out_17(LOGIC_OUT[7]));
endmodule

// Full-Adder
module aritmethic_operations (
  input  [15:0] INST_IN,
  input  [7:0] DR_IN,
  input  [11:0] PC_IN,
  input  [7:0] RX_IN,
  input  [11:0] JMP_IN,
  output [11:0] ADDER_OUT,
  output CARRY_8,
  output CARRY_12
);

  wire and_1_out, and_2_out, and_3_out, and_4_out, and_5_out, and_6_out, and_7_out, and_8_out, and_9_out,
       and_10_out, and_11_out, and_12_out, and_13_out, and_14_out, and_15_out, and_16_out, and_17_out,
       and_18_out, and_19_out, and_20_out, and_21_out, and_22_out, and_23_out, and_24_out, mixer_1_out_5,
       mixer_1_out_6, mixer_1_out_7, mixer_1_out_8, mixer_1_out_9, mixer_1_out_10, mixer_1_out_11,
       mixer_1_out_12, mixer_1_out_13, mixer_1_out_14, mixer_1_out_15, mixer_1_out_16, mixer_2_out_5,
       mixer_2_out_6, mixer_2_out_7, mixer_2_out_8, mixer_2_out_9, mixer_2_out_10, mixer_2_out_11,
       mixer_2_out_12, mixer_2_out_13, mixer_2_out_14, mixer_2_out_15, mixer_2_out_16, or_1_out, or_2_out,
       or_3_out, or_4_out, or_5_out, or_6_out, or_7_out, or_8_out, or_9_out, or_11_out, or_12_out, or_13_out,
       or_15_out, xor_1_out, xor_2_out, xor_3_out, xor_4_out, xor_5_out, xor_6_out, xor_7_out, xor_8_out,
       xor_9_out, xor_10_out, xor_11_out, xor_12_out, xor_13_out, xor_14_out, xor_15_out, xor_16_out,
       xor_17_out, xor_18_out, xor_19_out, xor_20_out, xor_21_out, xor_22_out, xor_23_out, xor_24_out,
       xor_25_out, xor_26_out, xor_27_out, xor_28_out, xor_29_out, xor_30_out, xor_31_out, xor_32_out,
       xor_33_out, xor_34_out, xor_35_out, xor_36_out;

  mixer mixer_1 (
    .in_1(DR_IN), .in_2(PC_IN), .in_3(DR_IN), .in_4(DR_IN), .out_5(mixer_1_out_5), .out_6(mixer_1_out_6),
    .out_7(mixer_1_out_7), .out_8(mixer_1_out_8), .out_9(mixer_1_out_9), .out_10(mixer_1_out_10),
    .out_11(mixer_1_out_11), .out_12(mixer_1_out_12), .out_13(mixer_1_out_13), .out_14(mixer_1_out_14),
    .out_15(mixer_1_out_15), .out_16(mixer_1_out_16));
  mixer mixer_2 (
    .in_1(RX_IN), .in_2(JMP_IN), .in_3(RX_IN), .in_4(RX_IN), .out_5(mixer_2_out_5), .out_6(mixer_2_out_6),
    .out_7(mixer_2_out_7), .out_8(mixer_2_out_8), .out_9(mixer_2_out_9), .out_10(mixer_2_out_10),
    .out_11(mixer_2_out_11), .out_12(mixer_2_out_12), .out_13(mixer_2_out_13), .out_14(mixer_2_out_14),
    .out_15(mixer_2_out_15), .out_16(mixer_2_out_16));
  xor xor_1 (xor_1_out, mixer_1_out_16, xor_2_out);
  xor xor_2 (xor_2_out, mixer_2_out_16, or_5_out);
  xor xor_3 (xor_3_out, mixer_1_out_15, xor_4_out);
  xor xor_4 (xor_4_out, or_5_out, mixer_2_out_15);
  xor xor_5 (xor_5_out, or_5_out, mixer_2_out_14);
  xor xor_6 (xor_6_out, or_5_out, mixer_2_out_13);
  and and_1 (and_1_out, mixer_1_out_16, xor_2_out);
  and and_2 (and_2_out, mixer_1_out_15, xor_4_out);
  xor xor_7 (xor_7_out, mixer_1_out_14, xor_5_out);
  and and_3 (and_3_out, mixer_1_out_14, xor_5_out);
  xor xor_8 (xor_8_out, mixer_1_out_13, xor_6_out);
  and and_4 (and_4_out, mixer_1_out_13, xor_6_out);
  xor xor_9 (xor_9_out, or_5_out, xor_1_out);
  and and_5 (and_5_out, or_5_out, xor_1_out);
  or or_1 (or_1_out, and_5_out, and_1_out);
  xor xor_10 (xor_10_out, or_1_out, xor_3_out);
  and and_6 (and_6_out, or_1_out, xor_3_out);
  or or_2 (or_2_out, and_6_out, and_2_out);
  xor xor_11 (xor_11_out, or_2_out, xor_7_out);
  and and_7 (and_7_out, or_2_out, xor_7_out);
  or or_3 (or_3_out, and_7_out, and_3_out);
  xor xor_12 (xor_12_out, or_3_out, xor_8_out);
  and and_8 (and_8_out, or_3_out, xor_8_out);
  or or_4 (or_4_out, and_8_out, and_4_out);
  or or_5 (or_5_out, INST_IN[12], INST_IN[5]);
  xor xor_13 (xor_13_out, mixer_2_out_12, or_5_out);
  xor xor_14 (xor_14_out, or_5_out, mixer_2_out_11);
  xor xor_15 (xor_15_out, or_5_out, mixer_2_out_10);
  xor xor_16 (xor_16_out, or_5_out, mixer_2_out_9);
  or or_6 (or_6_out, INST_IN[13], INST_IN[14], INST_IN[15]);
  xor xor_17 (xor_17_out, mixer_1_out_12, xor_13_out);
  and and_9 (and_9_out, mixer_1_out_12, xor_13_out);
  xor xor_18 (xor_18_out, mixer_1_out_11, xor_14_out);
  and and_10 (and_10_out, mixer_1_out_11, xor_14_out);
  xor xor_19 (xor_19_out, mixer_1_out_10, xor_15_out);
  and and_11 (and_11_out, mixer_1_out_10, xor_15_out);
  xor xor_20 (xor_20_out, mixer_1_out_9, xor_16_out);
  and and_12 (and_12_out, mixer_1_out_9, xor_16_out);
  xor xor_21 (xor_21_out, or_4_out, xor_17_out);
  and and_13 (and_13_out, or_4_out, xor_17_out);
  or or_7 (or_7_out, and_13_out, and_9_out);
  xor xor_22 (xor_22_out, or_7_out, xor_18_out);
  and and_14 (and_14_out, or_7_out, xor_18_out);
  or or_8 (or_8_out, and_14_out, and_10_out);
  xor xor_23 (xor_23_out, or_8_out, xor_19_out);
  or or_9 (or_9_out, and_15_out, and_11_out);
  xor xor_24 (xor_24_out, or_9_out, xor_20_out);
  or or_10 (CARRY_8, and_16_out, and_12_out);
  and and_15 (and_15_out, or_8_out, xor_19_out);
  and and_16 (and_16_out, or_9_out, xor_20_out);
  xor xor_25 (xor_25_out, mixer_1_out_8, xor_26_out);
  and and_17 (and_17_out, mixer_1_out_8, xor_26_out);
  xor xor_26 (xor_26_out, mixer_2_out_8, or_5_out);
  xor xor_27 (xor_27_out, mixer_1_out_7, xor_28_out);
  and and_18 (and_18_out, mixer_1_out_7, xor_28_out);
  xor xor_28 (xor_28_out, or_5_out, mixer_2_out_7);
  xor xor_29 (xor_29_out, mixer_1_out_6, xor_30_out);
  xor xor_30 (xor_30_out, or_5_out, mixer_2_out_6);
  xor xor_31 (xor_31_out, mixer_1_out_5, xor_32_out);
  xor xor_32 (xor_32_out, or_5_out, mixer_2_out_5);
  xor xor_33 (xor_33_out, CARRY_8, xor_25_out);
  or or_11 (or_11_out, and_21_out, and_17_out);
  xor xor_34 (xor_34_out, or_11_out, xor_27_out);
  or or_12 (or_12_out, and_22_out, and_18_out);
  and and_19 (and_19_out, mixer_1_out_6, xor_30_out);
  and and_20 (and_20_out, mixer_1_out_5, xor_32_out);
  and and_21 (and_21_out, CARRY_8, xor_25_out);
  and and_22 (and_22_out, or_11_out, xor_27_out);
  xor xor_35 (xor_35_out, or_12_out, xor_29_out);
  and and_23 (and_23_out, or_12_out, xor_29_out);
  or or_13 (or_13_out, and_23_out, and_19_out);
  xor xor_36 (xor_36_out, or_13_out, xor_31_out);
  and and_24 (and_24_out, or_13_out, xor_31_out);
  or or_14 (CARRY_12, and_24_out, and_20_out);
  or or_15 (or_15_out, or_6_out, INST_IN[4], INST_IN[5], INST_IN[12]);
  switcher_12 switcher_12_1 (
    .in_1(or_15_out), .in_2(xor_36_out), .in_3(xor_35_out), .in_4(xor_34_out), .in_5(xor_33_out),
    .in_6(xor_24_out), .in_7(xor_23_out), .in_8(xor_22_out), .in_9(xor_21_out), .in_10(xor_12_out),
    .in_11(xor_11_out), .in_12(xor_10_out), .in_13(xor_9_out), .out_14(ADDER_OUT[11]),
    .out_15(ADDER_OUT[10]), .out_16(ADDER_OUT[9]), .out_17(ADDER_OUT[8]), .out_18(ADDER_OUT[7]),
    .out_19(ADDER_OUT[6]), .out_20(ADDER_OUT[5]), .out_21(ADDER_OUT[4]), .out_22(ADDER_OUT[3]),
    .out_23(ADDER_OUT[2]), .out_24(ADDER_OUT[1]), .out_25(ADDER_OUT[0]));

  // Notes on the sheet:
  //   x0
  //   x0
  //   x0
  //   x0
  //   c0
  //   c0
  //   c0
  //   c0
  //   s0
  //   s0
  //   s0
  //   s0
  //   x0
  //   x0
  //   c0
  //   c0
  //   x0
  //   x0
  //   s0
  //   s0
  //   s0
  //   c0
  //   s0
  //   c0
  //   x0
  //   x0
  //   x0
  //   x0
  //   s0
  //   c0
  //   s0
  //   c0
  //   c0
  //   c0
  //   s0
  //   s0
endmodule

// shifter
module shift_operations (
  input  [15:0] INST_IN,
  input  [7:0] DR_IN,
  input  [7:0] SHIFT_NUM,
  output [7:0] SHIFT_OUT,
  output SHIFT_CARRY
);

  wire and_1_out, and_2_out, and_3_out, multiplexer_1_out, multiplexer_2_out, multiplexer_3_out,
       multiplexer_4_out, multiplexer_5_out, multiplexer_6_out, multiplexer_7_out, multiplexer_8_out,
       multiplexer_9_out, multiplexer_10_out, multiplexer_11_out, multiplexer_12_out, multiplexer_13_out,
       multiplexer_14_out, multiplexer_15_out, multiplexer_16_out, multiplexer_17_out, multiplexer_18_out,
       multiplexer_19_out, multiplexer_20_out, multiplexer_21_out, multiplexer_22_out, multiplexer_23_out,
       multiplexer_24_out, not_1_out, or_2_out, or_buffer_1_out_6, or_buffer_2_out_6;
  wire [1:0] demultiplexer_1_out1, demultiplexer_2_out1, demultiplexer_3_out1;

  or or_1 (SHIFT_CARRY, and_1_out, and_2_out, and_3_out);
  and and_1 (and_1_out, DR_IN[7], not_1_out, INST_IN[11], SHIFT_NUM[0]);
  and and_2 (and_2_out, INST_IN[11], not_1_out, or_buffer_1_out_6, SHIFT_NUM[1]);
  and and_3 (and_3_out, INST_IN[11], not_1_out, or_buffer_2_out_6, SHIFT_NUM[2]);
  not not_1 (not_1_out, INST_IN[10]);
  or or_2 (or_2_out, INST_IN[10], INST_IN[11]);
  Demultiplexer #(.select(2)) demultiplexer_1 (
    .out1(demultiplexer_1_out1[0]), .out2(demultiplexer_1_out1[1]), .in(SHIFT_NUM[0]), .sel(INST_IN[11:10]),
    .en(or_2_out));  // open: out0, out3
  Demultiplexer #(.select(2)) demultiplexer_2 (
    .out1(demultiplexer_2_out1[0]), .out2(demultiplexer_2_out1[1]), .in(SHIFT_NUM[1]), .sel(INST_IN[11:10]),
    .en(or_2_out));  // open: out0, out3
  Demultiplexer #(.select(2)) demultiplexer_3 (
    .out1(demultiplexer_3_out1[0]), .out2(demultiplexer_3_out1[1]), .in(SHIFT_NUM[2]), .sel(INST_IN[11:10]),
    .en(or_2_out));  // open: out0, out3
  Multiplexer #(.select(2)) multiplexer_1 (
    .in0(DR_IN[7]), .in1(1'b0), .in2(DR_IN[6]), .in3(DR_IN[6]), .out(multiplexer_1_out),
    .sel(demultiplexer_1_out1));  // open: en
  or_buffer or_buffer_1 (
    .out_6(or_buffer_1_out_6), .in_1(or_2_out), .in_2(multiplexer_1_out), .in_3(multiplexer_4_out),
    .in_4(1'b0), .in_5(1'b0));
  Multiplexer #(.select(2)) multiplexer_2 (
    .in0(multiplexer_1_out), .in1(1'b0), .in2(multiplexer_7_out), .in3(multiplexer_7_out),
    .out(multiplexer_2_out), .sel(demultiplexer_2_out1));  // open: en
  or_buffer or_buffer_2 (
    .out_6(or_buffer_2_out_6), .in_1(or_2_out), .in_2(multiplexer_2_out), .in_3(multiplexer_5_out),
    .in_4(multiplexer_8_out), .in_5(multiplexer_11_out));
  Multiplexer #(.select(2)) multiplexer_3 (
    .in0(multiplexer_2_out), .in1(1'b0), .in2(multiplexer_14_out), .in3(multiplexer_14_out),
    .out(multiplexer_3_out), .sel(demultiplexer_3_out1));  // open: en
  Multiplexer #(.select(2)) multiplexer_4 (
    .in0(DR_IN[6]), .in1(DR_IN[7]), .in2(DR_IN[5]), .in3(DR_IN[5]), .out(multiplexer_4_out),
    .sel(demultiplexer_1_out1));  // open: en
  Multiplexer #(.select(2)) multiplexer_5 (
    .in0(multiplexer_4_out), .in1(1'b0), .in2(multiplexer_10_out), .in3(multiplexer_10_out),
    .out(multiplexer_5_out), .sel(demultiplexer_2_out1));  // open: en
  Multiplexer #(.select(2)) multiplexer_6 (
    .in0(multiplexer_5_out), .in1(1'b0), .in2(multiplexer_17_out), .in3(multiplexer_17_out),
    .out(multiplexer_6_out), .sel(demultiplexer_3_out1));  // open: en
  Multiplexer #(.select(2)) multiplexer_7 (
    .in0(DR_IN[5]), .in1(DR_IN[6]), .in2(DR_IN[4]), .in3(DR_IN[4]), .out(multiplexer_7_out),
    .sel(demultiplexer_1_out1));  // open: en
  Multiplexer #(.select(2)) multiplexer_8 (
    .in0(multiplexer_7_out), .in1(multiplexer_1_out), .in2(multiplexer_13_out), .in3(multiplexer_13_out),
    .out(multiplexer_8_out), .sel(demultiplexer_2_out1));  // open: en
  Multiplexer #(.select(2)) multiplexer_9 (
    .in0(multiplexer_8_out), .in1(1'b0), .in2(multiplexer_20_out), .in3(multiplexer_20_out),
    .out(multiplexer_9_out), .sel(demultiplexer_3_out1));  // open: en
  Multiplexer #(.select(2)) multiplexer_10 (
    .in0(DR_IN[4]), .in1(DR_IN[5]), .in2(DR_IN[3]), .in3(DR_IN[3]), .out(multiplexer_10_out),
    .sel(demultiplexer_1_out1));  // open: en
  Multiplexer #(.select(2)) multiplexer_11 (
    .in0(multiplexer_10_out), .in1(multiplexer_4_out), .in2(multiplexer_16_out), .in3(multiplexer_16_out),
    .out(multiplexer_11_out), .sel(demultiplexer_2_out1));  // open: en
  Multiplexer #(.select(2)) multiplexer_12 (
    .in0(multiplexer_11_out), .in1(1'b0), .in2(multiplexer_23_out), .in3(multiplexer_23_out),
    .out(multiplexer_12_out), .sel(demultiplexer_3_out1));  // open: en
  Multiplexer #(.select(2)) multiplexer_13 (
    .in0(DR_IN[3]), .in1(DR_IN[4]), .in2(DR_IN[2]), .in3(DR_IN[2]), .out(multiplexer_13_out),
    .sel(demultiplexer_1_out1));  // open: en
  Multiplexer #(.select(2)) multiplexer_14 (
    .in0(multiplexer_13_out), .in1(multiplexer_7_out), .in2(multiplexer_19_out), .in3(multiplexer_19_out),
    .out(multiplexer_14_out), .sel(demultiplexer_2_out1));  // open: en
  Multiplexer #(.select(2)) multiplexer_15 (
    .in0(multiplexer_14_out), .in1(multiplexer_2_out), .in2(1'b0), .in3(1'b0), .out(multiplexer_15_out),
    .sel(demultiplexer_3_out1));  // open: en
  Multiplexer #(.select(2)) multiplexer_16 (
    .in0(DR_IN[2]), .in1(DR_IN[3]), .in2(DR_IN[1]), .in3(DR_IN[1]), .out(multiplexer_16_out),
    .sel(demultiplexer_1_out1));  // open: en
  Multiplexer #(.select(2)) multiplexer_17 (
    .in0(multiplexer_16_out), .in1(multiplexer_10_out), .in2(multiplexer_22_out), .in3(multiplexer_22_out),
    .out(multiplexer_17_out), .sel(demultiplexer_2_out1));  // open: en
  Multiplexer #(.select(2)) multiplexer_18 (
    .in0(multiplexer_17_out), .in1(multiplexer_5_out), .in2(1'b0), .in3(1'b0), .out(multiplexer_18_out),
    .sel(demultiplexer_3_out1));  // open: en
  Multiplexer #(.select(2)) multiplexer_19 (
    .in0(DR_IN[1]), .in1(DR_IN[2]), .in2(DR_IN[0]), .in3(DR_IN[0]), .out(multiplexer_19_out),
    .sel(demultiplexer_1_out1));  // open: en
  Multiplexer #(.select(2)) multiplexer_20 (
    .in0(multiplexer_19_out), .in1(multiplexer_13_out), .in2(1'b0), .in3(1'b0), .out(multiplexer_20_out),
    .sel(demultiplexer_2_out1));  // open: en
  Multiplexer #(.select(2)) multiplexer_21 (
    .in0(multiplexer_20_out), .in1(multiplexer_8_out), .in2(1'b0), .in3(1'b0), .out(multiplexer_21_out),
    .sel(demultiplexer_3_out1));  // open: en
  Multiplexer #(.select(2)) multiplexer_22 (
    .in0(DR_IN[0]), .in1(DR_IN[1]), .in2(1'b0), .in3(1'b0), .out(multiplexer_22_out),
    .sel(demultiplexer_1_out1));  // open: en
  Multiplexer #(.select(2)) multiplexer_23 (
    .in0(multiplexer_22_out), .in1(multiplexer_16_out), .in2(1'b0), .in3(1'b0), .out(multiplexer_23_out),
    .sel(demultiplexer_2_out1));  // open: en
  Multiplexer #(.select(2)) multiplexer_24 (
    .in0(multiplexer_23_out), .in1(multiplexer_11_out), .in2(1'b0), .in3(1'b0), .out(multiplexer_24_out),
    .sel(demultiplexer_3_out1));  // open: en
  switcher switcher_1 (
    .EN(or_2_out), .in_2(multiplexer_24_out), .in_3(multiplexer_21_out), .in_4(multiplexer_18_out),
    .in_5(multiplexer_15_out), .in_6(multiplexer_12_out), .in_7(multiplexer_9_out), .in_8(multiplexer_6_out),
    .in_9(multiplexer_3_out), .out_10(SHIFT_OUT[0]), .out_11(SHIFT_OUT[1]), .out_12(SHIFT_OUT[2]),
    .out_13(SHIFT_OUT[3]), .out_14(SHIFT_OUT[4]), .out_15(SHIFT_OUT[5]), .out_16(SHIFT_OUT[6]),
    .out_17(SHIFT_OUT[7]));
endmodule
// INPUT
module input_enable (
  input  EX,
  input  [19:0] INST_IN,
  input  [7:0] DR_IN,
  input  [7:0] RX_IN,
  input  [7:0] IR_IN,
  input  [7:0] PX_IN,
  input  [11:0] PC_IN,
  input  [11:0] JMP_IN,
  input  [25:0] EXT_BITS,
  input  [2:0] EXT_BITS2,
  output [7:0] DR_OUT,
  output [7:0] RX_OUT,
  output [7:0] IR_OUT,
  output [7:0] PX_OUT,
  output [11:0] PC_OUT,
  output [11:0] JMP_OUT,
  output [15:0] INST_OUT,
  output [6:0] EXT_OUT
);

  wire and_2_out, not_2_out, not_3_out, or_2_out, or_3_out, or_4_out, or_5_out, or_6_out, or_7_out, or_8_out,
       or_9_out, or_10_out;

  and AND (INST_OUT[0], INST_IN[0], EX);
  and OR (INST_OUT[1], INST_IN[1], EX);
  and NOT (INST_OUT[2], INST_IN[2], EX);
  and XOR (INST_OUT[3], INST_IN[3], EX);
  and ADD (INST_OUT[4], INST_IN[4], EX);
  and SUB (INST_OUT[5], INST_IN[5], EX);
  and ST (INST_OUT[6], INST_IN[6], EX);
  and LD (INST_OUT[7], INST_IN[7], EX);
  and IN (INST_OUT[8], INST_IN[8], EX);
  and OUT (INST_OUT[9], INST_IN[9], EX);
  and SHR (INST_OUT[10], INST_IN[10], EX);
  and SHL (INST_OUT[11], INST_IN[11], EX);
  and BT (INST_OUT[12], INST_IN[12], EX);
  and JC (INST_OUT[13], INST_IN[16], EX);
  and JZ (INST_OUT[14], INST_IN[17], EX);
  and JP (INST_OUT[15], INST_IN[18], EX);
  and MUL (EXT_OUT[0], EXT_BITS[23], EX);
  and DIV (EXT_OUT[1], EXT_BITS[24], EX);
  and STL (EXT_OUT[2], EXT_BITS[25], EX);
  and STD (EXT_OUT[3], INST_IN[19], EX);
  and INCR (EXT_OUT[4], EXT_BITS2[0], EX);
  and DECR (EXT_OUT[5], EXT_BITS2[1], EX);
  and IDC (EXT_OUT[6], EXT_BITS2[2], EX);
  or or_2 (or_2_out, INST_OUT[13], INST_OUT[14], INST_OUT[15]);
  or or_3 (or_3_out, EXT_OUT[0], EXT_OUT[1]);
  or or_4 (or_4_out, EXT_OUT[4], EXT_OUT[5], EXT_OUT[6]);
  or or_5 (or_5_out, INST_OUT[10], INST_OUT[11]);
  or or_6 (or_6_out, or_9_out, INST_OUT[2], EXT_OUT[2]);
  not not_2 (not_2_out, INST_OUT[9]);
  not not_3 (not_3_out, or_5_out);
  or or_7 (or_7_out, or_5_out, INST_OUT[6], EXT_OUT[3]);
  or or_8 (or_8_out, INST_OUT[0], INST_OUT[1], INST_OUT[3], INST_OUT[4], INST_OUT[5], INST_OUT[7], INST_OUT[9], or_5_out, INST_OUT[12]);
  or or_9 (or_9_out, or_8_out, or_3_out, or_4_out);
  and and_2 (and_2_out, or_6_out, not_2_out, not_3_out);
  or or_10 (or_10_out, INST_OUT[8], or_4_out);
  enabler enabler_1 (
    .in_1(or_9_out), .in_2(DR_IN[0]), .in_3(DR_IN[1]), .in_4(DR_IN[2]), .in_5(DR_IN[3]), .in_6(DR_IN[4]),
    .in_7(DR_IN[5]), .in_8(DR_IN[6]), .in_9(DR_IN[7]), .out_10(DR_OUT[0]), .out_11(DR_OUT[1]),
    .out_12(DR_OUT[2]), .out_13(DR_OUT[3]), .out_14(DR_OUT[4]), .out_15(DR_OUT[5]), .out_16(DR_OUT[6]),
    .out_17(DR_OUT[7]));
  enabler enabler_2 (
    .in_1(and_2_out), .in_2(RX_IN[0]), .in_3(RX_IN[1]), .in_4(RX_IN[2]), .in_5(RX_IN[3]), .in_6(RX_IN[4]),
    .in_7(RX_IN[5]), .in_8(RX_IN[6]), .in_9(RX_IN[7]), .out_10(RX_OUT[0]), .out_11(RX_OUT[1]),
    .out_12(RX_OUT[2]), .out_13(RX_OUT[3]), .out_14(RX_OUT[4]), .out_15(RX_OUT[5]), .out_16(RX_OUT[6]),
    .out_17(RX_OUT[7]));
  enabler enabler_3 (
    .in_1(or_7_out), .in_2(IR_IN[0]), .in_3(IR_IN[1]), .in_4(IR_IN[2]), .in_5(IR_IN[3]), .in_6(IR_IN[4]),
    .in_7(IR_IN[5]), .in_8(IR_IN[6]), .in_9(IR_IN[7]), .out_10(IR_OUT[0]), .out_11(IR_OUT[1]),
    .out_12(IR_OUT[2]), .out_13(IR_OUT[3]), .out_14(IR_OUT[4]), .out_15(IR_OUT[5]), .out_16(IR_OUT[6]),
    .out_17(IR_OUT[7]));
  enabler enabler_4 (
    .in_1(or_10_out), .in_2(PX_IN[0]), .in_3(PX_IN[1]), .in_4(PX_IN[2]), .in_5(PX_IN[3]), .in_6(PX_IN[4]),
    .in_7(PX_IN[5]), .in_8(PX_IN[6]), .in_9(PX_IN[7]), .out_10(PX_OUT[0]), .out_11(PX_OUT[1]),
    .out_12(PX_OUT[2]), .out_13(PX_OUT[3]), .out_14(PX_OUT[4]), .out_15(PX_OUT[5]), .out_16(PX_OUT[6]),
    .out_17(PX_OUT[7]));
  enabler_12 enabler_12_1 (
    .in_1(or_2_out), .in_2(PC_IN[0]), .in_3(PC_IN[1]), .in_4(PC_IN[2]), .in_5(PC_IN[3]), .in_6(PC_IN[4]),
    .in_7(PC_IN[5]), .in_8(PC_IN[6]), .in_9(PC_IN[7]), .in_10(PC_IN[8]), .in_11(PC_IN[9]), .in_12(PC_IN[10]),
    .in_13(PC_IN[11]), .out_14(PC_OUT[0]), .out_15(PC_OUT[1]), .out_16(PC_OUT[2]), .out_17(PC_OUT[3]),
    .out_18(PC_OUT[4]), .out_19(PC_OUT[5]), .out_20(PC_OUT[6]), .out_21(PC_OUT[7]), .out_22(PC_OUT[8]),
    .out_23(PC_OUT[9]), .out_24(PC_OUT[10]), .out_25(PC_OUT[11]));
  enabler_12 enabler_12_2 (
    .in_1(or_2_out), .in_2(JMP_IN[0]), .in_3(JMP_IN[1]), .in_4(JMP_IN[2]), .in_5(JMP_IN[3]),
    .in_6(JMP_IN[4]), .in_7(JMP_IN[5]), .in_8(JMP_IN[6]), .in_9(JMP_IN[7]), .in_10(JMP_IN[8]),
    .in_11(JMP_IN[9]), .in_12(JMP_IN[10]), .in_13(JMP_IN[11]), .out_14(JMP_OUT[0]), .out_15(JMP_OUT[1]),
    .out_16(JMP_OUT[2]), .out_17(JMP_OUT[3]), .out_18(JMP_OUT[4]), .out_19(JMP_OUT[5]), .out_20(JMP_OUT[6]),
    .out_21(JMP_OUT[7]), .out_22(JMP_OUT[8]), .out_23(JMP_OUT[9]), .out_24(JMP_OUT[10]), .out_25(JMP_OUT[11]));
endmodule

module enabler (
  input  in_1,
  input  in_2,
  input  in_3,
  input  in_4,
  input  in_5,
  input  in_6,
  input  in_7,
  input  in_8,
  input  in_9,
  output out_10,
  output out_11,
  output out_12,
  output out_13,
  output out_14,
  output out_15,
  output out_16,
  output out_17
);

  and and_1 (out_10, in_1, in_2);
  and and_2 (out_11, in_1, in_3);
  and and_3 (out_12, in_1, in_4);
  and and_4 (out_13, in_1, in_5);
  and and_5 (out_14, in_1, in_6);
  and and_6 (out_15, in_1, in_7);
  and and_7 (out_16, in_1, in_8);
  and and_8 (out_17, in_1, in_9);
endmodule

module enabler_12 (
  input  in_1,
  input  in_2,
  input  in_3,
  input  in_4,
  input  in_5,
  input  in_6,
  input  in_7,
  input  in_8,
  input  in_9,
  input  in_10,
  input  in_11,
  input  in_12,
  input  in_13,
  output out_14,
  output out_15,
  output out_16,
  output out_17,
  output out_18,
  output out_19,
  output out_20,
  output out_21,
  output out_22,
  output out_23,
  output out_24,
  output out_25
);

  and and_1 (out_14, in_1, in_2);
  and and_2 (out_15, in_1, in_3);
  and and_3 (out_16, in_1, in_4);
  and and_4 (out_17, in_1, in_5);
  and and_5 (out_18, in_1, in_6);
  and and_6 (out_19, in_1, in_7);
  and and_7 (out_20, in_1, in_8);
  and and_8 (out_21, in_1, in_9);
  and and_9 (out_22, in_1, in_10);
  and and_10 (out_23, in_1, in_11);
  and and_11 (out_24, in_1, in_12);
  and and_12 (out_25, in_1, in_13);
endmodule

// Move
module move_operations (
  input  [15:0] INST_IN,
  input  [7:0] ST_IN,
  input  [7:0] LD_IN,
  input  [7:0] IN_DATA,
  input  [7:0] OUT_DATA,
  input  [7:0] STL_IN,
  input  [6:0] EXT_BIT,
  output [7:0] MOVE_OUT
);

  switcher switcher_1 (
    .EN(INST_IN[6]), .in_2(ST_IN[0]), .in_3(ST_IN[1]), .in_4(ST_IN[2]), .in_5(ST_IN[3]), .in_6(ST_IN[4]),
    .in_7(ST_IN[5]), .in_8(ST_IN[6]), .in_9(ST_IN[7]), .out_10(MOVE_OUT[0]), .out_11(MOVE_OUT[1]),
    .out_12(MOVE_OUT[2]), .out_13(MOVE_OUT[3]), .out_14(MOVE_OUT[4]), .out_15(MOVE_OUT[5]),
    .out_16(MOVE_OUT[6]), .out_17(MOVE_OUT[7]));
  switcher switcher_2 (
    .EN(INST_IN[7]), .in_2(LD_IN[0]), .in_3(LD_IN[1]), .in_4(LD_IN[2]), .in_5(LD_IN[3]), .in_6(LD_IN[4]),
    .in_7(LD_IN[5]), .in_8(LD_IN[6]), .in_9(LD_IN[7]), .out_10(MOVE_OUT[0]), .out_11(MOVE_OUT[1]),
    .out_12(MOVE_OUT[2]), .out_13(MOVE_OUT[3]), .out_14(MOVE_OUT[4]), .out_15(MOVE_OUT[5]),
    .out_16(MOVE_OUT[6]), .out_17(MOVE_OUT[7]));
  switcher switcher_3 (
    .EN(INST_IN[8]), .in_2(IN_DATA[0]), .in_3(IN_DATA[1]), .in_4(IN_DATA[2]), .in_5(IN_DATA[3]),
    .in_6(IN_DATA[4]), .in_7(IN_DATA[5]), .in_8(IN_DATA[6]), .in_9(IN_DATA[7]), .out_10(MOVE_OUT[0]),
    .out_11(MOVE_OUT[1]), .out_12(MOVE_OUT[2]), .out_13(MOVE_OUT[3]), .out_14(MOVE_OUT[4]),
    .out_15(MOVE_OUT[5]), .out_16(MOVE_OUT[6]), .out_17(MOVE_OUT[7]));
  switcher switcher_4 (
    .EN(INST_IN[9]), .in_2(OUT_DATA[0]), .in_3(OUT_DATA[1]), .in_4(OUT_DATA[2]), .in_5(OUT_DATA[3]),
    .in_6(OUT_DATA[4]), .in_7(OUT_DATA[5]), .in_8(OUT_DATA[6]), .in_9(OUT_DATA[7]), .out_10(MOVE_OUT[0]),
    .out_11(MOVE_OUT[1]), .out_12(MOVE_OUT[2]), .out_13(MOVE_OUT[3]), .out_14(MOVE_OUT[4]),
    .out_15(MOVE_OUT[5]), .out_16(MOVE_OUT[6]), .out_17(MOVE_OUT[7]));
  switcher switcher_5 (
    .EN(EXT_BIT[2]), .in_2(STL_IN[0]), .in_3(STL_IN[1]), .in_4(STL_IN[2]), .in_5(STL_IN[3]),
    .in_6(STL_IN[4]), .in_7(STL_IN[5]), .in_8(STL_IN[6]), .in_9(STL_IN[7]), .out_10(MOVE_OUT[0]),
    .out_11(MOVE_OUT[1]), .out_12(MOVE_OUT[2]), .out_13(MOVE_OUT[3]), .out_14(MOVE_OUT[4]),
    .out_15(MOVE_OUT[5]), .out_16(MOVE_OUT[6]), .out_17(MOVE_OUT[7]));
  switcher switcher_6 (
    .EN(EXT_BIT[3]), .in_2(ST_IN[0]), .in_3(ST_IN[1]), .in_4(ST_IN[2]), .in_5(ST_IN[3]), .in_6(ST_IN[4]),
    .in_7(ST_IN[5]), .in_8(ST_IN[6]), .in_9(ST_IN[7]), .out_10(MOVE_OUT[0]), .out_11(MOVE_OUT[1]),
    .out_12(MOVE_OUT[2]), .out_13(MOVE_OUT[3]), .out_14(MOVE_OUT[4]), .out_15(MOVE_OUT[5]),
    .out_16(MOVE_OUT[6]), .out_17(MOVE_OUT[7]));
  switcher switcher_7 (
    .EN(EXT_BIT[6]), .in_2(LD_IN[0]), .in_3(LD_IN[1]), .in_4(LD_IN[2]), .in_5(LD_IN[3]), .in_6(LD_IN[4]),
    .in_7(LD_IN[5]), .in_8(LD_IN[6]), .in_9(LD_IN[7]), .out_10(MOVE_OUT[0]), .out_11(MOVE_OUT[1]),
    .out_12(MOVE_OUT[2]), .out_13(MOVE_OUT[3]), .out_14(MOVE_OUT[4]), .out_15(MOVE_OUT[5]),
    .out_16(MOVE_OUT[6]), .out_17(MOVE_OUT[7]));
endmodule

module or_buffer (
  input  in_1,
  input  in_2,
  input  in_3,
  input  in_4,
  input  in_5,
  output out_6
);

  wire or_1_out;

  assign out_6 = in_1 ? or_1_out : 1'bz;  // Controlled_Buffer controlled_buffer_1
  or or_1 (or_1_out, in_2, in_3, in_4, in_5);
endmodule

// Result Register
module result_register (
  input  EX,
  input  [7:0] RR_8_IN,
  input  [11:0] RR_12_IN,
  output [11:0] RR_OUT
);

  D_Flip_Flop #(.trigger("falling")) d_ff_1 (
    .clk(EX), .D(RR_12_IN[11]), .Q(RR_OUT[11]));  // open: Qn, preset, en, reset
  D_Flip_Flop #(.trigger("falling")) d_ff_2 (
    .clk(EX), .D(RR_12_IN[10]), .Q(RR_OUT[10]));  // open: Qn, preset, en, reset
  D_Flip_Flop #(.trigger("falling")) d_ff_3 (.clk(EX), .D(RR_12_IN[9]), .Q(RR_OUT[9]));  // open: Qn, preset, en, reset
  D_Flip_Flop #(.trigger("falling")) d_ff_4 (.clk(EX), .D(RR_12_IN[8]), .Q(RR_OUT[8]));  // open: Qn, preset, en, reset
  D_Flip_Flop #(.trigger("falling")) d_ff_5 (.clk(EX), .D(RR_8_IN[7]), .Q(RR_OUT[7]));  // open: Qn, preset, en, reset
  D_Flip_Flop #(.trigger("falling")) d_ff_6 (.clk(EX), .D(RR_8_IN[6]), .Q(RR_OUT[6]));  // open: Qn, preset, en, reset
  D_Flip_Flop #(.trigger("falling")) d_ff_7 (.clk(EX), .D(RR_8_IN[5]), .Q(RR_OUT[5]));  // open: Qn, preset, en, reset
  D_Flip_Flop #(.trigger("falling")) d_ff_8 (.clk(EX), .D(RR_8_IN[4]), .Q(RR_OUT[4]));  // open: Qn, preset, en, reset
  D_Flip_Flop #(.trigger("falling")) d_ff_9 (.clk(EX), .D(RR_8_IN[3]), .Q(RR_OUT[3]));  // open: Qn, preset, en, reset
  D_Flip_Flop #(.trigger("falling")) d_ff_10 (.clk(EX), .D(RR_8_IN[2]), .Q(RR_OUT[2]));  // open: Qn, preset, en, reset
  D_Flip_Flop #(.trigger("falling")) d_ff_11 (.clk(EX), .D(RR_8_IN[1]), .Q(RR_OUT[1]));  // open: Qn, preset, en, reset
  D_Flip_Flop #(.trigger("falling")) d_ff_12 (.clk(EX), .D(RR_8_IN[0]), .Q(RR_OUT[0]));  // open: Qn, preset, en, reset

  assign RR_12_IN[7:0] = RR_8_IN;
endmodule

module mixer (
  input  [7:0] in_1,
  input  [11:0] in_2,
  input  [7:0] in_3,
  input  [7:0] in_4,
  output out_5,
  output out_6,
  output out_7,
  output out_8,
  output out_9,
  output out_10,
  output out_11,
  output out_12,
  output out_13,
  output out_14,
  output out_15,
  output out_16
);

  buf or_1 (out_5, in_2[11]);  // OR_Gate
  buf or_2 (out_6, in_2[10]);  // OR_Gate
  buf or_3 (out_7, in_2[9]);  // OR_Gate
  buf or_4 (out_8, in_2[8]);  // OR_Gate
  or or_5 (out_9, in_4[7], in_3[7], in_1[7], in_2[7]);
  or or_6 (out_10, in_4[6], in_3[6], in_1[6], in_2[6]);
  or or_7 (out_11, in_4[5], in_3[5], in_1[5], in_2[5]);
  or or_8 (out_12, in_4[4], in_3[4], in_1[4], in_2[4]);
  or or_9 (out_13, in_4[3], in_3[3], in_1[3], in_2[3]);
  or or_10 (out_14, in_4[2], in_3[2], in_1[2], in_2[2]);
  or or_11 (out_15, in_4[1], in_3[1], in_1[1], in_2[1]);
  or or_12 (out_16, in_4[0], in_3[0], in_1[0], in_2[0]);
endmodule

// Status
module Status_Temp (
  input  [15:0] INST_IN,
  input  EX,
  input  SHT_CARRY,
  input  CARRY_8,
  input  CARRY_12,
  input  INC_CARRY,
  input  DEC_BORROW,
  input  [11:0] RR_IN,
  input  WR,
  input  [2:0] EXT_BITS2,
  output COUT_8,
  output ZERO
);

  wire and_1_out, and_2_out, controlled_buffer_1_out, d_ff_2_q, nor_1_out, not_1_out, not_2_out, or_1_out,
       or_2_out, or_3_out, or_4_out;

  not not_1 (not_1_out, EXT_BITS2[1]);
  not not_2 (not_2_out, DEC_BORROW);
  or or_1 (or_1_out, EXT_BITS2[0], EXT_BITS2[1]);
  assign controlled_buffer_1_out = not_1_out ? INC_CARRY : 1'bz;  // Controlled_Buffer controlled_buffer_1
  assign controlled_buffer_1_out = EXT_BITS2[1] ? not_2_out : 1'bz;  // Controlled_Buffer controlled_buffer_2
  and and_1 (and_1_out, controlled_buffer_1_out, or_1_out);
  or or_2 (or_2_out, INST_IN[10], INST_IN[11]);
  or or_3 (or_3_out, SHT_CARRY, CARRY_8, and_1_out);
  and and_2 (and_2_out, EX, or_4_out);
  D_Flip_Flop #(.trigger("falling")) d_ff_1 (.clk(and_2_out), .D(or_3_out), .Q(COUT_8));  // open: Qn, preset, en, reset
  D_Flip_Flop #(.trigger("falling")) d_ff_2 (
    .clk(and_2_out), .D(CARRY_12), .Q(d_ff_2_q));  // open: Qn, preset, en, reset
  D_Flip_Flop #(.trigger("high")) d_ff_3 (.clk(WR), .D(nor_1_out), .Q(ZERO));  // open: Qn, preset, en, reset
  nor nor_1 (nor_1_out, RR_IN[0], RR_IN[1], RR_IN[2], RR_IN[3], RR_IN[4], RR_IN[5], RR_IN[6], RR_IN[7]);
  or or_4 (or_4_out, or_1_out, or_2_out, INST_IN[4], INST_IN[5], INST_IN[12]);
endmodule

// Jumps Register
module jump_register (
  input  JUMP_HIGH,
  input  JUMP_LOW,
  input  RESET,
  input  [7:0] JUMP_IN,
  input  CALL,
  input  SBIT,
  output [11:0] JUMP_OUT
);

  wire and_1_out, and_2_out, and_3_out, not_1_out, not_2_out, or_1_out;

  and and_1 (and_1_out, CALL, SBIT);
  and and_2 (and_2_out, CALL, not_1_out);
  not not_1 (not_1_out, SBIT);
  not not_2 (not_2_out, JUMP_LOW);
  and and_3 (and_3_out, not_2_out, JUMP_HIGH);
  D_Flip_Flop d_ff_1 (
    .clk(and_3_out), .D(JUMP_IN[3]), .Q(JUMP_OUT[11]), .preset(and_1_out), .reset(or_1_out));  // open: Qn, en
  or or_1 (or_1_out, RESET, and_2_out);
  D_Flip_Flop d_ff_2 (.clk(and_3_out), .D(JUMP_IN[2]), .Q(JUMP_OUT[10]), .reset(RESET));  // open: Qn, preset, en
  D_Flip_Flop d_ff_3 (.clk(and_3_out), .D(JUMP_IN[1]), .Q(JUMP_OUT[9]), .reset(RESET));  // open: Qn, preset, en
  D_Flip_Flop d_ff_4 (.clk(and_3_out), .D(JUMP_IN[0]), .Q(JUMP_OUT[8]), .reset(RESET));  // open: Qn, preset, en
  D_Flip_Flop d_ff_5 (.clk(JUMP_LOW), .D(JUMP_IN[7]), .Q(JUMP_OUT[7]), .reset(RESET));  // open: Qn, preset, en
  D_Flip_Flop d_ff_6 (.clk(JUMP_LOW), .D(JUMP_IN[6]), .Q(JUMP_OUT[6]), .reset(RESET));  // open: Qn, preset, en
  D_Flip_Flop d_ff_7 (.clk(JUMP_LOW), .D(JUMP_IN[5]), .Q(JUMP_OUT[5]), .reset(RESET));  // open: Qn, preset, en
  D_Flip_Flop d_ff_8 (.clk(JUMP_LOW), .D(JUMP_IN[4]), .Q(JUMP_OUT[4]), .reset(RESET));  // open: Qn, preset, en
  D_Flip_Flop d_ff_9 (.clk(JUMP_LOW), .D(JUMP_IN[3]), .Q(JUMP_OUT[3]), .reset(RESET));  // open: Qn, preset, en
  D_Flip_Flop d_ff_10 (.clk(JUMP_LOW), .D(JUMP_IN[2]), .Q(JUMP_OUT[2]), .reset(RESET));  // open: Qn, preset, en
  D_Flip_Flop d_ff_11 (.clk(JUMP_LOW), .D(JUMP_IN[1]), .Q(JUMP_OUT[1]), .reset(RESET));  // open: Qn, preset, en
  D_Flip_Flop d_ff_12 (.clk(JUMP_LOW), .D(JUMP_IN[0]), .Q(JUMP_OUT[0]), .reset(RESET));  // open: Qn, preset, en
endmodule

// I/O Unit
module ports_control (
  input  [7:0] P2_IN,
  input  [19:0] INST_SIGN,
  input  [7:0] RX_SIGN,
  input  [11:0] PC_IN,
  input  [7:0] P1_IN,
  input  [7:0] P0_IN,
  input  FE,
  input  CLK_IN,
  input  [7:0] P3_IN,
  input  [7:0] PX_IN,
  input  INT_STEP1,
  input  [7:0] P6_IN,
  input  [7:0] P7_IN,
  output P1_B0,
  output P1_B1,
  output P1_B2,
  output P1_B3,
  output P1_B4,
  output P1_B5,
  output P1_B6,
  output P1_B7,
  output P0_B0,
  output P0_B1,
  output [7:0] P2_OUT,
  output P0_B2,
  output P0_B3,
  output P0_B4,
  output MEM_EN,
  output P2S,
  output P3S,
  output CLK_OUT,
  output [7:0] P3_OUT,
  output [7:0] EXT_PX,
  output P6S,
  output [7:0] P6_OUT,
  output P7S,
  output [7:0] P7_OUT
);

  wire and_1_out, and_6_out, and_7_out, and_8_out, not_1_out, not_2_out, not_3_out, not_4_out, not_5_out,
       not_6_out, or_1_out, or_3_out;

  or or_1 (or_1_out, INST_SIGN[9], INST_SIGN[8], INT_STEP1);
  not not_1 (not_1_out, or_1_out);
  switcher_12 switcher_12_1 (
    .in_1(not_1_out), .in_2(PC_IN[0]), .in_3(PC_IN[1]), .in_4(PC_IN[2]), .in_5(PC_IN[3]), .in_6(PC_IN[4]),
    .in_7(PC_IN[5]), .in_8(PC_IN[6]), .in_9(PC_IN[7]), .in_10(PC_IN[8]), .in_11(PC_IN[9]), .in_12(PC_IN[10]),
    .in_13(PC_IN[11]), .out_14(P1_B0), .out_15(P1_B1), .out_16(P1_B2), .out_17(P1_B3), .out_18(P1_B4),
    .out_19(P1_B5), .out_20(P1_B6), .out_21(P1_B7), .out_22(P0_B0), .out_23(P0_B1), .out_24(P0_B2),
    .out_25(P0_B3));
  switcher_12 switcher_12_2 (
    .in_1(or_1_out), .in_2(P1_IN[0]), .in_3(P1_IN[1]), .in_4(P1_IN[2]), .in_5(P1_IN[3]), .in_6(P1_IN[4]),
    .in_7(P1_IN[5]), .in_8(P1_IN[6]), .in_9(P1_IN[7]), .in_10(P0_IN[0]), .in_11(P0_IN[1]), .in_12(P0_IN[2]),
    .in_13(P0_IN[3]), .out_14(P1_B0), .out_15(P1_B1), .out_16(P1_B2), .out_17(P1_B3), .out_18(P1_B4),
    .out_19(P1_B5), .out_20(P1_B6), .out_21(P1_B7), .out_22(P0_B0), .out_23(P0_B1), .out_24(P0_B2),
    .out_25(P0_B3));
  assign P0_B4 = not_2_out ? 1'b0 : 1'bz;  // Controlled_Buffer controlled_buffer_1
  not not_2 (not_2_out, or_1_out);
  assign P0_B4 = or_1_out ? P0_IN[4] : 1'bz;  // Controlled_Buffer controlled_buffer_2
  or or_2 (MEM_EN, FE, P0_IN[5]);
  not not_3 (not_3_out, P0_IN[6]);
  and and_1 (and_1_out, P0_IN[5], not_3_out, or_3_out);
  or or_3 (or_3_out, RX_SIGN[2], INT_STEP1);
  switcher switcher_1 (
    .EN(and_1_out), .in_2(P2_IN[7]), .in_3(P2_IN[6]), .in_4(P2_IN[5]), .in_5(P2_IN[4]), .in_6(P2_IN[3]),
    .in_7(P2_IN[2]), .in_8(P2_IN[1]), .in_9(P2_IN[0]), .out_10(EXT_PX[7]), .out_11(EXT_PX[6]),
    .out_12(EXT_PX[5]), .out_13(EXT_PX[4]), .out_14(EXT_PX[3]), .out_15(EXT_PX[2]), .out_16(EXT_PX[1]),
    .out_17(EXT_PX[0]));
  and and_2 (P2S, RX_SIGN[2], P0_IN[6], P0_IN[5]);
  switcher switcher_2 (
    .EN(P2S), .in_2(PX_IN[0]), .in_3(PX_IN[1]), .in_4(PX_IN[2]), .in_5(PX_IN[3]), .in_6(PX_IN[4]),
    .in_7(PX_IN[5]), .in_8(PX_IN[6]), .in_9(PX_IN[7]), .out_10(P2_OUT[0]), .out_11(P2_OUT[1]),
    .out_12(P2_OUT[2]), .out_13(P2_OUT[3]), .out_14(P2_OUT[4]), .out_15(P2_OUT[5]), .out_16(P2_OUT[6]),
    .out_17(P2_OUT[7]));
  not not_4 (not_4_out, P0_IN[7]);
  switcher switcher_3 (
    .EN(and_6_out), .in_2(P3_IN[7]), .in_3(P3_IN[6]), .in_4(P3_IN[5]), .in_5(P3_IN[4]), .in_6(P3_IN[3]),
    .in_7(P3_IN[2]), .in_8(P3_IN[1]), .in_9(P3_IN[0]), .out_10(EXT_PX[7]), .out_11(EXT_PX[6]),
    .out_12(EXT_PX[5]), .out_13(EXT_PX[4]), .out_14(EXT_PX[3]), .out_15(EXT_PX[2]), .out_16(EXT_PX[1]),
    .out_17(EXT_PX[0]));
  switcher switcher_4 (
    .EN(P3S), .in_2(PX_IN[0]), .in_3(PX_IN[1]), .in_4(PX_IN[2]), .in_5(PX_IN[3]), .in_6(PX_IN[4]),
    .in_7(PX_IN[5]), .in_8(PX_IN[6]), .in_9(PX_IN[7]), .out_10(P3_OUT[0]), .out_11(P3_OUT[1]),
    .out_12(P3_OUT[2]), .out_13(P3_OUT[3]), .out_14(P3_OUT[4]), .out_15(P3_OUT[5]), .out_16(P3_OUT[6]),
    .out_17(P3_OUT[7]));
  and and_3 (P3S, RX_SIGN[3], P0_IN[7]);
  not not_5 (not_5_out, P0_IN[6]);
  switcher switcher_5 (
    .EN(and_7_out), .in_2(P6_IN[7]), .in_3(P6_IN[6]), .in_4(P6_IN[5]), .in_5(P6_IN[4]), .in_6(P6_IN[3]),
    .in_7(P6_IN[2]), .in_8(P6_IN[1]), .in_9(P6_IN[0]), .out_10(EXT_PX[7]), .out_11(EXT_PX[6]),
    .out_12(EXT_PX[5]), .out_13(EXT_PX[4]), .out_14(EXT_PX[3]), .out_15(EXT_PX[2]), .out_16(EXT_PX[1]),
    .out_17(EXT_PX[0]));
  and and_4 (P6S, RX_SIGN[6], P0_IN[6]);
  switcher switcher_6 (
    .EN(P6S), .in_2(PX_IN[0]), .in_3(PX_IN[1]), .in_4(PX_IN[2]), .in_5(PX_IN[3]), .in_6(PX_IN[4]),
    .in_7(PX_IN[5]), .in_8(PX_IN[6]), .in_9(PX_IN[7]), .out_10(P6_OUT[0]), .out_11(P6_OUT[1]),
    .out_12(P6_OUT[2]), .out_13(P6_OUT[3]), .out_14(P6_OUT[4]), .out_15(P6_OUT[5]), .out_16(P6_OUT[6]),
    .out_17(P6_OUT[7]));
  not not_6 (not_6_out, P0_IN[7]);
  switcher switcher_7 (
    .EN(and_8_out), .in_2(P7_IN[7]), .in_3(P7_IN[6]), .in_4(P7_IN[5]), .in_5(P7_IN[4]), .in_6(P7_IN[3]),
    .in_7(P7_IN[2]), .in_8(P7_IN[1]), .in_9(P7_IN[0]), .out_10(EXT_PX[7]), .out_11(EXT_PX[6]),
    .out_12(EXT_PX[5]), .out_13(EXT_PX[4]), .out_14(EXT_PX[3]), .out_15(EXT_PX[2]), .out_16(EXT_PX[1]),
    .out_17(EXT_PX[0]));
  switcher switcher_8 (
    .EN(P7S), .in_2(PX_IN[0]), .in_3(PX_IN[1]), .in_4(PX_IN[2]), .in_5(PX_IN[3]), .in_6(PX_IN[4]),
    .in_7(PX_IN[5]), .in_8(PX_IN[6]), .in_9(PX_IN[7]), .out_10(P7_OUT[0]), .out_11(P7_OUT[1]),
    .out_12(P7_OUT[2]), .out_13(P7_OUT[3]), .out_14(P7_OUT[4]), .out_15(P7_OUT[5]), .out_16(P7_OUT[6]),
    .out_17(P7_OUT[7]));
  and and_5 (P7S, RX_SIGN[7], P0_IN[7]);
  and and_6 (and_6_out, not_4_out, RX_SIGN[3]);
  and and_7 (and_7_out, not_5_out, RX_SIGN[6]);
  and and_8 (and_8_out, not_6_out, RX_SIGN[7]);

  assign CLK_OUT = CLK_IN;

  // Notes on the sheet:
  //   P0 PORT
  //   P1 PORT
  //   P0<6>
  //   P0<7>
  //   P2 PORT
  //   P3 PORT
  //   P6 PORT
  //   P7 PORT
endmodule

// WR80
module WR80_Arch (
  input  VDD,
  input  RS,
  input  ON,
  input  CLK_EXT,
  input  CLKIN_EN,
  input  OVER_EN,
  input  DBG_ON,
  input  STEP_IN,
  input  I0,
  input  I1,
  input  I2,
  input  I3,
  input  [7:0] P2_IN,
  input  [7:0] P3_IN,
  input  [7:0] P6_IN,
  input  [7:0] P7_IN,
  output CLEAR,
  output CLK_OUT,
  output P3S,
  output P2S,
  output MEM_EN,
  output ROM_ACCESS,
  output [11:0] P0_P1,
  output [7:0] P2_OUT,
  output [7:0] P3_OUT,
  output [15:0] P4_P5,
  output [7:0] P6_OUT,
  output [7:0] P7_OUT,
  output P6S,
  output P7S,
  output IN_ACC
);

  wire control_unit_1_call, control_unit_1_clk_out, control_unit_1_clr, control_unit_1_ex, control_unit_1_fe,
       control_unit_1_int_step1, control_unit_1_ints_clk, control_unit_1_ints_out, control_unit_1_jump_high,
       control_unit_1_jump_low, control_unit_1_sbit, control_unit_1_sr_sig, control_unit_1_wr, or_1_out,
       register_bank_1_carry, register_bank_1_zero, rw_controller_1_control_w, rw_controller_1_data_w,
       rw_controller_1_dr_h, rw_controller_1_dr_l, rw_controller_1_gpr_w, rw_controller_1_idc_w,
       rw_controller_1_inc_w, rw_controller_1_p2_w, rw_controller_1_p3_w, rw_controller_1_pc_w,
       rw_controller_1_px_r, rw_controller_1_px_w, rw_controller_1_ram_rw, rw_controller_1_sr_c,
       rw_controller_1_sr_z;
  wire [1:0] register_bank_1_idc_sel;
  wire [2:0] control_unit_1_extbits2;
  wire [3:0] alu_1_status_bit, control_unit_1_sr_out, register_bank_1_p0_out_2, register_bank_1_sr_out;
  wire [7:0] alu_1_rx_out, control_unit_1_ir_out, control_unit_1_reg_out, ports_control_1_ext_px,
       register_bank_1_dr_out, register_bank_1_p1_out, register_bank_1_px_out, register_bank_1_rx_out;
  wire [11:0] alu_1_alu_out, control_unit_1_dr_out, control_unit_1_intr_out, control_unit_1_pc_out,
       jump_register_1_jump_out;
  wire [11:8] register_bank_1_p0_out;
  wire [19:0] control_unit_1_inst_out;
  wire [25:0] control_unit_1_extbits;

  or or_1 (or_1_out, RS, ON);
  ports_control ports_control_1 (
    .INST_SIGN(control_unit_1_inst_out), .RX_SIGN(control_unit_1_reg_out), .PC_IN(control_unit_1_pc_out),
    .P1_IN(register_bank_1_p1_out), .P0_IN({register_bank_1_p0_out_2, register_bank_1_p0_out}),
    .FE(control_unit_1_fe), .CLK_IN(control_unit_1_clk_out), .P1_B0(P0_P1[0]), .P1_B1(P0_P1[1]),
    .P1_B2(P0_P1[2]), .P1_B3(P0_P1[3]), .P2_IN(P2_IN), .P1_B4(P0_P1[4]), .P1_B5(P0_P1[5]), .P1_B6(P0_P1[6]),
    .P1_B7(P0_P1[7]), .P0_B0(P0_P1[8]), .P0_B1(P0_P1[9]), .P2_OUT(P2_OUT), .P0_B2(P0_P1[10]),
    .P0_B3(P0_P1[11]), .P0_B4(ROM_ACCESS), .MEM_EN(MEM_EN), .P2S(P2S), .P3S(P3S), .CLK_OUT(CLK_OUT),
    .P3_IN(P3_IN), .P3_OUT(P3_OUT), .EXT_PX(ports_control_1_ext_px), .PX_IN(register_bank_1_px_out),
    .INT_STEP1(control_unit_1_int_step1), .P6_IN(P6_IN), .P6_OUT(P6_OUT), .P7_IN(P7_IN), .P7_OUT(P7_OUT),
    .P6S(P6S), .P7S(P7S));
  control_unit control_unit_1 (
    .RS(or_1_out), .ON(ON), .CLK_EXT(CLK_EXT), .CLKIN_EN(CLKIN_EN), .OVER_EN(OVER_EN), .PC_IN(alu_1_alu_out),
    .IR_IN(P2_IN), .INST_OUT(control_unit_1_inst_out), .REG_OUT(control_unit_1_reg_out),
    .JUMP_LOW(control_unit_1_jump_low), .JUMP_HIGH(control_unit_1_jump_high),
    .CLK_OUT(control_unit_1_clk_out), .FE(control_unit_1_fe), .EX(control_unit_1_ex), .WR(control_unit_1_wr),
    .PC_OUT(control_unit_1_pc_out), .PC_W(rw_controller_1_pc_w), .IR_OUT(control_unit_1_ir_out),
    .DBG(DBG_ON), .STEP(STEP_IN), .I3(I3), .I2(I2), .I1(I1), .I0(I0), .VDD(VDD),
    .INTR({register_bank_1_p0_out, register_bank_1_p1_out}), .ExtBits(control_unit_1_extbits),
    .INTR_OUT(control_unit_1_intr_out), .INTS_OUT(control_unit_1_ints_out),
    .INTS_CLK(control_unit_1_ints_clk), .INT_STEP1(control_unit_1_int_step1),
    .P2_INPUT(register_bank_1_px_out), .SR_IN(register_bank_1_sr_out), .SR_OUT(control_unit_1_sr_out),
    .SR_SIG(control_unit_1_sr_sig), .DR_IN(register_bank_1_dr_out), .DR_OUT(control_unit_1_dr_out),
    .CALL(control_unit_1_call), .SBIT(control_unit_1_sbit), .RX_IN(register_bank_1_rx_out),
    .CLR(control_unit_1_clr), .ExtBits2(control_unit_1_extbits2));
  or or_2 (CLEAR, or_1_out, control_unit_1_clr);
  rw_controller rw_controller_1 (
    .CARRY(register_bank_1_carry), .ZERO(register_bank_1_zero), .WRITE(control_unit_1_wr),
    .INST_IN(control_unit_1_inst_out), .PC_W(rw_controller_1_pc_w), .DR_H(rw_controller_1_dr_h),
    .DR_L(rw_controller_1_dr_l), .SR_C(rw_controller_1_sr_c), .SR_Z(rw_controller_1_sr_z),
    .GPR_W(rw_controller_1_gpr_w), .PX_SIGN(control_unit_1_reg_out), .EXEC(control_unit_1_ex),
    .CLK_IN(control_unit_1_clk_out), .CONTROL_W(rw_controller_1_control_w), .P3_W(rw_controller_1_p3_w),
    .P2_W(rw_controller_1_p2_w), .PX_W(rw_controller_1_px_w), .PX_R(rw_controller_1_px_r),
    .RAM_RW(rw_controller_1_ram_rw), .DATA_W(rw_controller_1_data_w), .ExtBits(control_unit_1_extbits),
    .ExtBits2(control_unit_1_extbits2), .IDC_W(rw_controller_1_idc_w), .INC_W(rw_controller_1_inc_w));
  jump_register jump_register_1 (
    .JUMP_HIGH(control_unit_1_jump_high), .JUMP_LOW(control_unit_1_jump_low), .RESET(or_1_out),
    .JUMP_IN(control_unit_1_ir_out), .JUMP_OUT(jump_register_1_jump_out), .CALL(control_unit_1_call),
    .SBIT(control_unit_1_sbit));
  ALU alu_1 (
    .EX(control_unit_1_ex), .WR(control_unit_1_wr), .INST_IN(control_unit_1_inst_out),
    .DR_IN(register_bank_1_dr_out), .RX_IN(register_bank_1_rx_out), .IR_IN(control_unit_1_ir_out),
    .PX_IN(register_bank_1_px_out), .PC_IN(control_unit_1_pc_out), .JMP_IN(jump_register_1_jump_out),
    .ALU_OUT(alu_1_alu_out), .STATUS_BIT(alu_1_status_bit), .EXT_BITS(control_unit_1_extbits),
    .RX_OUT(alu_1_rx_out), .EXT_BITS2(control_unit_1_extbits2), .IDC_SEL(register_bank_1_idc_sel),
    .CLOCK(control_unit_1_clk_out));
  register_bank register_bank_1 (
    .DR_H(rw_controller_1_dr_h), .DR_L(rw_controller_1_dr_l), .RS(or_1_out), .SR_C(rw_controller_1_sr_c),
    .SR_Z(rw_controller_1_sr_z), .GPR_R(control_unit_1_ex), .GPR_W(rw_controller_1_gpr_w),
    .REG_DATA(alu_1_alu_out), .SR_DATA(alu_1_status_bit), .DR_OUT(register_bank_1_dr_out),
    .RX_OUT(register_bank_1_rx_out), .CARRY(register_bank_1_carry), .ZERO(register_bank_1_zero),
    .RX_SIGN(control_unit_1_reg_out), .CONTROL_W(rw_controller_1_control_w), .PX_W(rw_controller_1_px_w),
    .PX_R(rw_controller_1_px_r), .RAM_RW(rw_controller_1_ram_rw), .P2_W(rw_controller_1_p2_w),
    .P3_W(rw_controller_1_p3_w), .IR_IN(control_unit_1_ir_out), .INT_PXIN(alu_1_alu_out),
    .EXT_PXIN(ports_control_1_ext_px), .P0_OUT({register_bank_1_p0_out_2, register_bank_1_p0_out}),
    .P1_OUT(register_bank_1_p1_out), .PX_OUT(register_bank_1_px_out), .OUT_INT(rw_controller_1_data_w),
    .PS_C(control_unit_1_fe), .ExtBits(control_unit_1_extbits), .INTR_IN(control_unit_1_intr_out),
    .INTS_IN(control_unit_1_ints_out), .INTS_CLK(control_unit_1_ints_clk),
    .INT_STEP1(control_unit_1_int_step1), .SR_OUT(register_bank_1_sr_out), .SR_IN(control_unit_1_sr_out),
    .SR_W(control_unit_1_sr_sig), .DR_IN(control_unit_1_dr_out), .P4_OUT(P4_P5[15:8]), .P5_OUT(P4_P5[7:0]),
    .ASSYNC_RX_IN(alu_1_rx_out), .ExtBits2(control_unit_1_extbits2), .IDC_W(rw_controller_1_idc_w),
    .IDC_SEL(register_bank_1_idc_sel), .INC_W(rw_controller_1_inc_w), .CLOCK(control_unit_1_clk_out));
  and and_1 (IN_ACC, control_unit_1_reg_out[3], control_unit_1_inst_out[8], control_unit_1_wr);
endmodule

// RAM Controller
module RAM_Controller (
  input  ROM_ACC,
  input  MEM_EN,
  input  P2S,
  input  D7,
  input  D6,
  input  D5,
  input  D4,
  input  D3,
  input  D2,
  input  D1,
  input  D0,
  output ROM_SEL_LD,
  output RAM_SEL_LD,
  output RAM_STR,
  output O7,
  output O6,
  output O5,
  output O4,
  output O3,
  output O2,
  output O1,
  output O0
);

  wire and_3_out, not_1_out, not_2_out;

  not not_1 (not_1_out, ROM_ACC);
  not not_2 (not_2_out, P2S);
  and and_1 (ROM_SEL_LD, MEM_EN, ROM_ACC);
  and and_2 (RAM_SEL_LD, not_1_out, MEM_EN);
  and and_3 (and_3_out, not_2_out, MEM_EN);
  and and_4 (RAM_STR, not_1_out, MEM_EN, P2S);
  switcher switcher_1 (
    .EN(and_3_out), .in_2(D7), .in_3(D6), .in_4(D5), .in_5(D4), .in_6(D3), .in_7(D2), .in_8(D1), .in_9(D0),
    .out_10(O7), .out_11(O6), .out_12(O5), .out_13(O4), .out_14(O3), .out_15(O2), .out_16(O1), .out_17(O0));
endmodule

// separator
module mux_switcher (
  input  ON,
  input  ADDR,
  input  [3:0] DATA1,
  input  [7:0] DATA2,
  output b7,
  output b6,
  output b5,
  output b4,
  output b3,
  output b2,
  output b1,
  output b0
);

  wire [7:0] bit_extender_1_out;

  assign bit_extender_1_out = {{4{1'b0}}, DATA1};  // Bit_Extender bit_extender_1
  Multiplexer multiplexer_1 (.in0(bit_extender_1_out[7]), .in1(DATA2[7]), .out(b7), .sel(ADDR), .en(ON));
  Multiplexer multiplexer_2 (.in0(bit_extender_1_out[6]), .in1(DATA2[6]), .out(b6), .sel(ADDR), .en(ON));
  Multiplexer multiplexer_3 (.in0(bit_extender_1_out[5]), .in1(DATA2[5]), .out(b5), .sel(ADDR), .en(ON));
  Multiplexer multiplexer_4 (.in0(bit_extender_1_out[4]), .in1(DATA2[4]), .out(b4), .sel(ADDR), .en(ON));
  Multiplexer multiplexer_5 (.in0(bit_extender_1_out[3]), .in1(DATA2[3]), .out(b3), .sel(ADDR), .en(ON));
  Multiplexer multiplexer_6 (.in0(bit_extender_1_out[2]), .in1(DATA2[2]), .out(b2), .sel(ADDR), .en(ON));
  Multiplexer multiplexer_7 (.in0(bit_extender_1_out[1]), .in1(DATA2[1]), .out(b1), .sel(ADDR), .en(ON));
  Multiplexer multiplexer_8 (.in0(bit_extender_1_out[0]), .in1(DATA2[0]), .out(b0), .sel(ADDR), .en(ON));
endmodule

// Interrupt CI
module interrupt_circuit (
  input  CLK,
  input  FE,
  input  JUMP,
  input  INTS,
  input  INTE,
  input  I3,
  input  I2,
  input  I1,
  input  I0,
  input  [11:0] P0_P1,
  input  [7:0] P2,
  input  DI,
  output PC_LOCK,
  output PC_WRITE,
  output INTS_OUT,
  output INTS_CLK,
  output INT_STEP1,
  output [11:0] INTR_OUT,
  output [11:0] ADDR_OUT,
  output SIGN1,
  output SIGN2
);

  wire and_1_out, and_2_out, and_3_out, and_4_out, and_5_out, and_6_out, and_7_out, and_8_out, and_9_out,
       and_10_out, and_11_out, and_12_out, and_13_out, and_14_out, and_15_out, and_16_out, and_17_out,
       and_18_out, and_21_out, d_ff_1_q, d_ff_2_q, d_ff_3_q, d_ff_4_q, d_ff_5_q, d_ff_6_q, d_ff_7_q,
       d_ff_8_q, d_ff_10_q, d_ff_11_q, DI_q, EI_q, not_1_out, not_2_out, not_3_out, not_4_out, not_5_out,
       not_6_out, not_7_out, not_8_out, not_9_out, not_10_out, not_11_out, not_12_out, not_14_out, or_1_out,
       or_2_out, or_3_out, or_4_out, or_5_out, or_6_out, or_7_out, or_8_out;
  wire [2:0] multiplexer_3_out;
  wire [7:0] register_2_q;
  wire [7:4] register_4_q;
  wire [11:0] adder_1_out, bit_extender_1_out, controlled_buffer_1_out, register_1_q, register_3_q;

  not not_1 (not_1_out, CLK);
  D_Flip_Flop d_ff_1 (.clk(CLK), .D(FE), .Q(d_ff_1_q), .reset(d_ff_7_q));  // open: Qn, preset, en
  not not_2 (not_2_out, JUMP);
  not not_3 (not_3_out, d_ff_11_q);
  or or_1 (or_1_out, INTS, and_3_out, and_1_out);
  and and_1 (and_1_out, CLK, d_ff_7_q);
  and and_2 (and_2_out, and_13_out, CLK);
  and and_3 (and_3_out, d_ff_11_q, not_1_out);
  and and_4 (and_4_out, d_ff_1_q, FE);
  and and_5 (and_5_out, INTE, I3);
  and and_6 (and_6_out, INTE, I2);
  and and_7 (and_7_out, INTE, I1);
  and and_8 (and_8_out, INTE, I0);
  assign controlled_buffer_1_out = not_3_out ? P0_P1 : 12'bz;  // Controlled_Buffer controlled_buffer_1
  Register #(.width(12)) register_1 (.D(controlled_buffer_1_out), .Q(register_1_q), .clk(and_9_out));  // open: en, clr
  assign controlled_buffer_1_out = d_ff_11_q ? register_3_q : 12'bz;  // Controlled_Buffer controlled_buffer_2
  and and_9 (and_9_out, EI_q, or_1_out);
  D_Flip_Flop #(.trigger("falling")) d_ff_2 (
    .clk(and_2_out), .D(and_13_out), .Q(d_ff_2_q));  // open: Qn, preset, en, reset
  Register #(.trigger("falling")) register_2 (.D(P2), .Q(register_2_q), .clk(INT_STEP1), .clr(d_ff_10_q));  // open: en
  D_Flip_Flop EI (.Q(EI_q), .preset(and_10_out), .reset(DI));  // open: clk, D, Qn, en
  and and_10 (and_10_out, INTS, not_4_out);
  and and_11 (and_11_out, or_2_out, and_4_out);
  D_Flip_Flop d_ff_3 (.clk(and_5_out), .D(INTE), .Q(d_ff_3_q), .reset(d_ff_7_q));  // open: Qn, preset, en
  D_Flip_Flop d_ff_4 (.clk(and_6_out), .D(INTE), .Q(d_ff_4_q), .reset(d_ff_7_q));  // open: Qn, preset, en
  D_Flip_Flop d_ff_5 (.clk(and_7_out), .D(INTE), .Q(d_ff_5_q), .reset(d_ff_7_q));  // open: Qn, preset, en
  D_Flip_Flop d_ff_6 (.clk(and_8_out), .D(INTE), .Q(d_ff_6_q), .reset(d_ff_7_q));  // open: Qn, preset, en
  Register #(.width(12), .trigger("falling")) register_3 (
    .D(register_1_q), .Q(register_3_q), .clk(INTS));  // open: en, clr
  assign bit_extender_1_out = {{9{1'b0}}, multiplexer_3_out};  // Bit_Extender bit_extender_1
  D_Flip_Flop d_ff_7 (.clk(CLK), .D(d_ff_2_q), .Q(d_ff_7_q));  // open: Qn, preset, en, reset
  Register register_4 (.D(register_2_q), .Q({register_4_q, ADDR_OUT[11:8]}), .clk(INT_STEP1));  // open: en, clr
  not not_4 (not_4_out, DI_q);
  D_Flip_Flop #(.trigger("falling")) u_DI (.clk(INTS), .D(EI_q), .Q(DI_q));  // open: Qn, preset, en, reset
  D_Flip_Flop d_ff_8 (.clk(and_11_out), .D(and_4_out), .Q(d_ff_8_q), .reset(d_ff_7_q));  // open: Qn, preset, en
  or or_2 (or_2_out, d_ff_3_q, d_ff_4_q, d_ff_5_q, d_ff_6_q);
  Adder #(.width(12)) adder_1 (.a(register_1_q), .b(bit_extender_1_out), .out(adder_1_out), .cin(1'b0));  // open: cout
  D_Flip_Flop #(.trigger("falling")) d_ff_9 (.clk(CLK), .D(d_ff_7_q), .Q(SIGN1));  // open: Qn, preset, en, reset
  and and_12 (and_12_out, SIGN1, CLK);
  Register register_5 (.D({register_4_q, ADDR_OUT[11:8]}), .Q(ADDR_OUT[7:0]), .clk(INT_STEP1));  // open: en, clr
  and and_13 (and_13_out, INTE, d_ff_8_q, not_2_out, or_2_out);
  assign INTR_OUT = d_ff_10_q ? register_3_q : 12'bz;  // Controlled_Buffer controlled_buffer_3
  assign INTR_OUT = not_5_out ? adder_1_out : 12'bz;  // Controlled_Buffer controlled_buffer_4
  not not_5 (not_5_out, d_ff_10_q);
  or or_3 (or_3_out, SIGN1, d_ff_11_q, d_ff_10_q);
  D_Flip_Flop #(.trigger("falling")) d_ff_10 (
    .clk(and_12_out), .D(SIGN1), .Q(d_ff_10_q), .reset(d_ff_11_q));  // open: Qn, preset, en
  or or_4 (or_4_out, and_13_out, or_3_out);
  or or_5 (or_5_out, d_ff_3_q, d_ff_5_q);
  or or_6 (or_6_out, d_ff_3_q, d_ff_4_q);
  not not_6 (not_6_out, d_ff_3_q);
  not not_7 (not_7_out, d_ff_4_q);
  not not_8 (not_8_out, d_ff_5_q);
  not not_9 (not_9_out, d_ff_6_q);
  Multiplexer multiplexer_1 (.in0(and_16_out), .in1(and_15_out), .out(multiplexer_3_out[1]), .sel(1'b1));  // open: en
  Multiplexer multiplexer_2 (.in0(and_17_out), .in1(and_16_out), .out(multiplexer_3_out[2]), .sel(1'b1));  // open: en
  not not_10 (not_10_out, SIGN1);
  and and_14 (and_14_out, not_10_out, not_12_out, or_7_out);
  or or_7 (or_7_out, and_13_out, d_ff_7_q);
  or or_8 (or_8_out, d_ff_2_q, SIGN1);
  not not_11 (not_11_out, CLK);
  not not_12 (not_12_out, INT_STEP1);
  not not_13 (PC_LOCK, or_4_out);
  and and_15 (and_15_out, not_7_out, or_5_out, not_9_out);
  and and_16 (and_16_out, or_6_out, not_8_out, not_9_out);
  and and_17 (and_17_out, not_6_out, not_7_out, not_8_out, not_9_out);
  Multiplexer multiplexer_3 (.in0(and_15_out), .in1(and_17_out), .out(multiplexer_3_out[0]), .sel(1'b1));  // open: en
  not not_14 (not_14_out, CLK);
  and and_18 (and_18_out, CLK, and_14_out);
  and and_19 (INT_STEP1, or_8_out, not_11_out);
  and and_20 (PC_WRITE, not_14_out, d_ff_10_q);
  or or_9 (INTS_OUT, and_14_out, d_ff_10_q);
  or or_10 (INTS_CLK, and_18_out, and_21_out);
  and and_21 (and_21_out, CLK, d_ff_10_q);
  D_Flip_Flop #(.trigger("falling")) d_ff_11 (
    .clk(not_11_out), .D(d_ff_10_q), .Q(d_ff_11_q));  // open: Qn, preset, en, reset
  or or_11 (SIGN2, d_ff_10_q, d_ff_11_q);
endmodule

// Stack Circuit
module stack_circuit (
  input  [11:0] PC_IN,
  input  [3:0] SR_IN,
  input  WRITE,
  input  SYNC_1,
  input  EI_CLK,
  input  ON,
  input  SYNC_2,
  input  CLK,
  input  EX,
  input  WR,
  input  IRET,
  input  PUSHB,
  input  POPB,
  input  PUSHS,
  input  POPS,
  input  SBP,
  input  ABP,
  input  SSP,
  input  PUSHD,
  input  POPD,
  input  PUSH,
  input  POP,
  input  SBW,
  input  [7:0] DR_IN,
  input  CALL,
  input  [7:0] RX_IN,
  input  RET,
  output [11:0] PC_OUT,
  output [3:0] SR_OUT,
  output SR_W
);

  wire and_1_out, and_2_out, and_3_out, and_4_out, and_5_out, and_6_out, and_7_out, and_8_out, and_9_out,
       buffer_1_out, buffer_2_out, buffer_3_out, buffer_4_out, buffer_5_out, CALL_2_out, CALL_4_out,
       CALL_out, d_ff_1_q, delay_1_out, delay_2_out, delay_3_out, delay_4_out, delay_5_out, delay_6_out,
       iret_2_out, iret_3_out, iret_out, nor_1_out, nor_2_out, nor_3_out, nor_4_out, not_1_out, not_2_out,
       not_3_out, not_4_out, not_5_out, not_6_out, not_7_out, not_8_out, not_9_out, not_10_out, not_11_out,
       not_12_out, not_13_out, or_1_out, or_2_out, or_3_out, or_4_out, or_5_out, or_6_out, or_7_out,
       or_8_out, or_9_out, or_10_out, or_11_out, or_12_out, or_13_out, or_14_out, or_15_out, or_16_out,
       or_17_out, or_18_out, or_19_out, or_20_out, or_21_out, or_22_out, or_23_out, or_24_out, or_25_out,
       or_26_out, or_27_out, or_28_out, or_29_out, or_30_out, or_31_out, or_32_out, or_33_out, or_34_out,
       or_35_out, or_36_out, or_37_out, or_38_out, or_39_out, or_40_out, or_41_out, or_42_out, or_43_out,
       or_44_out, or_45_out, or_46_out, or_47_out, or_48_out, pop_2_out, pop_3_out, pop_4_out, pop_out,
       pops_2_out, pops_3_out, pops_4_out, pops_out, pshs_2_out, pshs_3_out, pshs_4_out, pshs_out,
       push_2_out, push_3_out, push_4_out, push_out, sbw_2_out, sbw_out, sp_sync_1_out;
  wire [3:0] adder_3_out_2, BP_q_2, controlled_buffer_3_out;
  wire [7:0] adder_3_out, BP_q, controlled_buffer_5_out, controlled_buffer_10_out, controlled_buffer_18_out,
       controlled_buffer_26_out, ram_1_data, register_1_q;
  wire [11:0] adder_1_out, adder_2_out, adder_4_out, bit_extender_1_out, controlled_buffer_1_out,
       controlled_buffer_14_out, controlled_buffer_16_out, controlled_buffer_20_out,
       controlled_buffer_23_out, SP_q, subtractor_1_out, subtractor_2_out;

  or or_1 (or_1_out, CALL_4_out, not_2_out);
  or or_2 (or_2_out, SBW, PUSH);
  assign controlled_buffer_1_out = not_1_out ? {12{1'b0}} : 12'bz;  // Controlled_Buffer controlled_buffer_1
  not not_1 (not_1_out, CALL);
  assign controlled_buffer_1_out = CALL ? 12'h1 : 12'bz;  // Controlled_Buffer controlled_buffer_2
  D_Flip_Flop d_ff_1 (.clk(or_1_out), .D(CALL_4_out), .Q(d_ff_1_q));  // open: Qn, preset, en, reset
  not not_2 (not_2_out, CLK);
  or or_3 (or_3_out, delay_3_out, WRITE);
  or or_4 (or_4_out, CALL_4_out, d_ff_1_q, SYNC_1);
  or or_5 (or_5_out, or_25_out, EI_CLK);
  or or_6 (or_6_out, or_7_out, or_10_out, or_11_out);
  or or_7 (or_7_out, SBP, ABP, SSP);
  or or_8 (or_8_out, delay_4_out, or_7_out, delay_1_out);
  or or_9 (or_9_out, PUSHD, PUSH);
  or or_10 (or_10_out, POPD, POP);
  or or_11 (or_11_out, SBW, PUSHD, PUSH);
  Adder #(.width(12)) adder_1 (.a(PC_IN), .b(controlled_buffer_1_out), .out(adder_1_out));  // open: cin, cout
  assign controlled_buffer_3_out = not_3_out ? SR_IN : 4'bz;  // Controlled_Buffer controlled_buffer_3
  not not_3 (not_3_out, CALL);
  assign controlled_buffer_3_out = CALL ? 4'b0000 : 4'bz;  // Controlled_Buffer controlled_buffer_4
  and and_1 (and_1_out, nor_2_out, nor_1_out);
  nor nor_1 (nor_1_out, or_5_out, CALL, or_13_out);
  or or_12 (or_12_out, or_7_out, or_10_out, POPB);
  or or_13 (or_13_out, RET, IRET);
  or or_14 (or_14_out, pops_3_out, pop_3_out);
  or or_15 (or_15_out, iret_out, or_23_out, or_5_out, or_8_out);
  or or_16 (or_16_out, iret_3_out, or_23_out, or_5_out, or_14_out);
  and and_2 (and_2_out, EX, or_13_out);
  and and_3 (and_3_out, WR, or_13_out);
  nor nor_2 (nor_2_out, PUSHS, PUSHB, or_6_out, POPB, POPS);
  buf buffer_1 (buffer_1_out, PUSHB);
  or or_17 (or_17_out, buffer_1_out, or_9_out);
  or or_18 (or_18_out, PUSHS, SSP, or_17_out);
  or or_19 (or_19_out, POPS, or_10_out, POPB);
  buf buffer_2 (buffer_2_out, PUSHS);
  buf buffer_3 (buffer_3_out, POPS);
  or or_20 (or_20_out, POPB, or_10_out);
  and and_4 (and_4_out, nor_2_out, not_4_out);
  not not_4 (not_4_out, and_2_out);
  or or_21 (or_21_out, and_2_out, POPS, or_12_out);
  and and_5 (and_5_out, nor_2_out, not_5_out);
  not not_5 (not_5_out, and_3_out);
  or or_22 (or_22_out, and_3_out, POPS, or_12_out);
  buf buffer_4 (buffer_4_out, buffer_5_out);
  buf buffer_5 (buffer_5_out, or_15_out);
  or or_23 (or_23_out, delay_6_out, or_31_out, push_out);
  not not_6 (not_6_out, CLK);
  assign controlled_buffer_5_out = and_4_out ? adder_1_out[7:0] : 8'bz;  // Controlled_Buffer controlled_buffer_5
  assign controlled_buffer_5_out = or_21_out ? ram_1_data : 8'bz;  // Controlled_Buffer controlled_buffer_6
  assign controlled_buffer_5_out = PUSHB ? BP_q : 8'bz;  // Controlled_Buffer controlled_buffer_7
  assign controlled_buffer_5_out = PUSHS ? adder_3_out : 8'bz;  // Controlled_Buffer controlled_buffer_8
  assign controlled_buffer_5_out = or_11_out ? controlled_buffer_26_out : 8'bz;  // Controlled_Buffer controlled_buffer_9
  assign controlled_buffer_10_out = and_5_out ? {controlled_buffer_3_out, adder_1_out[11:8]} : 8'bz;  // Controlled_Buffer controlled_buffer_10
  assign controlled_buffer_10_out = or_22_out ? ram_1_data : 8'bz;  // Controlled_Buffer controlled_buffer_11
  assign controlled_buffer_10_out = PUSHB ? {4'b0000, BP_q_2} : 8'bz;  // Controlled_Buffer controlled_buffer_12
  assign controlled_buffer_10_out = PUSHS ? {4'b0000, adder_3_out_2} : 8'bz;  // Controlled_Buffer controlled_buffer_13
  and u_iret (iret_out, not_6_out, or_13_out, EX);
  and iret_2 (iret_2_out, CLK, or_13_out, WR);
  and iret_3 (iret_3_out, not_6_out, or_13_out, WR);
  and u_push (push_out, CLK, EX, buffer_1_out);
  and push_2 (push_2_out, not_6_out, EX, buffer_1_out);
  and push_3 (push_3_out, CLK, WR, or_17_out);
  or or_24 (or_24_out, push_2_out, or_32_out);
  and push_4 (push_4_out, not_6_out, WR, or_17_out);
  delay delay_1 (.Delay(pop_out), .Clear(or_38_out), .OUT(delay_1_out));
  and u_pop (pop_out, CLK, EX, or_20_out);
  and pop_2 (pop_2_out, not_6_out, EX, or_20_out);
  and pop_3 (pop_3_out, CLK, WR, POPB);
  and pop_4 (pop_4_out, not_6_out, WR, POPB);
  and u_CALL (CALL_out, EX, CLK, CALL);
  and CALL_2 (CALL_2_out, EX, not_6_out, CALL);
  buf or_25 (or_25_out, CALL_out);  // OR_Gate
  // AND_Gate CALL_3 has open pins: in0=WR, in1=CLK, in2=CALL, out=open
  or or_26 (or_26_out, CALL_2_out, CALL_4_out);
  and CALL_4 (CALL_4_out, WR, not_6_out, CALL);
  Register STLR (.D(controlled_buffer_5_out), .Q(PC_OUT[7:0]), .clk(delay_2_out));  // open: en, clr
  delay delay_2 (.Delay(buffer_4_out), .Clear(and_1_out), .OUT(delay_2_out));
  Register STHR (.D(controlled_buffer_10_out), .Q({SR_OUT, PC_OUT[11:8]}), .clk(or_16_out));  // open: en, clr
  and and_6 (and_6_out, nor_2_out, not_7_out);
  not not_7 (not_7_out, or_4_out);
  or or_27 (or_27_out, or_5_out, or_18_out);
  assign controlled_buffer_14_out = delay_5_out ? PC_OUT : 12'bz;  // Controlled_Buffer controlled_buffer_14
  assign controlled_buffer_14_out = ON ? {12{1'b1}} : 12'bz;  // Controlled_Buffer controlled_buffer_15
  assign controlled_buffer_16_out = pop_4_out ? PC_OUT : 12'bz;  // Controlled_Buffer controlled_buffer_16
  assign controlled_buffer_16_out = ON ? {12{1'b1}} : 12'bz;  // Controlled_Buffer controlled_buffer_17
  or or_28 (or_28_out, or_5_out, ON, or_29_out, or_30_out);
  or or_29 (or_29_out, iret_2_out, iret_3_out);
  or or_30 (or_30_out, or_43_out, push_out, push_3_out, or_33_out);
  or or_31 (or_31_out, push_3_out, sbw_out);
  and u_sbw (sbw_out, CLK, WR, or_11_out);
  or or_32 (or_32_out, push_4_out, sbw_2_out);
  and sbw_2 (sbw_2_out, not_6_out, WR, or_11_out);
  or or_33 (or_33_out, pop_2_out, pop_4_out);
  delay delay_3 (.Delay(or_26_out), .Clear(CLK), .OUT(delay_3_out));
  or or_34 (or_34_out, or_37_out, or_4_out);
  assign controlled_buffer_18_out = or_35_out ? {SR_OUT, PC_OUT[11:8]} : 8'bz;  // Controlled_Buffer controlled_buffer_18
  or or_35 (or_35_out, or_36_out, and_6_out);
  Register #(.width(12)) SP (.D(controlled_buffer_14_out), .Q(SP_q), .clk(sp_sync_1_out));  // open: en, clr
  sp_sync sp_sync_1 (
    .OR(or_28_out), .SUB(and_9_out), .ADD(or_27_out), .OUT(sp_sync_1_out), .ON(ON), .POPS(delay_5_out),
    .WR(WR), .SSP(SSP));
  or or_36 (or_36_out, push_2_out, pshs_2_out);
  or or_37 (or_37_out, or_32_out, pshs_4_out);
  buf or_38 (or_38_out, or_33_out);  // OR_Gate
  assign controlled_buffer_18_out = or_34_out ? PC_OUT[7:0] : 8'bz;  // Controlled_Buffer controlled_buffer_19
  or or_39 (or_39_out, or_34_out, or_35_out);
  assign controlled_buffer_20_out = SSP ? bit_extender_1_out : 12'bz;  // Controlled_Buffer controlled_buffer_20
  assign controlled_buffer_20_out = nor_3_out ? 12'h1 : 12'bz;  // Controlled_Buffer controlled_buffer_21
  assign controlled_buffer_20_out = or_40_out ? {12{1'b0}} : 12'bz;  // Controlled_Buffer controlled_buffer_22
  or or_40 (or_40_out, or_37_out, SYNC_2);
  assign controlled_buffer_23_out = nor_4_out ? SP_q : 12'bz;  // Controlled_Buffer controlled_buffer_23
  Register #(.width(12)) BP (.D(controlled_buffer_16_out), .Q({BP_q_2, BP_q}), .clk(or_41_out));  // open: en, clr
  or or_41 (or_41_out, or_28_out, pop_4_out);
  and pshs (pshs_out, CLK, EX, buffer_2_out);
  and pshs_2 (pshs_2_out, not_6_out, EX, buffer_2_out);
  and pshs_3 (pshs_3_out, CLK, WR, buffer_2_out);
  and pshs_4 (pshs_4_out, not_6_out, WR, buffer_2_out);
  and u_pops (pops_out, CLK, EX, buffer_3_out);
  and pops_2 (pops_2_out, not_6_out, EX, buffer_3_out);
  and pops_3 (pops_3_out, CLK, WR, buffer_3_out);
  and pops_4 (pops_4_out, not_6_out, WR, buffer_3_out);
  not not_8 (not_8_out, POPS);
  not not_9 (not_9_out, sbw_2_out);
  not not_10 (not_10_out, delay_2_out);
  nor nor_3 (nor_3_out, or_40_out, SSP);
  Subtractor #(.width(12)) subtractor_1 (
    .a(SP_q), .b(controlled_buffer_20_out), .out(subtractor_1_out));  // open: bin, bout
  and and_7 (and_7_out, or_39_out, or_42_out);
  or or_42 (or_42_out, or_3_out, or_44_out, or_24_out);
  Adder #(.width(12)) adder_2 (.a(SP_q), .b(12'h1), .out(adder_2_out));  // open: cin, cout
  not not_11 (not_11_out, pops_4_out);
  or or_43 (or_43_out, pshs_out, or_45_out, pshs_3_out);
  or or_44 (or_44_out, pshs_2_out, pshs_4_out);
  delay delay_4 (.Delay(pops_out), .Clear(or_47_out), .OUT(delay_4_out));
  or or_45 (or_45_out, pops_2_out, pops_4_out);
  delay delay_5 (.Delay(pops_4_out), .Clear(not_8_out), .OUT(delay_5_out));
  and and_8 (and_8_out, not_9_out, not_10_out, or_2_out);
  assign controlled_buffer_14_out = or_27_out ? subtractor_1_out : 12'bz;  // Controlled_Buffer controlled_buffer_24
  RAM #(.addrWidth(12), .bus("separate")) ram_1 (
    .addr(controlled_buffer_23_out), .din(controlled_buffer_18_out), .data(ram_1_data), .str(and_7_out),
    .sel(1'b1), .clk(and_7_out));  // open: ld, clr
  assign controlled_buffer_14_out = and_9_out ? adder_2_out : 12'bz;  // Controlled_Buffer controlled_buffer_25
  and and_9 (and_9_out, not_11_out, or_46_out);
  or or_46 (or_46_out, or_29_out, or_19_out);
  delay delay_6 (.Delay(pshs_out), .Clear(or_44_out), .OUT(delay_6_out));
  and and_10 (SR_W, iret_3_out, not_12_out);
  not not_12 (not_12_out, RET);
  or or_47 (or_47_out, or_45_out, nor_2_out);
  not not_13 (not_13_out, and_8_out);
  Register #(.trigger("falling")) register_1 (.D(RX_IN), .Q(register_1_q), .clk(CLK));  // open: en, clr
  Adder #(.width(12)) adder_3 (.a({12{1'b0}}), .b(SP_q), .out({adder_3_out_2, adder_3_out}));  // open: cin, cout
  nor nor_4 (nor_4_out, ABP, or_48_out);
  assign controlled_buffer_26_out = not_13_out ? DR_IN : 8'bz;  // Controlled_Buffer controlled_buffer_26
  assign controlled_buffer_26_out = and_8_out ? register_1_q : 8'bz;  // Controlled_Buffer controlled_buffer_27
  or or_48 (or_48_out, SBP, SBW);
  assign bit_extender_1_out = {{4{1'b0}}, controlled_buffer_26_out};  // Bit_Extender bit_extender_1
  assign controlled_buffer_23_out = or_48_out ? subtractor_2_out : 12'bz;  // Controlled_Buffer controlled_buffer_28
  Subtractor #(.width(12)) subtractor_2 (
    .a({BP_q_2, BP_q}), .b(bit_extender_1_out), .out(subtractor_2_out));  // open: bin, bout
  assign controlled_buffer_23_out = ABP ? adder_4_out : 12'bz;  // Controlled_Buffer controlled_buffer_29
  Adder #(.width(12)) adder_4 (.a({BP_q_2, BP_q}), .b(bit_extender_1_out), .out(adder_4_out));  // open: cin, cout

  // Notes on the sheet:
  //   Stack System
endmodule

// Extender
module extender (
  input  FE,
  input  DE,
  input  [3:0] ADDR,
  input  AND,
  input  OR,
  input  NOT,
  input  XOR,
  input  ADD,
  input  SUBLD,
  input  JUMP_CALL,
  input  IN,
  input  OUT,
  input  SHR,
  input  SHL,
  output [25:0] ExtOut,
  output [2:0] ExtOut2,
  output CLR,
  output CALL_TMP,
  output CALL_FIX,
  output STD
);

  wire ABP_out, and_1_out, and_2_out, and_3_out, CDR_out, CLR_out, d_ff_31_q, DC_out, DD_out, DECR_out,
       DI_out, DIV_out, EC_out, ED_out, EI_out, IDC_out, INCR_out, IRET_out, MUL_out, not_1_out, not_2_out,
       not_3_out, not_4_out, not_5_out, not_6_out, or_1_out, or_2_out, or_3_out, POP_out, POPB_out, POPD_out,
       POPS_out, PUSH_out, PUSHB_out, PUSHD_out, PUSHS_out, RET_out, SBP_out, SBW_out, SSP_out, STD_out,
       STL_out;

  not not_1 (not_1_out, ADDR[2]);
  not not_2 (not_2_out, ADDR[1]);
  not not_3 (not_3_out, ADDR[0]);
  and EI (EI_out, AND, ADDR[3], not_1_out, not_2_out, not_3_out);
  and DI (DI_out, AND, ADDR[3], not_1_out, not_2_out, ADDR[0]);
  and ED (ED_out, AND, ADDR[3], not_1_out, ADDR[1], not_3_out);
  and DD (DD_out, AND, ADDR[3], not_1_out, ADDR[1], ADDR[0]);
  and EC (EC_out, AND, ADDR[3], ADDR[2], not_2_out, not_3_out);
  and DC (DC_out, AND, ADDR[3], ADDR[2], not_2_out, ADDR[0]);
  and CDR (CDR_out, AND, ADDR[3], ADDR[2], ADDR[1], not_3_out);
  and u_CLR (CLR_out, AND, ADDR[3], ADDR[2], ADDR[1], ADDR[0]);
  and PUSHB (PUSHB_out, OR, ADDR[3], not_1_out, not_2_out, not_3_out);
  and POPB (POPB_out, OR, ADDR[3], not_1_out, not_2_out, ADDR[0]);
  and PUSHS (PUSHS_out, OR, ADDR[3], not_1_out, ADDR[1], not_3_out);
  and POPS (POPS_out, OR, ADDR[3], not_1_out, ADDR[1], ADDR[0]);
  and SBP (SBP_out, OR, ADDR[3], ADDR[2], not_2_out, not_3_out);
  and ABP (ABP_out, OR, ADDR[3], ADDR[2], not_2_out, ADDR[0]);
  and SSP (SSP_out, OR, ADDR[3], ADDR[2], ADDR[1], not_3_out);
  and IRET (IRET_out, OR, ADDR[3], ADDR[2], ADDR[1], ADDR[0]);
  and PUSHD (PUSHD_out, NOT, ADDR[3], not_1_out, not_2_out, not_3_out);
  and POPD (POPD_out, NOT, ADDR[3], not_1_out, not_2_out, ADDR[0]);
  and RET (RET_out, NOT, ADDR[3], ADDR[2], ADDR[1], ADDR[0]);
  and SBW (SBW_out, NOT, ADDR[3], not_1_out, ADDR[1], not_3_out);
  and PUSH (PUSH_out, XOR, ADDR[3]);
  and POP (POP_out, ADD, ADDR[3]);
  and CALL (CALL_TMP, SUBLD, ADDR[3]);
  and MUL (MUL_out, IN, ADDR[3]);
  and DIV (DIV_out, OUT, ADDR[3]);
  and STL (STL_out, SHR, ADDR[3]);
  and u_STD (STD_out, SHL, ADDR[3], not_1_out, not_2_out, not_3_out);
  and INCR (INCR_out, SHL, ADDR[3], not_1_out, not_2_out, ADDR[0]);
  and DECR (DECR_out, SHL, ADDR[3], not_1_out, ADDR[1], not_3_out);
  and IDC (IDC_out, SHL, ADDR[3], not_1_out, ADDR[1], ADDR[0]);
  D_Flip_Flop #(.trigger("falling")) d_ff_1 (.clk(DE), .D(EI_out), .Q(ExtOut[0]));  // open: Qn, preset, en, reset
  D_Flip_Flop #(.trigger("falling")) d_ff_2 (.clk(DE), .D(DI_out), .Q(ExtOut[1]));  // open: Qn, preset, en, reset
  D_Flip_Flop #(.trigger("falling")) d_ff_3 (.clk(DE), .D(ED_out), .Q(ExtOut[2]));  // open: Qn, preset, en, reset
  D_Flip_Flop #(.trigger("falling")) d_ff_4 (.clk(DE), .D(DD_out), .Q(ExtOut[3]));  // open: Qn, preset, en, reset
  D_Flip_Flop #(.trigger("falling")) d_ff_5 (.clk(DE), .D(EC_out), .Q(ExtOut[4]));  // open: Qn, preset, en, reset
  D_Flip_Flop #(.trigger("falling")) d_ff_6 (.clk(DE), .D(DC_out), .Q(ExtOut[5]));  // open: Qn, preset, en, reset
  D_Flip_Flop #(.trigger("falling")) d_ff_7 (.clk(DE), .D(CDR_out), .Q(ExtOut[6]));  // open: Qn, preset, en, reset
  D_Flip_Flop #(.trigger("falling")) d_ff_8 (.clk(DE), .D(CLR_out), .Q(ExtOut[7]));  // open: Qn, preset, en, reset
  D_Flip_Flop #(.trigger("falling")) d_ff_9 (
    .clk(DE), .D(PUSHB_out), .Q(ExtOut[8]), .reset(and_1_out));  // open: Qn, preset, en
  D_Flip_Flop #(.trigger("falling")) d_ff_10 (
    .clk(DE), .D(POPB_out), .Q(ExtOut[9]), .reset(and_1_out));  // open: Qn, preset, en
  D_Flip_Flop #(.trigger("falling")) d_ff_11 (
    .clk(DE), .D(PUSHS_out), .Q(ExtOut[10]), .reset(and_1_out));  // open: Qn, preset, en
  D_Flip_Flop #(.trigger("falling")) d_ff_12 (
    .clk(DE), .D(POPS_out), .Q(ExtOut[11]), .reset(and_1_out));  // open: Qn, preset, en
  D_Flip_Flop #(.trigger("falling")) d_ff_13 (
    .clk(DE), .D(SBP_out), .Q(ExtOut[12]), .reset(and_1_out));  // open: Qn, preset, en
  D_Flip_Flop #(.trigger("falling")) d_ff_14 (
    .clk(DE), .D(ABP_out), .Q(ExtOut[13]), .reset(and_1_out));  // open: Qn, preset, en
  D_Flip_Flop #(.trigger("falling")) d_ff_15 (
    .clk(DE), .D(SSP_out), .Q(ExtOut[14]), .reset(and_1_out));  // open: Qn, preset, en
  D_Flip_Flop #(.trigger("falling")) d_ff_16 (
    .clk(DE), .D(IRET_out), .Q(ExtOut[15]), .reset(and_1_out));  // open: Qn, preset, en
  D_Flip_Flop #(.trigger("falling")) d_ff_17 (
    .clk(DE), .D(PUSHD_out), .Q(ExtOut[16]), .reset(and_2_out));  // open: Qn, preset, en
  D_Flip_Flop #(.trigger("falling")) d_ff_18 (
    .clk(DE), .D(POPD_out), .Q(ExtOut[17]), .reset(and_2_out));  // open: Qn, preset, en
  D_Flip_Flop #(.trigger("falling")) d_ff_19 (
    .clk(DE), .D(RET_out), .Q(ExtOut[18]), .reset(and_2_out));  // open: Qn, preset, en
  D_Flip_Flop #(.trigger("falling")) d_ff_20 (
    .clk(DE), .D(SBW_out), .Q(ExtOut[22]), .reset(and_2_out));  // open: Qn, preset, en
  D_Flip_Flop #(.trigger("falling")) d_ff_21 (
    .clk(DE), .D(PUSH_out), .Q(ExtOut[20]), .reset(and_2_out));  // open: Qn, preset, en
  D_Flip_Flop #(.trigger("falling")) d_ff_22 (
    .clk(DE), .D(POP_out), .Q(ExtOut[21]), .reset(and_2_out));  // open: Qn, preset, en
  D_Flip_Flop #(.trigger("falling")) d_ff_23 (
    .clk(DE), .D(JUMP_CALL), .Q(CALL_FIX), .reset(and_2_out));  // open: Qn, preset, en
  D_Flip_Flop #(.trigger("falling")) d_ff_24 (
    .clk(DE), .D(MUL_out), .Q(ExtOut[23]), .reset(and_3_out));  // open: Qn, preset, en
  D_Flip_Flop #(.trigger("falling")) d_ff_25 (
    .clk(DE), .D(DIV_out), .Q(ExtOut[24]), .reset(and_3_out));  // open: Qn, preset, en
  D_Flip_Flop #(.trigger("falling")) d_ff_26 (
    .clk(DE), .D(STL_out), .Q(ExtOut[25]), .reset(and_3_out));  // open: Qn, preset, en
  D_Flip_Flop #(.trigger("falling")) d_ff_27 (
    .clk(DE), .D(STD_out), .Q(STD), .reset(and_3_out));  // open: Qn, preset, en
  D_Flip_Flop #(.trigger("falling")) d_ff_28 (
    .clk(DE), .D(INCR_out), .Q(ExtOut2[0]), .reset(and_3_out));  // open: Qn, preset, en
  D_Flip_Flop #(.trigger("falling")) d_ff_29 (
    .clk(DE), .D(DECR_out), .Q(ExtOut2[1]), .reset(and_3_out));  // open: Qn, preset, en
  D_Flip_Flop #(.trigger("falling")) d_ff_30 (
    .clk(DE), .D(IDC_out), .Q(ExtOut2[2]), .reset(and_3_out));  // open: Qn, preset, en
  D_Flip_Flop #(.trigger("falling")) d_ff_31 (.clk(DE), .D(ExtOut[7]), .Q(d_ff_31_q));  // open: Qn, preset, en, reset
  and and_1 (and_1_out, or_1_out, not_4_out, FE);
  and and_2 (and_2_out, or_2_out, not_5_out, FE);
  and and_3 (and_3_out, or_3_out, not_6_out, FE);
  not not_4 (not_4_out, DE);
  not not_5 (not_5_out, DE);
  not not_6 (not_6_out, DE);
  and and_4 (CLR, FE, ExtOut[7], d_ff_31_q);
  or or_1 (or_1_out, ExtOut[8], ExtOut[9], ExtOut[10], ExtOut[11], ExtOut[12], ExtOut[13], ExtOut[14]);
  or or_2 (or_2_out, ExtOut[16], ExtOut[17], ExtOut[18], ExtOut[20], ExtOut[21], ExtOut[22], CALL_FIX);
  or or_3 (or_3_out, ExtOut[23], ExtOut2[2], ExtOut2[1], ExtOut2[0], STD, ExtOut[25], ExtOut[24]);

  assign ExtOut[19] = CALL_FIX;
endmodule

module delay (
  input  Delay,
  input  Clear,
  output OUT
);

  wire d_ff_1_q;

  D_Flip_Flop d_ff_1 (.clk(Delay), .D(1'b1), .Q(d_ff_1_q), .reset(Clear));  // open: Qn, preset, en
  Multiplexer multiplexer_1 (.in0(1'b0), .in1(Delay), .out(OUT), .sel(d_ff_1_q));  // open: en
endmodule

module sp_sync (
  input  SSP,
  input  WR,
  input  OR,
  input  SUB,
  input  ADD,
  input  ON,
  input  POPS,
  output OUT
);

  wire and_1_out, and_2_out, and_3_out, and_4_out, or_1_out;

  and and_1 (and_1_out, ADD, SSP, WR);
  and and_2 (and_2_out, OR, SUB);
  and and_3 (and_3_out, OR, ADD);
  and and_4 (and_4_out, OR, WR, POPS);
  or or_1 (or_1_out, and_2_out, and_1_out, and_3_out);
  or or_2 (OUT, or_1_out, ON, and_4_out);
endmodule

// TTY
module TTY_Controller (
  input  [7:0] tty_data,
  input  tty_wr,
  input  tty_clk,
  input  tty_on,
  output [6:0] data,
  output clk,
  output en
);

  wire not_1_out;

  and and_1 (clk, tty_wr, not_1_out);
  not not_1 (not_1_out, tty_clk);
  D_Flip_Flop d_ff_1 (.clk(tty_on), .D(1'b1), .Q(en));  // open: Qn, preset, en, reset

  assign data = tty_data[6:0];
endmodule

module edge_detector (
  input  CLK,
  output OUT
);

  wire and_1_out, nand_1_out, not_1_out, not_2_out;

  not not_1 (not_1_out, CLK);
  not not_2 (not_2_out, CLK);
  nand nand_1 (nand_1_out, not_1_out, CLK);
  and and_1 (and_1_out, not_2_out, CLK);
  Multiplexer multiplexer_1 (.in0(nand_1_out), .in1(and_1_out), .out(OUT), .sel(CLK));  // open: en
endmodule

// Transfer
module transfer_circuit (
  input  T_ON,
  input  [11:0] A,
  input  [7:0] CPU_D,
  input  [7:0] ROM_D,
  input  RAM_STR,
  input  CLK_OUT,
  input  ROM_SEL,
  output [11:0] ADDR,
  output [7:0] DATA,
  output CPU_ON,
  output SEL,
  output STR,
  output ROM
);

  wire clock_1_out, comparator_1_eq, edge_detector_1_out, not_1_out, not_2_out, not_3_out;
  wire [11:0] counter_1_q;

  Clock clock_1 (.out(clock_1_out));
  not not_1 (not_1_out, T_ON);
  Comparator #(.width(12)) comparator_1 (.a({12{1'b1}}), .b(counter_1_q), .eq(comparator_1_eq));  // open: gt, lt
  edge_detector edge_detector_1 (.CLK(clock_1_out), .OUT(edge_detector_1_out));
  or or_1 (CPU_ON, not_1_out, comparator_1_eq);
  Counter #(.width(12), .max('hfff)) counter_1 (
    .count(not_3_out), .Q(counter_1_q), .clk(edge_detector_1_out));  // open: load, D, carry, clr
  assign ADDR = CPU_ON ? A : 12'bz;  // Controlled_Buffer controlled_buffer_1
  assign DATA = CPU_ON ? CPU_D : 8'bz;  // Controlled_Buffer controlled_buffer_2
  assign DATA = not_3_out ? ROM_D : 8'bz;  // Controlled_Buffer controlled_buffer_3
  not not_2 (not_2_out, not_3_out);
  assign ADDR = not_3_out ? counter_1_q : 12'bz;  // Controlled_Buffer controlled_buffer_4
  not not_3 (not_3_out, CPU_ON);
  or or_2 (SEL, not_3_out, RAM_STR);
  assign STR = not_3_out ? edge_detector_1_out : 1'bz;  // Controlled_Buffer controlled_buffer_5
  assign STR = not_2_out ? CLK_OUT : 1'bz;  // Controlled_Buffer controlled_buffer_6
  or or_3 (ROM, not_3_out, ROM_SEL);
endmodule

// RX Decoder
module RX_selector (
  input  CLEAR,
  input  CLK,
  input  EN,
  input  B2,
  input  B1,
  input  B0,
  output R0,
  output R1,
  output R2,
  output R3,
  output R4,
  output R5,
  output R6,
  output R7
);

  wire and_1_out, and_2_out, and_3_out, and_4_out, and_5_out, and_6_out, and_7_out, and_8_out, not_1_out,
       not_2_out, not_3_out;

  not not_1 (not_1_out, B0);
  not not_2 (not_2_out, B1);
  not not_3 (not_3_out, B2);
  and and_1 (and_1_out, not_1_out, not_2_out, not_3_out);
  and and_2 (and_2_out, not_3_out, not_2_out, B0);
  and and_3 (and_3_out, not_3_out, B1, not_1_out);
  and and_4 (and_4_out, not_3_out, B1, B0);
  and and_5 (and_5_out, B2, not_2_out, not_1_out);
  and and_6 (and_6_out, B2, not_2_out, B0);
  and and_7 (and_7_out, B2, B1, not_1_out);
  and and_8 (and_8_out, B2, B1, B0);
  D_Flip_Flop #(.trigger("falling")) d_ff_1 (.clk(CLK), .D(and_1_out), .Q(R0), .reset(CLEAR));  // open: Qn, preset, en
  D_Flip_Flop #(.trigger("falling")) d_ff_2 (.clk(CLK), .D(and_2_out), .Q(R1), .reset(CLEAR));  // open: Qn, preset, en
  D_Flip_Flop #(.trigger("falling")) d_ff_3 (.clk(CLK), .D(and_3_out), .Q(R2), .reset(CLEAR));  // open: Qn, preset, en
  D_Flip_Flop #(.trigger("falling")) d_ff_4 (.clk(CLK), .D(and_4_out), .Q(R3), .reset(CLEAR));  // open: Qn, preset, en
  D_Flip_Flop #(.trigger("falling")) d_ff_5 (.clk(CLK), .D(and_5_out), .Q(R4), .reset(CLEAR));  // open: Qn, preset, en
  D_Flip_Flop #(.trigger("falling")) d_ff_6 (.clk(CLK), .D(and_6_out), .Q(R5), .reset(CLEAR));  // open: Qn, preset, en
  D_Flip_Flop #(.trigger("falling")) d_ff_7 (.clk(CLK), .D(and_7_out), .Q(R6), .reset(CLEAR));  // open: Qn, preset, en
  D_Flip_Flop #(.trigger("falling")) d_ff_8 (.clk(CLK), .D(and_8_out), .Q(R7), .reset(CLEAR));  // open: Qn, preset, en
endmodule

// Led Matrix 32x32x2 Decoder
module graph_decoder (
  input  CLR,
  input  [15:0] YX,
  input  [7:0] DATA,
  input  COUNTER,
  input  CLK,
  output [31:0] L0,
  output [31:0] L8,
  output [31:0] L16,
  output [31:0] L24,
  output [31:0] L1,
  output [31:0] L9,
  output [31:0] L17,
  output [31:0] L25,
  output [31:0] L2,
  output [31:0] L10,
  output [31:0] L18,
  output [31:0] L26,
  output [7:0] Count,
  output [31:0] L3,
  output [31:0] L11,
  output [31:0] L19,
  output [31:0] L27,
  output [31:0] L4,
  output [31:0] L12,
  output [31:0] L20,
  output [31:0] L28,
  output [31:0] L5,
  output [31:0] L13,
  output [31:0] L21,
  output [31:0] L29,
  output [31:0] L6,
  output [31:0] L14,
  output [31:0] L22,
  output [31:0] L30,
  output [31:0] L7,
  output [31:0] L15,
  output [31:0] L23,
  output [31:0] L31
);

  wire demultiplexer_2_out0, demultiplexer_2_out1, demultiplexer_2_out2, demultiplexer_2_out3,
       demultiplexer_2_out4, demultiplexer_2_out5, demultiplexer_2_out6, demultiplexer_2_out7,
       demultiplexer_3_out0, demultiplexer_3_out1, demultiplexer_3_out2, demultiplexer_3_out3;
  wire [31:0] demultiplexer_1_out0, multiplexer_1_out, multiplexer_2_out, pixel_manager_1_store,
       pixel_manager_2_store, pixel_manager_3_store, pixel_manager_4_store, pixel_manager_5_store,
       pixel_manager_6_store, pixel_manager_7_store, pixel_manager_8_store, pixel_manager_9_store,
       pixel_manager_10_store, pixel_manager_11_store, pixel_manager_12_store, pixel_manager_13_store,
       pixel_manager_14_store, pixel_manager_15_store, pixel_manager_16_store, pixel_manager_17_store,
       pixel_manager_18_store, pixel_manager_19_store, pixel_manager_20_store, pixel_manager_21_store,
       pixel_manager_22_store, pixel_manager_23_store, pixel_manager_24_store, pixel_manager_25_store,
       pixel_manager_26_store, pixel_manager_27_store, pixel_manager_28_store, pixel_manager_29_store,
       pixel_manager_30_store, pixel_manager_31_store, pixel_manager_32_store;

  Demultiplexer #(.select(5)) demultiplexer_1 (
    .out0(demultiplexer_1_out0[0]), .out1(demultiplexer_1_out0[1]), .out2(demultiplexer_1_out0[2]),
    .out3(demultiplexer_1_out0[3]), .out4(demultiplexer_1_out0[4]), .out5(demultiplexer_1_out0[5]),
    .out6(demultiplexer_1_out0[6]), .out7(demultiplexer_1_out0[7]), .out8(demultiplexer_1_out0[8]),
    .out9(demultiplexer_1_out0[9]), .out10(demultiplexer_1_out0[10]), .out11(demultiplexer_1_out0[11]),
    .out12(demultiplexer_1_out0[12]), .out13(demultiplexer_1_out0[13]), .out14(demultiplexer_1_out0[14]),
    .out15(demultiplexer_1_out0[15]), .out16(demultiplexer_1_out0[16]), .out17(demultiplexer_1_out0[17]),
    .out18(demultiplexer_1_out0[18]), .out19(demultiplexer_1_out0[19]), .out20(demultiplexer_1_out0[20]),
    .out21(demultiplexer_1_out0[21]), .out22(demultiplexer_1_out0[22]), .out23(demultiplexer_1_out0[23]),
    .out24(demultiplexer_1_out0[24]), .out25(demultiplexer_1_out0[25]), .out26(demultiplexer_1_out0[26]),
    .out27(demultiplexer_1_out0[27]), .out28(demultiplexer_1_out0[28]), .out29(demultiplexer_1_out0[29]),
    .out30(demultiplexer_1_out0[30]), .out31(demultiplexer_1_out0[31]), .in(CLK), .sel(YX[4:0]));  // open: en
  Counter counter_1 (.count(1'b1), .Q(Count), .clk(COUNTER), .clr(CLR));  // open: load, D, carry
  Multiplexer #(.width(32)) multiplexer_1 (
    .in0(demultiplexer_1_out0), .in1({32{1'b0}}), .out(multiplexer_1_out), .sel(DATA[0]));  // open: en
  Multiplexer #(.width(32)) multiplexer_2 (
    .in0({32{1'b0}}), .in1(demultiplexer_1_out0), .out(multiplexer_2_out), .sel(DATA[0]));  // open: en
  Demultiplexer #(.select(3)) demultiplexer_2 (
    .out0(demultiplexer_2_out0), .out1(demultiplexer_2_out1), .out2(demultiplexer_2_out2),
    .out3(demultiplexer_2_out3), .out4(demultiplexer_2_out4), .out5(demultiplexer_2_out5),
    .out6(demultiplexer_2_out6), .out7(demultiplexer_2_out7), .in(CLK), .sel(YX[10:8]));  // open: en
  Register #(.width(32), .trigger("high")) register_1 (
    .D(pixel_manager_1_store), .en(demultiplexer_3_out0), .Q(L0), .clk(demultiplexer_2_out0), .clr(CLR));
  Register #(.width(32), .trigger("high")) register_2 (
    .D(pixel_manager_2_store), .en(demultiplexer_3_out0), .Q(L1), .clk(demultiplexer_2_out1), .clr(CLR));
  Register #(.width(32), .trigger("high")) register_3 (
    .D(pixel_manager_3_store), .en(demultiplexer_3_out0), .Q(L2), .clk(demultiplexer_2_out2), .clr(CLR));
  Register #(.width(32), .trigger("high")) register_4 (
    .D(pixel_manager_4_store), .en(demultiplexer_3_out0), .Q(L3), .clk(demultiplexer_2_out3), .clr(CLR));
  Register #(.width(32), .trigger("high")) register_5 (
    .D(pixel_manager_5_store), .en(demultiplexer_3_out0), .Q(L4), .clk(demultiplexer_2_out4), .clr(CLR));
  Register #(.width(32), .trigger("high")) register_6 (
    .D(pixel_manager_6_store), .en(demultiplexer_3_out0), .Q(L5), .clk(demultiplexer_2_out5), .clr(CLR));
  Register #(.width(32), .trigger("high")) register_7 (
    .D(pixel_manager_7_store), .en(demultiplexer_3_out0), .Q(L6), .clk(demultiplexer_2_out6), .clr(CLR));
  Register #(.width(32), .trigger("high")) register_8 (
    .D(pixel_manager_8_store), .en(demultiplexer_3_out0), .Q(L7), .clk(demultiplexer_2_out7), .clr(CLR));
  pixel_manager pixel_manager_1 (
    .BitsToClear(multiplexer_1_out), .Value(multiplexer_2_out), .Register(L0), .Store(pixel_manager_1_store));
  pixel_manager pixel_manager_2 (
    .BitsToClear(multiplexer_1_out), .Value(multiplexer_2_out), .Register(L1), .Store(pixel_manager_2_store));
  pixel_manager pixel_manager_3 (
    .BitsToClear(multiplexer_1_out), .Value(multiplexer_2_out), .Register(L2), .Store(pixel_manager_3_store));
  pixel_manager pixel_manager_4 (
    .BitsToClear(multiplexer_1_out), .Value(multiplexer_2_out), .Register(L3), .Store(pixel_manager_4_store));
  pixel_manager pixel_manager_5 (
    .BitsToClear(multiplexer_1_out), .Value(multiplexer_2_out), .Register(L4), .Store(pixel_manager_5_store));
  pixel_manager pixel_manager_6 (
    .BitsToClear(multiplexer_1_out), .Value(multiplexer_2_out), .Register(L5), .Store(pixel_manager_6_store));
  pixel_manager pixel_manager_7 (
    .BitsToClear(multiplexer_1_out), .Value(multiplexer_2_out), .Register(L6), .Store(pixel_manager_7_store));
  pixel_manager pixel_manager_8 (
    .BitsToClear(multiplexer_1_out), .Value(multiplexer_2_out), .Register(L7), .Store(pixel_manager_8_store));
  pixel_manager pixel_manager_9 (
    .BitsToClear(multiplexer_1_out), .Value(multiplexer_2_out), .Register(L8), .Store(pixel_manager_9_store));
  Register #(.width(32), .trigger("high")) register_9 (
    .D(pixel_manager_9_store), .en(demultiplexer_3_out1), .Q(L8), .clk(demultiplexer_2_out0), .clr(CLR));
  pixel_manager pixel_manager_10 (
    .BitsToClear(multiplexer_1_out), .Value(multiplexer_2_out), .Register(L9), .Store(pixel_manager_10_store));
  Register #(.width(32), .trigger("high")) register_10 (
    .D(pixel_manager_10_store), .en(demultiplexer_3_out1), .Q(L9), .clk(demultiplexer_2_out1), .clr(CLR));
  pixel_manager pixel_manager_11 (
    .BitsToClear(multiplexer_1_out), .Value(multiplexer_2_out), .Register(L10), .Store(pixel_manager_11_store));
  Register #(.width(32), .trigger("high")) register_11 (
    .D(pixel_manager_11_store), .en(demultiplexer_3_out1), .Q(L10), .clk(demultiplexer_2_out2), .clr(CLR));
  pixel_manager pixel_manager_12 (
    .BitsToClear(multiplexer_1_out), .Value(multiplexer_2_out), .Register(L11), .Store(pixel_manager_12_store));
  Register #(.width(32), .trigger("high")) register_12 (
    .D(pixel_manager_12_store), .en(demultiplexer_3_out1), .Q(L11), .clk(demultiplexer_2_out3), .clr(CLR));
  pixel_manager pixel_manager_13 (
    .BitsToClear(multiplexer_1_out), .Value(multiplexer_2_out), .Register(L12), .Store(pixel_manager_13_store));
  Register #(.width(32), .trigger("high")) register_13 (
    .D(pixel_manager_13_store), .en(demultiplexer_3_out1), .Q(L12), .clk(demultiplexer_2_out4), .clr(CLR));
  pixel_manager pixel_manager_14 (
    .BitsToClear(multiplexer_1_out), .Value(multiplexer_2_out), .Register(L13), .Store(pixel_manager_14_store));
  Register #(.width(32), .trigger("high")) register_14 (
    .D(pixel_manager_14_store), .en(demultiplexer_3_out1), .Q(L13), .clk(demultiplexer_2_out5), .clr(CLR));
  pixel_manager pixel_manager_15 (
    .BitsToClear(multiplexer_1_out), .Value(multiplexer_2_out), .Register(L14), .Store(pixel_manager_15_store));
  Register #(.width(32), .trigger("high")) register_15 (
    .D(pixel_manager_15_store), .en(demultiplexer_3_out1), .Q(L14), .clk(demultiplexer_2_out6), .clr(CLR));
  pixel_manager pixel_manager_16 (
    .BitsToClear(multiplexer_1_out), .Value(multiplexer_2_out), .Register(L15), .Store(pixel_manager_16_store));
  Register #(.width(32), .trigger("high")) register_16 (
    .D(pixel_manager_16_store), .en(demultiplexer_3_out1), .Q(L15), .clk(demultiplexer_2_out7), .clr(CLR));
  Demultiplexer #(.select(2)) demultiplexer_3 (
    .out0(demultiplexer_3_out0), .out1(demultiplexer_3_out1), .out2(demultiplexer_3_out2),
    .out3(demultiplexer_3_out3), .in(CLK), .sel(YX[12:11]));  // open: en
  pixel_manager pixel_manager_17 (
    .BitsToClear(multiplexer_1_out), .Value(multiplexer_2_out), .Register(L16), .Store(pixel_manager_17_store));
  Register #(.width(32), .trigger("high")) register_17 (
    .D(pixel_manager_17_store), .en(demultiplexer_3_out2), .Q(L16), .clk(demultiplexer_2_out0), .clr(CLR));
  pixel_manager pixel_manager_18 (
    .BitsToClear(multiplexer_1_out), .Value(multiplexer_2_out), .Register(L17), .Store(pixel_manager_18_store));
  Register #(.width(32), .trigger("high")) register_18 (
    .D(pixel_manager_18_store), .en(demultiplexer_3_out2), .Q(L17), .clk(demultiplexer_2_out1), .clr(CLR));
  pixel_manager pixel_manager_19 (
    .BitsToClear(multiplexer_1_out), .Value(multiplexer_2_out), .Register(L18), .Store(pixel_manager_19_store));
  Register #(.width(32), .trigger("high")) register_19 (
    .D(pixel_manager_19_store), .en(demultiplexer_3_out2), .Q(L18), .clk(demultiplexer_2_out2), .clr(CLR));
  pixel_manager pixel_manager_20 (
    .BitsToClear(multiplexer_1_out), .Value(multiplexer_2_out), .Register(L19), .Store(pixel_manager_20_store));
  Register #(.width(32), .trigger("high")) register_20 (
    .D(pixel_manager_20_store), .en(demultiplexer_3_out2), .Q(L19), .clk(demultiplexer_2_out3), .clr(CLR));
  pixel_manager pixel_manager_21 (
    .BitsToClear(multiplexer_1_out), .Value(multiplexer_2_out), .Register(L20), .Store(pixel_manager_21_store));
  Register #(.width(32), .trigger("high")) register_21 (
    .D(pixel_manager_21_store), .en(demultiplexer_3_out2), .Q(L20), .clk(demultiplexer_2_out4), .clr(CLR));
  pixel_manager pixel_manager_22 (
    .BitsToClear(multiplexer_1_out), .Value(multiplexer_2_out), .Register(L21), .Store(pixel_manager_22_store));
  Register #(.width(32), .trigger("high")) register_22 (
    .D(pixel_manager_22_store), .en(demultiplexer_3_out2), .Q(L21), .clk(demultiplexer_2_out5), .clr(CLR));
  pixel_manager pixel_manager_23 (
    .BitsToClear(multiplexer_1_out), .Value(multiplexer_2_out), .Register(L22), .Store(pixel_manager_23_store));
  Register #(.width(32), .trigger("high")) register_23 (
    .D(pixel_manager_23_store), .en(demultiplexer_3_out2), .Q(L22), .clk(demultiplexer_2_out6), .clr(CLR));
  pixel_manager pixel_manager_24 (
    .BitsToClear(multiplexer_1_out), .Value(multiplexer_2_out), .Register(L23), .Store(pixel_manager_24_store));
  Register #(.width(32), .trigger("high")) register_24 (
    .D(pixel_manager_24_store), .en(demultiplexer_3_out2), .Q(L23), .clk(demultiplexer_2_out7), .clr(CLR));
  Register #(.width(32), .trigger("high")) register_25 (
    .D(pixel_manager_25_store), .en(demultiplexer_3_out3), .Q(L24), .clk(demultiplexer_2_out0), .clr(CLR));
  Register #(.width(32), .trigger("high")) register_26 (
    .D(pixel_manager_26_store), .en(demultiplexer_3_out3), .Q(L25), .clk(demultiplexer_2_out1), .clr(CLR));
  Register #(.width(32), .trigger("high")) register_27 (
    .D(pixel_manager_27_store), .en(demultiplexer_3_out3), .Q(L26), .clk(demultiplexer_2_out2), .clr(CLR));
  Register #(.width(32), .trigger("high")) register_28 (
    .D(pixel_manager_28_store), .en(demultiplexer_3_out3), .Q(L27), .clk(demultiplexer_2_out3), .clr(CLR));
  Register #(.width(32), .trigger("high")) register_29 (
    .D(pixel_manager_29_store), .en(demultiplexer_3_out3), .Q(L28), .clk(demultiplexer_2_out4), .clr(CLR));
  Register #(.width(32), .trigger("high")) register_30 (
    .D(pixel_manager_30_store), .en(demultiplexer_3_out3), .Q(L29), .clk(demultiplexer_2_out5), .clr(CLR));
  Register #(.width(32), .trigger("high")) register_31 (
    .D(pixel_manager_31_store), .en(demultiplexer_3_out3), .Q(L30), .clk(demultiplexer_2_out6), .clr(CLR));
  Register #(.width(32), .trigger("high")) register_32 (
    .D(pixel_manager_32_store), .en(demultiplexer_3_out3), .Q(L31), .clk(demultiplexer_2_out7), .clr(CLR));
  pixel_manager pixel_manager_25 (
    .BitsToClear(multiplexer_1_out), .Value(multiplexer_2_out), .Register(L24), .Store(pixel_manager_25_store));
  pixel_manager pixel_manager_26 (
    .BitsToClear(multiplexer_1_out), .Value(multiplexer_2_out), .Register(L25), .Store(pixel_manager_26_store));
  pixel_manager pixel_manager_27 (
    .BitsToClear(multiplexer_1_out), .Value(multiplexer_2_out), .Register(L26), .Store(pixel_manager_27_store));
  pixel_manager pixel_manager_28 (
    .BitsToClear(multiplexer_1_out), .Value(multiplexer_2_out), .Register(L27), .Store(pixel_manager_28_store));
  pixel_manager pixel_manager_29 (
    .BitsToClear(multiplexer_1_out), .Value(multiplexer_2_out), .Register(L28), .Store(pixel_manager_29_store));
  pixel_manager pixel_manager_30 (
    .BitsToClear(multiplexer_1_out), .Value(multiplexer_2_out), .Register(L29), .Store(pixel_manager_30_store));
  pixel_manager pixel_manager_31 (
    .BitsToClear(multiplexer_1_out), .Value(multiplexer_2_out), .Register(L30), .Store(pixel_manager_31_store));
  pixel_manager pixel_manager_32 (
    .BitsToClear(multiplexer_1_out), .Value(multiplexer_2_out), .Register(L31), .Store(pixel_manager_32_store));
endmodule

module pixel_manager (
  input  [31:0] BitsToClear,
  input  [31:0] Value,
  input  [31:0] Register,
  output [31:0] Store
);

  wire [31:0] not_1_out, or_1_out;

  assign not_1_out = ~BitsToClear;  // NOT_Gate not_1, 32 bits wide
  assign Store = not_1_out & or_1_out;  // AND_Gate and_1, 32 bits wide
  assign or_1_out = Value | Register;  // OR_Gate or_1, 32 bits wide
endmodule

// MDU
module MultiplierDivider (
  input  [7:0] DR,
  input  [7:0] RX,
  input  [6:0] EXT_IN,
  input  EX,
  output [7:0] DR_OUT,
  output [7:0] RX_OUT
);

  wire nand_1_out, not_1_out, or_1_out;
  wire [7:0] divider_1_out, divider_1_rem, multiplexer_2_out, multiplier_1_cout, multiplier_1_out,
       register_1_q;

  not not_1 (not_1_out, EXT_IN[1]);
  Multiplier multiplier_1 (.a(DR), .b(RX), .out(multiplier_1_out), .cout(multiplier_1_cout));  // open: cin
  Divider divider_1 (.a(DR), .b(RX), .out(divider_1_out), .rem(divider_1_rem));  // open: upper
  nand nand_1 (nand_1_out, EXT_IN[0], not_1_out);
  or or_1 (or_1_out, EXT_IN[0], EXT_IN[1]);
  Multiplexer #(.width(8)) multiplexer_1 (
    .in0(multiplier_1_out), .in1(divider_1_out), .out(DR_OUT), .sel(nand_1_out), .en(or_1_out));
  Multiplexer #(.width(8)) multiplexer_2 (
    .in0(multiplier_1_cout), .in1(divider_1_rem), .out(multiplexer_2_out), .sel(nand_1_out), .en(or_1_out));
  assign RX_OUT = or_1_out ? register_1_q : 8'bz;  // Controlled_Buffer controlled_buffer_1
  Register #(.trigger("falling")) register_1 (.D(multiplexer_2_out), .Q(register_1_q), .clk(EX));  // open: en, clr
endmodule

// Inc-Dec
module incrementer (
  input  [7:0] PX_IN,
  input  [7:0] RX_IN,
  input  [7:0] DR_IN,
  input  [1:0] IDC_IN,
  input  [2:0] EXT_BITS2,
  input  CLK,
  input  EX,
  output CARRY_OUT,
  output [7:0] INC_OUT,
  output BORROW_OUT,
  output [7:0] INC_OUTH
);

  wire adder_1_cout, and_1_out, not_1_out, or_1_out, subtractor_1_bout;
  wire [7:0] adder_1_out, multiplexer_1_out, multiplexer_2_out, register_1_q, register_2_q, subtractor_1_out;

  Multiplexer #(.select(2), .width(8)) multiplexer_1 (
    .in0(PX_IN), .in1(RX_IN), .in2(DR_IN), .out(multiplexer_1_out), .sel(IDC_IN));  // open: in3, en
  Adder adder_1 (.a(multiplexer_1_out), .b(8'h1), .out(adder_1_out), .cout(adder_1_cout));  // open: cin
  Subtractor subtractor_1 (
    .a(multiplexer_1_out), .b(8'h1), .out(subtractor_1_out), .bout(subtractor_1_bout));  // open: bin
  or or_1 (or_1_out, EXT_BITS2[0], EXT_BITS2[1]);
  and and_1 (and_1_out, CLK, EX);
  D_Flip_Flop #(.trigger("falling")) d_ff_1 (
    .clk(and_1_out), .D(adder_1_cout), .Q(CARRY_OUT));  // open: Qn, preset, en, reset
  D_Flip_Flop #(.trigger("falling")) d_ff_2 (
    .clk(and_1_out), .D(subtractor_1_bout), .Q(BORROW_OUT));  // open: Qn, preset, en, reset
  Multiplexer #(.width(8)) multiplexer_2 (
    .in0(adder_1_out), .in1(subtractor_1_out), .out(multiplexer_2_out), .sel(EXT_BITS2[1]), .en(EX));
  Register #(.trigger("falling")) register_1 (.D(multiplexer_2_out), .Q(register_1_q), .clk(CLK));  // open: en, clr
  Register #(.trigger("falling")) register_2 (
    .D(multiplexer_2_out), .Q(register_2_q), .clk(not_1_out));  // open: en, clr
  not not_1 (not_1_out, CLK);
  assign INC_OUT = or_1_out ? register_1_q : 8'bz;  // Controlled_Buffer controlled_buffer_1
  assign INC_OUTH = or_1_out ? register_2_q : 8'bz;  // Controlled_Buffer controlled_buffer_2
endmodule
